// Logisim project Funkuhr.circ as structural Verilog
module Funkuhr_Main (
);

  wire Clock_Main_out, counter_second_1_p2;
  wire [12:0] counter_13bit_1_ausgang_counter;

  Clock Clock_Main (.out(Clock_Main_out));
  // Counter_Second counter_second_1: pin names not known; wires that end beside it: Clock_Main_out, counter_second_1_p2
  Counter_13bit counter_13bit_1 (
    .Clock(counter_second_1_p2), .Ausgang_Counter(counter_13bit_1_ausgang_counter));  // open: Reset, Load, Data_Load_13bit, Ausgang_Counter_Negiert
endmodule

module Counter_Second (
  input  Clock_2kHz,
  input  Set,
  input  [12:0] Data_SetClock_13bit,
  output Ausgang_Sekunde
);

  wire and_1_out;
  wire [12:0] counter_13bit_1_ausgang_counter, counter_13bit_1_ausgang_counter_negiert;

  and and_1 (and_1_out, Ausgang_Sekunde, ~Set);  // AND_Gate
  Counter_13bit counter_13bit_1 (
    .Clock(Clock_2kHz), .Reset(and_1_out), .Load(Set), .Data_Load_13bit(Data_SetClock_13bit),
    .Ausgang_Counter(counter_13bit_1_ausgang_counter),
    .Ausgang_Counter_Negiert(counter_13bit_1_ausgang_counter_negiert));
  and and_2 (Ausgang_Sekunde, counter_13bit_1_ausgang_counter_negiert[0], counter_13bit_1_ausgang_counter_negiert[1], counter_13bit_1_ausgang_counter_negiert[2], counter_13bit_1_ausgang_counter_negiert[3], counter_13bit_1_ausgang_counter[4], counter_13bit_1_ausgang_counter_negiert[5], counter_13bit_1_ausgang_counter[6], counter_13bit_1_ausgang_counter[7], counter_13bit_1_ausgang_counter[8], counter_13bit_1_ausgang_counter[9], counter_13bit_1_ausgang_counter[10], counter_13bit_1_ausgang_counter_negiert[11], counter_13bit_1_ausgang_counter_negiert[12]);
endmodule

module Multiplexer_13bit (
  input  [1:0] Umschalter,
  input  [12:0] Eingang_0,
  input  [12:0] Eingang_1,
  input  [12:0] Eingang_2,
  output [12:0] out_5
);

  Multiplexer_1bit Multiplexer_bit0 (
    .I_0(Eingang_0[0]), .I_1(Eingang_1[0]), .I_2(Eingang_2[0]), .Umschalter(Umschalter), .Ausgang(out_5[0]));
  Multiplexer_1bit Multiplexer_bit1 (
    .I_0(Eingang_0[1]), .I_1(Eingang_1[1]), .I_2(Eingang_2[1]), .Umschalter(Umschalter), .Ausgang(out_5[1]));
  Multiplexer_1bit Multiplexer_bit2 (
    .I_0(Eingang_0[2]), .I_1(Eingang_1[2]), .I_2(Eingang_2[2]), .Umschalter(Umschalter), .Ausgang(out_5[2]));
  Multiplexer_1bit Multiplexer_bit3 (
    .I_0(Eingang_0[3]), .I_1(Eingang_1[3]), .I_2(Eingang_2[3]), .Umschalter(Umschalter), .Ausgang(out_5[3]));
  Multiplexer_1bit Multiplexer_bit4 (
    .I_0(Eingang_0[4]), .I_1(Eingang_1[4]), .I_2(Eingang_2[4]), .Umschalter(Umschalter), .Ausgang(out_5[4]));
  Multiplexer_1bit Multiplexer_bit5 (
    .I_0(Eingang_0[5]), .I_1(Eingang_1[5]), .I_2(Eingang_2[5]), .Umschalter(Umschalter), .Ausgang(out_5[5]));
  Multiplexer_1bit Multiplexer_bit6 (
    .I_0(Eingang_0[6]), .I_1(Eingang_1[6]), .I_2(Eingang_2[6]), .Umschalter(Umschalter), .Ausgang(out_5[6]));
  Multiplexer_1bit Multiplexer_bit7 (
    .I_0(Eingang_0[7]), .I_1(Eingang_1[7]), .I_2(Eingang_2[7]), .Umschalter(Umschalter), .Ausgang(out_5[7]));
  Multiplexer_1bit Multiplexer_bit8 (
    .I_0(Eingang_0[8]), .I_1(Eingang_1[8]), .I_2(Eingang_2[8]), .Umschalter(Umschalter), .Ausgang(out_5[8]));
  Multiplexer_1bit Multiplexer_bit9 (
    .I_0(Eingang_0[9]), .I_1(Eingang_1[9]), .I_2(Eingang_2[9]), .Umschalter(Umschalter), .Ausgang(out_5[9]));
  Multiplexer_1bit Multiplexer_bit10 (
    .I_0(Eingang_0[10]), .I_1(Eingang_1[10]), .I_2(Eingang_2[10]), .Umschalter(Umschalter),
    .Ausgang(out_5[10]));
  Multiplexer_1bit Multiplexer_bit11 (
    .I_0(Eingang_0[11]), .I_1(Eingang_1[11]), .I_2(Eingang_2[11]), .Umschalter(Umschalter),
    .Ausgang(out_5[11]));
  Multiplexer_1bit Multiplexer_bit12 (
    .I_0(Eingang_0[12]), .I_1(Eingang_1[12]), .I_2(Eingang_2[12]), .Umschalter(Umschalter),
    .Ausgang(out_5[12]));
endmodule

module Multiplexer_1bit (
  input  I_0,
  input  I_1,
  input  I_2,
  input  [1:0] Umschalter,
  output Ausgang
);

  wire and_1_out, and_2_out, and_3_out;

  and and_1 (and_1_out, I_0, ~Umschalter[0], ~Umschalter[1]);  // AND_Gate
  and and_2 (and_2_out, I_1, Umschalter[0], ~Umschalter[1]);  // AND_Gate
  and and_3 (and_3_out, I_2, ~Umschalter[0], Umschalter[1]);  // AND_Gate
  or or_1 (Ausgang, and_1_out, and_2_out, and_3_out);
endmodule

module seg7 (
  input  A3,
  input  A2,
  input  A1,
  input  A0,
  output SEG_A,
  output SEG_B,
  output SEG_C,
  output SEG_D,
  output SEG_E,
  output SEG_F,
  output SEG_G
);

  wire nand_1_out, nand_2_out, nand_3_out, nand_4_out, nor_1_out, nor_2_out, nor_3_out, nor_4_out, nor_5_out,
       nor_6_out, nor_7_out, nor_8_out, nor_9_out, nor_10_out, nor_11_out, nor_12_out, nor_13_out,
       nor_14_out, nor_15_out, nor_16_out, nor_17_out, nor_18_out, nor_19_out, nor_20_out, nor_21_out,
       nor_22_out, nor_23_out, nor_24_out, nor_25_out, nor_26_out, nor_27_out, nor_28_out, nor_29_out,
       nor_31_out;

  nor nor_1 (nor_1_out, A0, A0);
  nor nor_2 (nor_2_out, A2, A2);
  nor nor_3 (nor_3_out, A0, A0);
  nor nor_4 (nor_4_out, A2, A2);
  nor nor_5 (nor_5_out, A1, A1);
  nor nor_6 (nor_6_out, A2, A2);
  nor nor_7 (nor_7_out, A1, A1);
  nor nor_8 (nor_8_out, A0, A0);
  nor nor_9 (nor_9_out, A2, A2);
  nor nor_10 (nor_10_out, A0, A0);
  nor nor_11 (nor_11_out, A1, A1);
  nor nor_12 (nor_12_out, A2, A2);
  nand nand_1 (nand_1_out, A0, A0);
  nand nand_2 (nand_2_out, A2, A2);
  nor nor_13 (nor_13_out, A1, A1);
  nor nor_14 (nor_14_out, A0, A0);
  nor nor_15 (nor_15_out, A1, A2, A3);
  nor nor_16 (nor_16_out, A0, A0);
  nor nor_17 (nor_17_out, A1, A1);
  nor nor_18 (nor_18_out, A2, A2);
  nor nor_19 (nor_19_out, nor_1_out, A1, A2, A3);
  nor nor_20 (nor_20_out, A3, A0, A1, nor_2_out);
  nand nand_3 (nand_3_out, A1, nand_1_out);
  nand nand_4 (nand_4_out, nand_1_out, nand_2_out);
  nor nor_21 (nor_21_out, A2, nor_13_out);
  nor nor_22 (nor_22_out, nor_13_out, nor_14_out);
  nor nor_23 (nor_23_out, nor_14_out, A2, A3);
  nor nor_24 (nor_24_out, nor_3_out, A1, A3, nor_4_out);
  nor nor_25 (nor_25_out, nor_5_out, nor_6_out, A0, A3);
  nor nor_26 (nor_26_out, nor_7_out, A0, A2, A3);
  nor nor_27 (nor_27_out, nor_8_out, A1, A2, A3);
  nor nor_28 (nor_28_out, nor_9_out, A0, A1, A3);
  nor nor_29 (nor_29_out, nor_10_out, nor_11_out, nor_12_out, A3);
  nand nand_5 (SEG_E, nand_3_out, nand_4_out);
  nor nor_30 (SEG_F, nor_21_out, nor_22_out, nor_23_out);
  nor nor_31 (nor_31_out, nor_16_out, nor_17_out, nor_18_out);
  nor nor_32 (SEG_A, nor_19_out, nor_20_out);
  nor nor_33 (SEG_B, nor_24_out, nor_25_out);
  nor nor_34 (SEG_C, nor_26_out, nor_26_out);
  nor nor_35 (SEG_D, nor_27_out, nor_28_out, nor_29_out);
  nor nor_36 (SEG_G, nor_15_out, nor_31_out);
endmodule

module add1bit (
  input  MINUS,
  input  C_IN,
  input  A,
  input  B,
  output S,
  output C_OUT
);

  wire and_1_out, and_2_out, and_3_out, xor_1_out, xor_2_out;

  xor xor_1 (xor_1_out, MINUS, A);
  xor xor_2 (xor_2_out, A, B);
  and and_1 (and_1_out, xor_1_out, B);
  and and_2 (and_2_out, C_IN, B);
  and and_3 (and_3_out, xor_1_out, C_IN);
  xor xor_3 (S, xor_2_out, C_IN);
  or or_1 (C_OUT, and_1_out, and_2_out, and_3_out);
endmodule

module sub1bit (
  input  C_IN,
  input  A,
  input  B,
  output S,
  output C_OUT
);

  wire and_1_out, and_2_out, and_3_out, nand_1_out, xor_1_out;

  nand nand_1 (nand_1_out, A, A);
  xor xor_1 (xor_1_out, A, B);
  xor xor_2 (S, xor_1_out, C_IN);
  and and_1 (and_1_out, nand_1_out, B);
  and and_2 (and_2_out, C_IN, B);
  and and_3 (and_3_out, nand_1_out, C_IN);
  or or_1 (C_OUT, and_1_out, and_2_out, and_3_out);
endmodule

module add13bit (
  input  MINUS,
  input  C_IN,
  input  [12:0] Eingang_0,
  input  [12:0] Eingang_1,
  output [12:0] Ausgangbus,
  output C_OUT
);

  wire add1bit_0_c_out, add1bit_1_c_out, add1bit_2_c_out, add1bit_3_c_out, add1bit_4_c_out, add1bit_5_c_out,
       add1bit_6_c_out, add1bit_7_c_out, add1bit_8_c_out, add1bit_9_c_out, add1bit_10_c_out, add1bit_11_c_out;

  add1bit add1bit_0 (
    .MINUS(MINUS), .C_IN(C_IN), .A(Eingang_0[0]), .B(Eingang_1[0]), .S(Ausgangbus[0]), .C_OUT(add1bit_0_c_out));
  add1bit add1bit_1 (
    .MINUS(MINUS), .C_IN(add1bit_0_c_out), .A(Eingang_0[1]), .B(Eingang_1[1]), .S(Ausgangbus[1]),
    .C_OUT(add1bit_1_c_out));
  add1bit add1bit_2 (
    .MINUS(MINUS), .C_IN(add1bit_1_c_out), .A(Eingang_0[2]), .B(Eingang_1[2]), .S(Ausgangbus[2]),
    .C_OUT(add1bit_2_c_out));
  add1bit add1bit_3 (
    .MINUS(MINUS), .C_IN(add1bit_2_c_out), .A(Eingang_0[3]), .B(Eingang_1[3]), .S(Ausgangbus[3]),
    .C_OUT(add1bit_3_c_out));
  add1bit add1bit_4 (
    .MINUS(MINUS), .C_IN(add1bit_3_c_out), .A(Eingang_0[4]), .B(Eingang_1[4]), .S(Ausgangbus[4]),
    .C_OUT(add1bit_4_c_out));
  add1bit add1bit_5 (
    .MINUS(MINUS), .C_IN(add1bit_4_c_out), .A(Eingang_0[5]), .B(Eingang_1[5]), .S(Ausgangbus[5]),
    .C_OUT(add1bit_5_c_out));
  add1bit add1bit_6 (
    .MINUS(MINUS), .C_IN(add1bit_5_c_out), .A(Eingang_0[6]), .B(Eingang_1[6]), .S(Ausgangbus[6]),
    .C_OUT(add1bit_6_c_out));
  add1bit add1bit_7 (
    .MINUS(MINUS), .C_IN(add1bit_6_c_out), .A(Eingang_0[7]), .B(Eingang_1[7]), .S(Ausgangbus[7]),
    .C_OUT(add1bit_7_c_out));
  add1bit add1bit_8 (
    .MINUS(MINUS), .C_IN(add1bit_7_c_out), .A(Eingang_0[8]), .B(Eingang_1[8]), .S(Ausgangbus[8]),
    .C_OUT(add1bit_8_c_out));
  add1bit add1bit_9 (
    .MINUS(MINUS), .C_IN(add1bit_8_c_out), .A(Eingang_0[9]), .B(Eingang_1[9]), .S(Ausgangbus[9]),
    .C_OUT(add1bit_9_c_out));
  add1bit add1bit_10 (
    .MINUS(MINUS), .C_IN(add1bit_9_c_out), .A(Eingang_0[10]), .B(Eingang_1[10]), .S(Ausgangbus[10]),
    .C_OUT(add1bit_10_c_out));
  add1bit add1bit_11 (
    .MINUS(MINUS), .C_IN(add1bit_10_c_out), .A(Eingang_0[11]), .B(Eingang_1[11]), .S(Ausgangbus[11]),
    .C_OUT(add1bit_11_c_out));
  add1bit add1bit_12 (
    .MINUS(MINUS), .C_IN(add1bit_11_c_out), .A(Eingang_0[12]), .B(Eingang_1[12]), .S(Ausgangbus[12]),
    .C_OUT(C_OUT));
endmodule

module sub8bit (
  input  C_IN,
  input  A0,
  input  B0,
  input  A1,
  input  B1,
  input  A2,
  input  B2,
  input  A3,
  input  B3,
  input  A4,
  input  B4,
  input  A5,
  input  B5,
  input  A6,
  input  B6,
  input  A7,
  input  B7,
  output S0,
  output S1,
  output S2,
  output S3,
  output S4,
  output S5,
  output S6,
  output S7,
  output C_OUT
);

  wire add1bit_3_c_out, add1bit_4_c_out, add1bit_5_c_out, add1bit_6_c_out, add1bit_7_c_out, add1bit_8_c_out,
       subb1_bit_0_c_out;

  sub1bit subb1_bit_0 (.C_IN(C_IN), .A(A0), .B(B0), .S(S0), .C_OUT(subb1_bit_0_c_out));
  add1bit add1bit_3 (.C_IN(subb1_bit_0_c_out), .A(A1), .B(B1), .S(S1), .C_OUT(add1bit_3_c_out));  // open: MINUS
  add1bit add1bit_8 (.C_IN(add1bit_3_c_out), .A(A2), .B(B2), .S(S2), .C_OUT(add1bit_8_c_out));  // open: MINUS
  add1bit add1bit_5 (.C_IN(add1bit_8_c_out), .A(A3), .B(B3), .S(S3), .C_OUT(add1bit_5_c_out));  // open: MINUS
  add1bit add1bit_4 (.C_IN(add1bit_5_c_out), .A(A4), .B(B4), .S(S4), .C_OUT(add1bit_4_c_out));  // open: MINUS
  add1bit add1bit_7 (.C_IN(add1bit_4_c_out), .A(A5), .B(B5), .S(S5), .C_OUT(add1bit_7_c_out));  // open: MINUS
  add1bit add1bit_6 (.C_IN(add1bit_7_c_out), .A(A6), .B(B6), .S(S6), .C_OUT(add1bit_6_c_out));  // open: MINUS
  add1bit add1bit_2 (.C_IN(add1bit_6_c_out), .A(A7), .B(B7), .S(S7), .C_OUT(C_OUT));  // open: MINUS
endmodule

module bcd_part (
  input  A0,
  input  A1,
  input  A2,
  input  A3,
  output S0,
  output S1,
  output S2,
  output S3
);

  wire and_1_out, and_2_out, and_3_out, and_4_out, and_5_out, and_6_out, and_7_out, not_1_out, not_2_out,
       not_3_out, not_4_out, or_1_out, or_2_out, or_3_out;

  not not_1 (not_1_out, A0);
  not not_2 (not_2_out, A1);
  not not_3 (not_3_out, A2);
  not not_4 (not_4_out, A3);
  and and_1 (and_1_out, A0, not_3_out, not_4_out);
  and and_2 (and_2_out, not_1_out, A3);
  and and_3 (and_3_out, not_1_out, A1, A2);
  or or_1 (or_1_out, A1, A3);
  or or_2 (or_2_out, A0, not_3_out);
  or or_3 (or_3_out, not_1_out, not_4_out);
  and and_4 (and_4_out, not_1_out, not_2_out, A2);
  and and_5 (and_5_out, A0, A3);
  and and_6 (and_6_out, A0, A2);
  and and_7 (and_7_out, A1, A2);
  or or_4 (S0, and_1_out, and_2_out, and_3_out);
  and and_8 (S1, or_1_out, or_2_out, or_3_out);
  or or_5 (S2, and_4_out, and_5_out);
  or or_6 (S3, and_6_out, and_7_out, A3);
endmodule

module bcd (
  input  A0,
  input  A1,
  input  A2,
  input  A3,
  input  A4,
  input  A5,
  input  A6,
  input  A7,
  input  A8,
  output U1,
  output U2,
  output U3,
  output U4,
  output D1,
  output D2,
  output D3,
  output D4,
  output C1,
  output C2,
  output C3
);

  wire bcd_part_1_s0, bcd_part_1_s1, bcd_part_1_s2, bcd_part_1_s3, bcd_part_2_s0, bcd_part_2_s1,
       bcd_part_2_s2, bcd_part_2_s3, bcd_part_3_s0, bcd_part_3_s1, bcd_part_3_s2, bcd_part_3_s3,
       bcd_part_4_s0, bcd_part_4_s1, bcd_part_4_s2, bcd_part_4_s3, bcd_part_5_s0, bcd_part_5_s1,
       bcd_part_5_s2, bcd_part_5_s3, bcd_part_6_s0, bcd_part_6_s1, bcd_part_6_s2, bcd_part_6_s3,
       bcd_part_7_s0, bcd_part_7_s1, bcd_part_7_s2, bcd_part_7_s3, bcd_part_8_s0, bcd_part_8_s1,
       bcd_part_8_s2;

  bcd_part bcd_part_2 (
    .A0(A6), .A1(A7), .A2(A8), .S0(bcd_part_2_s0), .S1(bcd_part_2_s1), .S2(bcd_part_2_s2), .S3(bcd_part_2_s3));  // open: A3
  bcd_part bcd_part_5 (
    .A0(A5), .A1(bcd_part_2_s0), .A2(bcd_part_2_s1), .A3(bcd_part_2_s2), .S0(bcd_part_5_s0),
    .S1(bcd_part_5_s1), .S2(bcd_part_5_s2), .S3(bcd_part_5_s3));
  bcd_part bcd_part_1 (
    .A0(A4), .A1(bcd_part_5_s0), .A2(bcd_part_5_s1), .A3(bcd_part_5_s2), .S0(bcd_part_1_s0),
    .S1(bcd_part_1_s1), .S2(bcd_part_1_s2), .S3(bcd_part_1_s3));
  bcd_part bcd_part_6 (
    .A0(bcd_part_1_s3), .A1(bcd_part_5_s3), .A2(bcd_part_2_s3), .S0(bcd_part_6_s0), .S1(bcd_part_6_s1),
    .S2(bcd_part_6_s2), .S3(bcd_part_6_s3));  // open: A3
  bcd_part bcd_part_4 (
    .A0(bcd_part_3_s3), .A1(bcd_part_6_s0), .A2(bcd_part_6_s1), .A3(bcd_part_6_s2), .S0(bcd_part_4_s0),
    .S1(bcd_part_4_s1), .S2(bcd_part_4_s2), .S3(bcd_part_4_s3));
  bcd_part bcd_part_8 (
    .A0(bcd_part_6_s3), .S0(bcd_part_8_s0), .S1(bcd_part_8_s1), .S2(bcd_part_8_s2));  // open: A1, A2, A3, S3
  bcd_part bcd_part_11 (
    .A0(bcd_part_7_s3), .A1(bcd_part_4_s0), .A2(bcd_part_4_s1), .A3(bcd_part_4_s2), .S0(D2), .S1(D3),
    .S2(D4), .S3(C1));
  bcd_part bcd_part_10 (
    .A0(bcd_part_4_s3), .A1(bcd_part_8_s0), .A2(bcd_part_8_s1), .A3(bcd_part_8_s2), .S0(C2), .S1(C3));  // open: S2, S3
  bcd_part bcd_part_3 (
    .A0(A3), .A1(bcd_part_1_s0), .A2(bcd_part_1_s1), .A3(bcd_part_1_s2), .S0(bcd_part_3_s0),
    .S1(bcd_part_3_s1), .S2(bcd_part_3_s2), .S3(bcd_part_3_s3));
  bcd_part bcd_part_7 (
    .A0(A2), .A1(bcd_part_3_s0), .A2(bcd_part_3_s1), .A3(bcd_part_3_s2), .S0(bcd_part_7_s0),
    .S1(bcd_part_7_s1), .S2(bcd_part_7_s2), .S3(bcd_part_7_s3));
  bcd_part bcd_part_12 (
    .A0(A1), .A1(bcd_part_7_s0), .A2(bcd_part_7_s1), .A3(bcd_part_7_s2), .S0(U2), .S1(U3), .S2(U4), .S3(D1));

  assign U1 = A0;
endmodule

module Counter_13bit (
  input  Clock,
  input  Reset,
  input  Load,
  input  [12:0] Data_Load_13bit,
  output [12:0] Ausgang_Counter,
  output [12:0] Ausgang_Counter_Negiert
);

  wire [12:0] add13bit_0_ausgangbus, Multiplexer_13bit_0_out_5;

  add13bit add13bit_0 (
    .MINUS(1'b0), .C_IN(1'b0), .Eingang_0(Ausgang_Counter), .Eingang_1(13'h1),
    .Ausgangbus(add13bit_0_ausgangbus));  // open: C_OUT
  Multiplexer_13bit Multiplexer_13bit_0 (
    .Umschalter({Load, Reset}), .Eingang_0(add13bit_0_ausgangbus), .Eingang_1({13{1'b0}}),
    .Eingang_2(Data_Load_13bit), .out_5(Multiplexer_13bit_0_out_5));
  D_Flip_Flop d_ff_1 (
    .D(Multiplexer_13bit_0_out_5[0]), .clk(Clock), .Q(Ausgang_Counter[0]), .Qn(Ausgang_Counter_Negiert[0]));  // open: preset, reset
  D_Flip_Flop d_ff_2 (
    .D(Multiplexer_13bit_0_out_5[1]), .clk(Clock), .Q(Ausgang_Counter[1]), .Qn(Ausgang_Counter_Negiert[1]));  // open: preset, reset
  D_Flip_Flop d_ff_3 (
    .D(Multiplexer_13bit_0_out_5[2]), .clk(Clock), .Q(Ausgang_Counter[2]), .Qn(Ausgang_Counter_Negiert[2]));  // open: preset, reset
  D_Flip_Flop d_ff_4 (
    .D(Multiplexer_13bit_0_out_5[3]), .clk(Clock), .Q(Ausgang_Counter[3]), .Qn(Ausgang_Counter_Negiert[3]));  // open: preset, reset
  D_Flip_Flop d_ff_5 (
    .D(Multiplexer_13bit_0_out_5[4]), .clk(Clock), .Q(Ausgang_Counter[4]), .Qn(Ausgang_Counter_Negiert[4]));  // open: preset, reset
  D_Flip_Flop d_ff_6 (
    .D(Multiplexer_13bit_0_out_5[5]), .clk(Clock), .Q(Ausgang_Counter[5]), .Qn(Ausgang_Counter_Negiert[5]));  // open: preset, reset
  D_Flip_Flop d_ff_7 (
    .D(Multiplexer_13bit_0_out_5[6]), .clk(Clock), .Q(Ausgang_Counter[6]), .Qn(Ausgang_Counter_Negiert[6]));  // open: preset, reset
  D_Flip_Flop d_ff_8 (
    .D(Multiplexer_13bit_0_out_5[7]), .clk(Clock), .Q(Ausgang_Counter[7]), .Qn(Ausgang_Counter_Negiert[7]));  // open: preset, reset
  D_Flip_Flop d_ff_9 (
    .D(Multiplexer_13bit_0_out_5[8]), .clk(Clock), .Q(Ausgang_Counter[8]), .Qn(Ausgang_Counter_Negiert[8]));  // open: preset, reset
  D_Flip_Flop d_ff_10 (
    .D(Multiplexer_13bit_0_out_5[9]), .clk(Clock), .Q(Ausgang_Counter[9]), .Qn(Ausgang_Counter_Negiert[9]));  // open: preset, reset
  D_Flip_Flop d_ff_11 (
    .D(Multiplexer_13bit_0_out_5[10]), .clk(Clock), .Q(Ausgang_Counter[10]), .Qn(Ausgang_Counter_Negiert[10]));  // open: preset, reset
  D_Flip_Flop d_ff_12 (
    .D(Multiplexer_13bit_0_out_5[11]), .clk(Clock), .Q(Ausgang_Counter[11]), .Qn(Ausgang_Counter_Negiert[11]));  // open: preset, reset
  D_Flip_Flop d_ff_13 (
    .D(Multiplexer_13bit_0_out_5[12]), .clk(Clock), .Q(Ausgang_Counter[12]), .Qn(Ausgang_Counter_Negiert[12]));  // open: preset, reset
endmodule

module Schieberegister_10bit (
  input  Clock_Eingang,
  input  Data_Seriell_Eingang,
  output [9:0] Data_Parallel_Ausgang
);

  D_Flip_Flop d_ff_1 (
    .D(Data_Seriell_Eingang), .clk(Clock_Eingang), .Q(Data_Parallel_Ausgang[0]));  // open: Qn, preset, reset
  D_Flip_Flop d_ff_2 (
    .D(Data_Parallel_Ausgang[0]), .clk(Clock_Eingang), .Q(Data_Parallel_Ausgang[1]));  // open: Qn, preset, reset
  D_Flip_Flop d_ff_3 (
    .D(Data_Parallel_Ausgang[1]), .clk(Clock_Eingang), .Q(Data_Parallel_Ausgang[2]));  // open: Qn, preset, reset
  D_Flip_Flop d_ff_4 (
    .D(Data_Parallel_Ausgang[2]), .clk(Clock_Eingang), .Q(Data_Parallel_Ausgang[3]));  // open: Qn, preset, reset
  D_Flip_Flop d_ff_5 (
    .D(Data_Parallel_Ausgang[3]), .clk(Clock_Eingang), .Q(Data_Parallel_Ausgang[4]));  // open: Qn, preset, reset
  D_Flip_Flop d_ff_6 (
    .D(Data_Parallel_Ausgang[4]), .clk(Clock_Eingang), .Q(Data_Parallel_Ausgang[5]));  // open: Qn, preset, reset
  D_Flip_Flop d_ff_7 (
    .D(Data_Parallel_Ausgang[5]), .clk(Clock_Eingang), .Q(Data_Parallel_Ausgang[6]));  // open: Qn, preset, reset
  D_Flip_Flop d_ff_8 (
    .D(Data_Parallel_Ausgang[6]), .clk(Clock_Eingang), .Q(Data_Parallel_Ausgang[7]));  // open: Qn, preset, reset
  D_Flip_Flop d_ff_9 (
    .D(Data_Parallel_Ausgang[7]), .clk(Clock_Eingang), .Q(Data_Parallel_Ausgang[8]));  // open: Qn, preset, reset
  D_Flip_Flop d_ff_10 (
    .D(Data_Parallel_Ausgang[8]), .clk(Clock_Eingang), .Q(Data_Parallel_Ausgang[9]));  // open: Qn, preset, reset
endmodule

module Schiebregister_100bit (
  input  Clock_Eingang,
  input  Data_Seriell_Eingang,
  output [9:0] Data_Parallel_0x10bit_Ausgang,
  output [9:0] Data_Parallel_1x10bit_Ausgang,
  output [9:0] Data_Parallel_2x10bit_Ausgang,
  output [9:0] Data_Parallel_3x10bit_Ausgang,
  output [9:0] Data_Parallel_4x10bit_Ausgang,
  output [9:0] Data_Parallel_5x10bit_Ausgang,
  output [9:0] Data_Parallel_6x10bit_Ausgang,
  output [9:0] Data_Parallel_7x10bit_Ausgang,
  output [9:0] Data_Parallel_8x10bit_Ausgang,
  output [9:0] Data_Parallel_9x10bit_Ausgang
);

  Schieberegister_10bit Schieberegister_10bit_0 (
    .Clock_Eingang(Clock_Eingang), .Data_Seriell_Eingang(Data_Seriell_Eingang),
    .Data_Parallel_Ausgang(Data_Parallel_0x10bit_Ausgang));
  Schieberegister_10bit Schieberegister_10bit_1 (
    .Clock_Eingang(Clock_Eingang), .Data_Seriell_Eingang(Data_Parallel_0x10bit_Ausgang[9]),
    .Data_Parallel_Ausgang(Data_Parallel_1x10bit_Ausgang));
  Schieberegister_10bit Schieberegister_10bit_2 (
    .Clock_Eingang(Clock_Eingang), .Data_Seriell_Eingang(Data_Parallel_1x10bit_Ausgang[9]),
    .Data_Parallel_Ausgang(Data_Parallel_2x10bit_Ausgang));
  Schieberegister_10bit Schieberegister_10bit_3 (
    .Clock_Eingang(Clock_Eingang), .Data_Seriell_Eingang(Data_Parallel_2x10bit_Ausgang[9]),
    .Data_Parallel_Ausgang(Data_Parallel_3x10bit_Ausgang));
  Schieberegister_10bit Schieberegister_10bit_4 (
    .Clock_Eingang(Clock_Eingang), .Data_Seriell_Eingang(Data_Parallel_3x10bit_Ausgang[9]),
    .Data_Parallel_Ausgang(Data_Parallel_4x10bit_Ausgang));
  Schieberegister_10bit Schieberegister_10bit_5 (
    .Clock_Eingang(Clock_Eingang), .Data_Seriell_Eingang(Data_Parallel_4x10bit_Ausgang[9]),
    .Data_Parallel_Ausgang(Data_Parallel_5x10bit_Ausgang));
  Schieberegister_10bit Schieberegister_10bit_6 (
    .Clock_Eingang(Clock_Eingang), .Data_Seriell_Eingang(Data_Parallel_5x10bit_Ausgang[9]),
    .Data_Parallel_Ausgang(Data_Parallel_6x10bit_Ausgang));
  Schieberegister_10bit Schieberegister_10bit_7 (
    .Clock_Eingang(Clock_Eingang), .Data_Seriell_Eingang(Data_Parallel_6x10bit_Ausgang[9]),
    .Data_Parallel_Ausgang(Data_Parallel_7x10bit_Ausgang));
  Schieberegister_10bit Schieberegister_10bit_8 (
    .Clock_Eingang(Clock_Eingang), .Data_Seriell_Eingang(Data_Parallel_7x10bit_Ausgang[9]),
    .Data_Parallel_Ausgang(Data_Parallel_8x10bit_Ausgang));
  Schieberegister_10bit Schieberegister_10bit_9 (
    .Clock_Eingang(Clock_Eingang), .Data_Seriell_Eingang(Data_Parallel_8x10bit_Ausgang[9]),
    .Data_Parallel_Ausgang(Data_Parallel_9x10bit_Ausgang));
endmodule

module Addierer_Bitweise_10bit (
  input  [9:0] Data_10bit_Eingang,
  output [3:0] Data_4bit_Ausgang
);

  wire add1bit5_c_out, add1bit5_s, add1bit_0_c_out, add1bit_0_s, add1bit_1_c_out, add1bit_1_s,
       add1bit_2_c_out, add1bit_2_s, add1bit_3_c_out, add1bit_3_s, add2bit_0_c_out, add2bit_0_s0,
       add2bit_0_s1, add2bit_1_c_out, add2bit_1_s0, add2bit_1_s1, add3bit_0_s0, add3bit_0_s1, add3bit_0_s2,
       add3bit_0_s3;

  add1bit add1bit_0 (
    .MINUS(1'b0), .C_IN(1'b0), .A(Data_10bit_Eingang[0]), .B(Data_10bit_Eingang[1]), .S(add1bit_0_s),
    .C_OUT(add1bit_0_c_out));
  add1bit add1bit_1 (
    .MINUS(1'b0), .C_IN(1'b0), .A(Data_10bit_Eingang[2]), .B(Data_10bit_Eingang[3]), .S(add1bit_1_s),
    .C_OUT(add1bit_1_c_out));
  add1bit add1bit_2 (
    .MINUS(1'b0), .C_IN(1'b0), .A(Data_10bit_Eingang[4]), .B(Data_10bit_Eingang[5]), .S(add1bit_2_s),
    .C_OUT(add1bit_2_c_out));
  add1bit add1bit_3 (
    .MINUS(1'b0), .C_IN(1'b0), .A(Data_10bit_Eingang[6]), .B(Data_10bit_Eingang[7]), .S(add1bit_3_s),
    .C_OUT(add1bit_3_c_out));
  add1bit add1bit5 (
    .MINUS(1'b0), .C_IN(1'b0), .A(Data_10bit_Eingang[8]), .B(Data_10bit_Eingang[9]), .S(add1bit5_s),
    .C_OUT(add1bit5_c_out));
  add2bit add2bit_0 (
    .Minus(1'b0), .C_IN(1'b0), .A0(add1bit_0_s), .A1(add1bit_0_c_out), .B0(add1bit_1_s),
    .B1(add1bit_1_c_out), .S0(add2bit_0_s0), .S1(add2bit_0_s1), .C_OUT(add2bit_0_c_out));
  add2bit add2bit_1 (
    .Minus(1'b0), .C_IN(1'b0), .A0(add1bit_2_s), .A1(add1bit_2_c_out), .B0(add1bit_3_s),
    .B1(add1bit_3_c_out), .S0(add2bit_1_s0), .S1(add2bit_1_s1), .C_OUT(add2bit_1_c_out));
  add3bit add3bit_0 (
    .Minus(1'b0), .C_IN(1'b0), .A0(add2bit_0_s0), .A1(add2bit_0_s1), .A2(add2bit_0_c_out), .B0(add2bit_1_s0),
    .B1(add2bit_1_s1), .B2(add2bit_1_c_out), .S0(add3bit_0_s0), .S1(add3bit_0_s1), .S2(add3bit_0_s2),
    .S3(add3bit_0_s3));
  add4bit add4bit_0 (
    .Minus(1'b0), .C_IN(1'b0), .A0(add3bit_0_s0), .A1(add3bit_0_s1), .A2(add3bit_0_s2), .A3(add3bit_0_s3),
    .B0(add1bit5_s), .B1(add1bit5_c_out), .B2(1'b0), .B3(1'b0), .S0(Data_4bit_Ausgang[0]),
    .S1(Data_4bit_Ausgang[1]), .S3(Data_4bit_Ausgang[2]), .S4(Data_4bit_Ausgang[3]));  // open: C_OUT
endmodule

module add2bit (
  input  Minus,
  input  C_IN,
  input  A0,
  input  A1,
  input  B0,
  input  B1,
  output S0,
  output S1,
  output C_OUT
);

  wire add1bit_0_c_out;

  add1bit add1bit_0 (.MINUS(Minus), .C_IN(C_IN), .A(A0), .B(B0), .S(S0), .C_OUT(add1bit_0_c_out));
  add1bit add1bit_1 (.MINUS(Minus), .C_IN(add1bit_0_c_out), .A(A1), .B(B1), .S(S1), .C_OUT(C_OUT));
endmodule

module add3bit (
  input  Minus,
  input  C_IN,
  input  A0,
  input  A1,
  input  A2,
  input  B0,
  input  B1,
  input  B2,
  output S0,
  output S1,
  output S2,
  output S3
);

  wire add1bit_0_c_out, add1bit_1_c_out;

  add1bit add1bit_0 (.MINUS(Minus), .C_IN(C_IN), .A(A0), .B(B0), .S(S0), .C_OUT(add1bit_0_c_out));
  add1bit add1bit_1 (.MINUS(Minus), .C_IN(add1bit_0_c_out), .A(A1), .B(B1), .S(S1), .C_OUT(add1bit_1_c_out));
  add1bit add1bit_2 (.MINUS(Minus), .C_IN(add1bit_1_c_out), .A(A2), .B(B2), .S(S2), .C_OUT(S3));
endmodule

module add4bit (
  input  Minus,
  input  C_IN,
  input  A0,
  input  A1,
  input  A2,
  input  A3,
  input  B0,
  input  B1,
  input  B2,
  input  B3,
  output S0,
  output S1,
  output S3,
  output S4,
  output C_OUT
);

  wire add1bit_0_c_out, add1bit_1_c_out, add1bit_2_c_out;

  add1bit add1bit_0 (.MINUS(Minus), .C_IN(C_IN), .A(A0), .B(B0), .S(S0), .C_OUT(add1bit_0_c_out));
  add1bit add1bit_1 (.MINUS(Minus), .C_IN(add1bit_0_c_out), .A(A1), .B(B1), .S(S1), .C_OUT(add1bit_1_c_out));
  add1bit add1bit_2 (.MINUS(Minus), .C_IN(add1bit_1_c_out), .A(A2), .B(B2), .S(S3), .C_OUT(add1bit_2_c_out));
  add1bit add1bit_3 (.MINUS(Minus), .C_IN(add1bit_2_c_out), .A(A3), .B(B3), .S(S4), .C_OUT(C_OUT));
endmodule

module Addierer_Bitweise_100bit (
  input  [9:0] Data_10bit_Eingang_0,
  input  [9:0] Data_10bit_Eingang_1,
  input  [9:0] Data_10bit_Eingang_2,
  input  [9:0] Data_10bit_Eingang_3,
  input  [9:0] Data_10bit_Eingang_4,
  input  [9:0] Data_10bit_Eingang_5,
  input  [9:0] Data_10bit_Eingang_6,
  input  [9:0] Data_10bit_Eingang_7,
  input  [9:0] Data_10bit_Eingang_8,
  input  [9:0] Data_10bit_Eingang_9,
  output [7:0] Data_8bit_Ausgang
);

  wire add4bit_0_c_out, add4bit_0_s0, add4bit_0_s1, add4bit_0_s3, add4bit_0_s4, add4bit_1_c_out,
       add4bit_1_s0, add4bit_1_s1, add4bit_1_s3, add4bit_1_s4, add4bit_2_c_out, add4bit_2_s0, add4bit_2_s1,
       add4bit_2_s3, add4bit_2_s4, add4bit_3_c_out, add4bit_3_s0, add4bit_3_s1, add4bit_3_s3, add4bit_3_s4,
       add4bit_4_c_out, add4bit_4_s0, add4bit_4_s1, add4bit_4_s3, add4bit_4_s4, add5bit_0_c_out,
       add5bit_0_s0, add5bit_0_s1, add5bit_0_s2, add5bit_0_s3, add5bit_0_s4, add5bit_1_c_out, add5bit_1_s0,
       add5bit_1_s1, add5bit_1_s2, add5bit_1_s3, add5bit_1_s4, add6bit_0_c_out, add6bit_0_s0, add6bit_0_s1,
       add6bit_0_s2, add6bit_0_s3, add6bit_0_s4, add6bit_0_s5;
  wire [3:0] Addierer_Bitweise_10bit_0_data_4bit_ausgang, Addierer_Bitweise_10bit_1_data_4bit_ausgang,
       Addierer_Bitweise_10bit_2_data_4bit_ausgang, Addierer_Bitweise_10bit_3_data_4bit_ausgang,
       Addierer_Bitweise_10bit_4_data_4bit_ausgang, Addierer_Bitweise_10bit_5_data_4bit_ausgang,
       Addierer_Bitweise_10bit_6_data_4bit_ausgang, Addierer_Bitweise_10bit_7_data_4bit_ausgang,
       Addierer_Bitweise_10bit_8_data_4bit_ausgang, Addierer_Bitweise_10bit_9_data_4bit_ausgang;

  Addierer_Bitweise_10bit Addierer_Bitweise_10bit_0 (
    .Data_10bit_Eingang(Data_10bit_Eingang_0), .Data_4bit_Ausgang(Addierer_Bitweise_10bit_0_data_4bit_ausgang));
  Addierer_Bitweise_10bit Addierer_Bitweise_10bit_1 (
    .Data_10bit_Eingang(Data_10bit_Eingang_1), .Data_4bit_Ausgang(Addierer_Bitweise_10bit_1_data_4bit_ausgang));
  Addierer_Bitweise_10bit Addierer_Bitweise_10bit_2 (
    .Data_10bit_Eingang(Data_10bit_Eingang_2), .Data_4bit_Ausgang(Addierer_Bitweise_10bit_2_data_4bit_ausgang));
  Addierer_Bitweise_10bit Addierer_Bitweise_10bit_3 (
    .Data_10bit_Eingang(Data_10bit_Eingang_3), .Data_4bit_Ausgang(Addierer_Bitweise_10bit_3_data_4bit_ausgang));
  Addierer_Bitweise_10bit Addierer_Bitweise_10bit_4 (
    .Data_10bit_Eingang(Data_10bit_Eingang_4), .Data_4bit_Ausgang(Addierer_Bitweise_10bit_4_data_4bit_ausgang));
  Addierer_Bitweise_10bit Addierer_Bitweise_10bit_5 (
    .Data_10bit_Eingang(Data_10bit_Eingang_5), .Data_4bit_Ausgang(Addierer_Bitweise_10bit_5_data_4bit_ausgang));
  Addierer_Bitweise_10bit Addierer_Bitweise_10bit_6 (
    .Data_10bit_Eingang(Data_10bit_Eingang_6), .Data_4bit_Ausgang(Addierer_Bitweise_10bit_6_data_4bit_ausgang));
  Addierer_Bitweise_10bit Addierer_Bitweise_10bit_7 (
    .Data_10bit_Eingang(Data_10bit_Eingang_7), .Data_4bit_Ausgang(Addierer_Bitweise_10bit_7_data_4bit_ausgang));
  Addierer_Bitweise_10bit Addierer_Bitweise_10bit_8 (
    .Data_10bit_Eingang(Data_10bit_Eingang_8), .Data_4bit_Ausgang(Addierer_Bitweise_10bit_8_data_4bit_ausgang));
  Addierer_Bitweise_10bit Addierer_Bitweise_10bit_9 (
    .Data_10bit_Eingang(Data_10bit_Eingang_9), .Data_4bit_Ausgang(Addierer_Bitweise_10bit_9_data_4bit_ausgang));
  add4bit add4bit_0 (
    .Minus(1'b0), .C_IN(1'b0), .A0(Addierer_Bitweise_10bit_0_data_4bit_ausgang[0]),
    .A1(Addierer_Bitweise_10bit_0_data_4bit_ausgang[1]), .A2(Addierer_Bitweise_10bit_0_data_4bit_ausgang[2]),
    .A3(Addierer_Bitweise_10bit_0_data_4bit_ausgang[3]), .B0(Addierer_Bitweise_10bit_1_data_4bit_ausgang[0]),
    .B1(Addierer_Bitweise_10bit_1_data_4bit_ausgang[1]), .B2(Addierer_Bitweise_10bit_1_data_4bit_ausgang[2]),
    .B3(Addierer_Bitweise_10bit_1_data_4bit_ausgang[3]), .S0(add4bit_0_s0), .S1(add4bit_0_s1),
    .S3(add4bit_0_s3), .S4(add4bit_0_s4), .C_OUT(add4bit_0_c_out));
  add4bit add4bit_1 (
    .Minus(1'b0), .C_IN(1'b0), .A0(Addierer_Bitweise_10bit_2_data_4bit_ausgang[0]),
    .A1(Addierer_Bitweise_10bit_2_data_4bit_ausgang[1]), .A2(Addierer_Bitweise_10bit_2_data_4bit_ausgang[2]),
    .A3(Addierer_Bitweise_10bit_2_data_4bit_ausgang[3]), .B0(Addierer_Bitweise_10bit_3_data_4bit_ausgang[0]),
    .B1(Addierer_Bitweise_10bit_3_data_4bit_ausgang[1]), .B2(Addierer_Bitweise_10bit_3_data_4bit_ausgang[2]),
    .B3(Addierer_Bitweise_10bit_3_data_4bit_ausgang[3]), .S0(add4bit_1_s0), .S1(add4bit_1_s1),
    .S3(add4bit_1_s3), .S4(add4bit_1_s4), .C_OUT(add4bit_1_c_out));
  add4bit add4bit_2 (
    .Minus(1'b0), .C_IN(1'b0), .A0(Addierer_Bitweise_10bit_4_data_4bit_ausgang[0]),
    .A1(Addierer_Bitweise_10bit_4_data_4bit_ausgang[1]), .A2(Addierer_Bitweise_10bit_4_data_4bit_ausgang[2]),
    .A3(Addierer_Bitweise_10bit_4_data_4bit_ausgang[3]), .B0(Addierer_Bitweise_10bit_5_data_4bit_ausgang[0]),
    .B1(Addierer_Bitweise_10bit_5_data_4bit_ausgang[1]), .B2(Addierer_Bitweise_10bit_5_data_4bit_ausgang[2]),
    .B3(Addierer_Bitweise_10bit_5_data_4bit_ausgang[3]), .S0(add4bit_2_s0), .S1(add4bit_2_s1),
    .S3(add4bit_2_s3), .S4(add4bit_2_s4), .C_OUT(add4bit_2_c_out));
  add4bit add4bit_3 (
    .Minus(1'b0), .C_IN(1'b0), .A0(Addierer_Bitweise_10bit_6_data_4bit_ausgang[0]),
    .A1(Addierer_Bitweise_10bit_6_data_4bit_ausgang[1]), .A2(Addierer_Bitweise_10bit_6_data_4bit_ausgang[2]),
    .A3(Addierer_Bitweise_10bit_6_data_4bit_ausgang[3]), .B0(Addierer_Bitweise_10bit_7_data_4bit_ausgang[0]),
    .B1(Addierer_Bitweise_10bit_7_data_4bit_ausgang[1]), .B2(Addierer_Bitweise_10bit_7_data_4bit_ausgang[2]),
    .B3(Addierer_Bitweise_10bit_7_data_4bit_ausgang[3]), .S0(add4bit_3_s0), .S1(add4bit_3_s1),
    .S3(add4bit_3_s3), .S4(add4bit_3_s4), .C_OUT(add4bit_3_c_out));
  add4bit add4bit_4 (
    .Minus(1'b0), .C_IN(1'b0), .A0(Addierer_Bitweise_10bit_8_data_4bit_ausgang[0]),
    .A1(Addierer_Bitweise_10bit_8_data_4bit_ausgang[1]), .A2(Addierer_Bitweise_10bit_8_data_4bit_ausgang[2]),
    .A3(Addierer_Bitweise_10bit_8_data_4bit_ausgang[3]), .B0(Addierer_Bitweise_10bit_9_data_4bit_ausgang[0]),
    .B1(Addierer_Bitweise_10bit_9_data_4bit_ausgang[1]), .B2(Addierer_Bitweise_10bit_9_data_4bit_ausgang[2]),
    .B3(Addierer_Bitweise_10bit_9_data_4bit_ausgang[3]), .S0(add4bit_4_s0), .S1(add4bit_4_s1),
    .S3(add4bit_4_s3), .S4(add4bit_4_s4), .C_OUT(add4bit_4_c_out));
  add5bit add5bit_0 (
    .Minus(1'b0), .C_IN(1'b0), .A0(add4bit_0_s0), .A1(add4bit_0_s1), .A2(add4bit_0_s3), .A3(add4bit_0_s4),
    .A4(add4bit_0_c_out), .B0(add4bit_1_s0), .B1(add4bit_1_s1), .B2(add4bit_1_s3), .B3(add4bit_1_s4),
    .B4(add4bit_1_c_out), .S0(add5bit_0_s0), .S1(add5bit_0_s1), .S2(add5bit_0_s2), .S3(add5bit_0_s3),
    .S4(add5bit_0_s4), .C_OUT(add5bit_0_c_out));
  add5bit add5bit_1 (
    .Minus(1'b0), .C_IN(1'b0), .A0(add4bit_2_s0), .A1(add4bit_2_s1), .A2(add4bit_2_s3), .A3(add4bit_2_s4),
    .A4(add4bit_2_c_out), .B0(add4bit_3_s0), .B1(add4bit_3_s1), .B2(add4bit_3_s3), .B3(add4bit_3_s4),
    .B4(add4bit_3_c_out), .S0(add5bit_1_s0), .S1(add5bit_1_s1), .S2(add5bit_1_s2), .S3(add5bit_1_s3),
    .S4(add5bit_1_s4), .C_OUT(add5bit_1_c_out));
  add6bit add6bit_0 (
    .Minus(1'b0), .C_IN(1'b0), .A0(add5bit_0_s0), .A1(add5bit_0_s1), .A2(add5bit_0_s2), .A3(add5bit_0_s3),
    .A4(add5bit_0_s4), .A5(add5bit_0_c_out), .B0(add5bit_1_s0), .B1(add5bit_1_s1), .B2(add5bit_1_s2),
    .B3(add5bit_1_s3), .B4(add5bit_1_s4), .B5(add5bit_1_c_out), .S0(add6bit_0_s0), .S1(add6bit_0_s1),
    .S2(add6bit_0_s2), .S3(add6bit_0_s3), .S4(add6bit_0_s4), .S5(add6bit_0_s5), .C_OUT(add6bit_0_c_out));
  add7bit add7bit_0 (
    .Minus(1'b0), .C_IN(1'b0), .A0(add6bit_0_s0), .A1(add6bit_0_s1), .A2(add6bit_0_s2), .A3(add6bit_0_s3),
    .A4(add6bit_0_s4), .A5(add6bit_0_s5), .A6(add6bit_0_c_out), .B0(add4bit_4_s0), .B1(add4bit_4_s1),
    .B2(add4bit_4_s3), .B3(add4bit_4_s4), .B4(add4bit_4_c_out), .S0(Data_8bit_Ausgang[0]),
    .S1(Data_8bit_Ausgang[1]), .S2(Data_8bit_Ausgang[2]), .S3(Data_8bit_Ausgang[3]),
    .S4(Data_8bit_Ausgang[4]), .S5(Data_8bit_Ausgang[5]), .S6(Data_8bit_Ausgang[6]), .S7(Data_8bit_Ausgang[7]));  // open: B5, B7
endmodule

module add5bit (
  input  Minus,
  input  C_IN,
  input  A0,
  input  A1,
  input  A2,
  input  A3,
  input  A4,
  input  B0,
  input  B1,
  input  B2,
  input  B3,
  input  B4,
  output S0,
  output S1,
  output S2,
  output S3,
  output S4,
  output C_OUT
);

  wire add1bit_0_c_out, add1bit_1_c_out, add1bit_2_c_out, add1bit_3_c_out;

  add1bit add1bit_0 (.MINUS(Minus), .C_IN(C_IN), .A(A0), .B(B0), .S(S0), .C_OUT(add1bit_0_c_out));
  add1bit add1bit_1 (.MINUS(Minus), .C_IN(add1bit_0_c_out), .A(A1), .B(B1), .S(S1), .C_OUT(add1bit_1_c_out));
  add1bit add1bit_2 (.MINUS(Minus), .C_IN(add1bit_1_c_out), .A(A2), .B(B2), .S(S2), .C_OUT(add1bit_2_c_out));
  add1bit add1bit_3 (.MINUS(Minus), .C_IN(add1bit_2_c_out), .A(A3), .B(B3), .S(S3), .C_OUT(add1bit_3_c_out));
  add1bit add1bit_4 (.MINUS(Minus), .C_IN(add1bit_3_c_out), .A(A4), .B(B4), .S(S4), .C_OUT(C_OUT));
endmodule

module add6bit (
  input  Minus,
  input  C_IN,
  input  A0,
  input  A1,
  input  A2,
  input  A3,
  input  A4,
  input  A5,
  input  B0,
  input  B1,
  input  B2,
  input  B3,
  input  B4,
  input  B5,
  output S0,
  output S1,
  output S2,
  output S3,
  output S4,
  output S5,
  output C_OUT
);

  wire add1bit_0_c_out, add1bit_1_c_out, add1bit_2_c_out, add1bit_3_c_out, add1bit_4_c_out;

  add1bit add1bit_0 (.MINUS(Minus), .C_IN(C_IN), .A(A0), .B(B0), .S(S0), .C_OUT(add1bit_0_c_out));
  add1bit add1bit_1 (.MINUS(Minus), .C_IN(add1bit_0_c_out), .A(A1), .B(B1), .S(S1), .C_OUT(add1bit_1_c_out));
  add1bit add1bit_2 (.MINUS(Minus), .C_IN(add1bit_1_c_out), .A(A2), .B(B2), .S(S2), .C_OUT(add1bit_2_c_out));
  add1bit add1bit_3 (.MINUS(Minus), .C_IN(add1bit_2_c_out), .A(A3), .B(B3), .S(S3), .C_OUT(add1bit_3_c_out));
  add1bit add1bit_4 (.MINUS(Minus), .C_IN(add1bit_3_c_out), .A(A4), .B(B4), .S(S4), .C_OUT(add1bit_4_c_out));
  add1bit add1bit_5 (.MINUS(Minus), .C_IN(add1bit_4_c_out), .A(A5), .B(B5), .S(S5), .C_OUT(C_OUT));
endmodule

module add7bit (
  input  Minus,
  input  C_IN,
  input  A0,
  input  A1,
  input  A2,
  input  A3,
  input  A4,
  input  A5,
  input  A6,
  input  B0,
  input  B1,
  input  B2,
  input  B3,
  input  B4,
  input  B5,
  input  B7,
  output S0,
  output S1,
  output S2,
  output S3,
  output S4,
  output S5,
  output S6,
  output S7
);

  wire add1bit_0_c_out, add1bit_1_c_out, add1bit_2_c_out, add1bit_3_c_out, add1bit_4_c_out, add1bit_5_c_out;

  add1bit add1bit_0 (.MINUS(Minus), .C_IN(C_IN), .A(A0), .B(B0), .S(S0), .C_OUT(add1bit_0_c_out));
  add1bit add1bit_1 (.MINUS(Minus), .C_IN(add1bit_0_c_out), .A(A1), .B(B1), .S(S1), .C_OUT(add1bit_1_c_out));
  add1bit add1bit_2 (.MINUS(Minus), .C_IN(add1bit_1_c_out), .A(A2), .B(B2), .S(S2), .C_OUT(add1bit_2_c_out));
  add1bit add1bit_3 (.MINUS(Minus), .C_IN(add1bit_2_c_out), .A(A3), .B(B3), .S(S3), .C_OUT(add1bit_3_c_out));
  add1bit add1bit_4 (.MINUS(Minus), .C_IN(add1bit_3_c_out), .A(A4), .B(B4), .S(S4), .C_OUT(add1bit_4_c_out));
  add1bit add1bit_5 (.MINUS(Minus), .C_IN(add1bit_4_c_out), .A(A5), .B(B5), .S(S5), .C_OUT(add1bit_5_c_out));
  add1bit add1bit_6 (.MINUS(Minus), .C_IN(add1bit_5_c_out), .A(A6), .B(B7), .S(S6), .C_OUT(S7));
endmodule

module add8bit (
  input  Minus,
  input  C_IN,
  input  A0,
  input  A1,
  input  A2,
  input  A3,
  input  A4,
  input  A5,
  input  A6,
  input  A7,
  input  B0,
  input  B1,
  input  B2,
  input  B3,
  input  B4,
  input  B5,
  input  B6,
  input  B7,
  output S0,
  output S1,
  output S2,
  output S3,
  output S4,
  output S5,
  output S6,
  output S7,
  output C_OUT
);

  wire add1bit_0_c_out, add1bit_1_c_out, add1bit_2_c_out, add1bit_3_c_out, add1bit_4_c_out, add1bit_6_c_out,
       add1bit_7_c_out;

  add1bit add1bit_0 (.MINUS(Minus), .C_IN(C_IN), .A(A0), .B(B0), .S(S0), .C_OUT(add1bit_0_c_out));
  add1bit add1bit_1 (.MINUS(Minus), .C_IN(add1bit_0_c_out), .A(A1), .B(B1), .S(S1), .C_OUT(add1bit_1_c_out));
  add1bit add1bit_2 (.MINUS(Minus), .C_IN(add1bit_1_c_out), .A(A2), .B(B2), .S(S2), .C_OUT(add1bit_2_c_out));
  add1bit add1bit_3 (.MINUS(Minus), .C_IN(add1bit_2_c_out), .A(A3), .B(B3), .S(S3), .C_OUT(add1bit_3_c_out));
  add1bit add1bit_4 (.MINUS(Minus), .C_IN(add1bit_3_c_out), .A(A4), .B(B4), .S(S4), .C_OUT(add1bit_4_c_out));
  add1bit add1bit_6 (.MINUS(Minus), .C_IN(add1bit_4_c_out), .A(A5), .B(B5), .S(S5), .C_OUT(add1bit_6_c_out));
  add1bit add1bit_7 (.MINUS(Minus), .C_IN(add1bit_6_c_out), .A(A6), .B(B6), .S(S6), .C_OUT(add1bit_7_c_out));
  add1bit add1bit_8 (.MINUS(add1bit_7_c_out), .C_IN(Minus), .A(A7), .B(B7), .S(S7), .C_OUT(C_OUT));
endmodule

module Addierer_Bitweise_200bit (
  input  [9:0] Data_10bit_Eingang_0,
  input  [9:0] Data_10bit_Eingang_1,
  input  [9:0] Data_10bit_Eingang_2,
  input  [9:0] Data_10bit_Eingang_3,
  input  [9:0] Data_10bit_Eingang_4,
  input  [9:0] Data_10bit_Eingang_5,
  input  [9:0] Data_10bit_Eingang_6,
  input  [9:0] Data_10bit_Eingang_7,
  input  [9:0] Data_10bit_Eingang_8,
  input  [9:0] Data_10bit_Eingang_9,
  input  [9:0] Data_10bit_Eingang_10,
  input  [9:0] Data_10bit_Eingang_11,
  input  [9:0] Data_10bit_Eingang_12,
  input  [9:0] Data_10bit_Eingang_13,
  input  [9:0] Data_10bit_Eingang_14,
  input  [9:0] Data_10bit_Eingang_15,
  input  [9:0] Data_10bit_Eingang_16,
  input  [9:0] Data_10bit_Eingang_17,
  input  [9:0] Data_10bit_Eingang_18,
  input  [9:0] Data_10bit_Eingang_19,
  output [7:0] Data_8bit_Ausgang
);

  wire [7:0] Addierer_Bitweise_100bit_0_data_8bit_ausgang, Addierer_Bitweise_100bit_1_data_8bit_ausgang;

  Addierer_Bitweise_100bit Addierer_Bitweise_100bit_0 (
    .Data_10bit_Eingang_0(Data_10bit_Eingang_0), .Data_10bit_Eingang_1(Data_10bit_Eingang_1),
    .Data_10bit_Eingang_2(Data_10bit_Eingang_2), .Data_10bit_Eingang_3(Data_10bit_Eingang_3),
    .Data_10bit_Eingang_4(Data_10bit_Eingang_4), .Data_10bit_Eingang_5(Data_10bit_Eingang_5),
    .Data_10bit_Eingang_6(Data_10bit_Eingang_6), .Data_10bit_Eingang_7(Data_10bit_Eingang_7),
    .Data_10bit_Eingang_8(Data_10bit_Eingang_8), .Data_10bit_Eingang_9(Data_10bit_Eingang_9),
    .Data_8bit_Ausgang(Addierer_Bitweise_100bit_0_data_8bit_ausgang));
  Addierer_Bitweise_100bit Addierer_Bitweise_100bit_1 (
    .Data_10bit_Eingang_0(Data_10bit_Eingang_10), .Data_10bit_Eingang_1(Data_10bit_Eingang_11),
    .Data_10bit_Eingang_2(Data_10bit_Eingang_12), .Data_10bit_Eingang_3(Data_10bit_Eingang_13),
    .Data_10bit_Eingang_4(Data_10bit_Eingang_14), .Data_10bit_Eingang_5(Data_10bit_Eingang_15),
    .Data_10bit_Eingang_6(Data_10bit_Eingang_16), .Data_10bit_Eingang_7(Data_10bit_Eingang_17),
    .Data_10bit_Eingang_8(Data_10bit_Eingang_18), .Data_10bit_Eingang_9(Data_10bit_Eingang_19),
    .Data_8bit_Ausgang(Addierer_Bitweise_100bit_1_data_8bit_ausgang));
  add8bit add8bit_0 (
    .Minus(1'b0), .C_IN(1'b0), .A0(Addierer_Bitweise_100bit_0_data_8bit_ausgang[0]),
    .A1(Addierer_Bitweise_100bit_0_data_8bit_ausgang[1]),
    .A2(Addierer_Bitweise_100bit_0_data_8bit_ausgang[2]),
    .A3(Addierer_Bitweise_100bit_0_data_8bit_ausgang[3]),
    .A4(Addierer_Bitweise_100bit_0_data_8bit_ausgang[4]),
    .A5(Addierer_Bitweise_100bit_0_data_8bit_ausgang[5]),
    .A6(Addierer_Bitweise_100bit_0_data_8bit_ausgang[6]),
    .A7(Addierer_Bitweise_100bit_0_data_8bit_ausgang[7]),
    .B0(Addierer_Bitweise_100bit_1_data_8bit_ausgang[0]),
    .B1(Addierer_Bitweise_100bit_1_data_8bit_ausgang[1]),
    .B2(Addierer_Bitweise_100bit_1_data_8bit_ausgang[2]),
    .B3(Addierer_Bitweise_100bit_1_data_8bit_ausgang[3]),
    .B4(Addierer_Bitweise_100bit_1_data_8bit_ausgang[4]),
    .B5(Addierer_Bitweise_100bit_1_data_8bit_ausgang[5]),
    .B6(Addierer_Bitweise_100bit_1_data_8bit_ausgang[6]),
    .B7(Addierer_Bitweise_100bit_1_data_8bit_ausgang[7]), .S0(Data_8bit_Ausgang[0]),
    .S1(Data_8bit_Ausgang[1]), .S2(Data_8bit_Ausgang[2]), .S3(Data_8bit_Ausgang[3]),
    .S4(Data_8bit_Ausgang[4]), .S5(Data_8bit_Ausgang[5]), .S6(Data_8bit_Ausgang[6]), .S7(Data_8bit_Ausgang[7]));  // open: C_OUT
endmodule

module Decode_Jahr (
  input  [7:0] Data_Jahr_8bit_Eingang,
  output [7:0] Data_Jahr_8bit_Ausgang
);

  wire and_1_out, and_2_out, and_3_out, and_4_out, and_5_out, and_6_out, and_7_out, and_8_out, and_9_out,
       and_10_out, and_11_out, and_12_out, and_13_out, and_14_out, and_15_out, and_16_out, and_17_out,
       and_18_out, not_1_out, not_2_out, not_3_out, not_4_out, not_5_out, not_6_out, not_7_out, not_8_out,
       not_9_out, not_10_out, not_11_out, not_12_out, not_13_out, not_14_out, not_15_out, not_16_out,
       not_17_out, not_18_out, not_19_out, not_20_out, not_21_out, not_22_out, not_23_out, not_24_out,
       not_25_out, not_26_out, or_1_out, or_2_out, or_3_out, or_4_out, or_5_out;

  and and_1 (and_1_out, Data_Jahr_8bit_Eingang[7], Data_Jahr_8bit_Eingang[6], Data_Jahr_8bit_Eingang[4]);
  and and_2 (and_2_out, Data_Jahr_8bit_Eingang[7], Data_Jahr_8bit_Eingang[6], Data_Jahr_8bit_Eingang[5]);
  not not_1 (not_1_out, Data_Jahr_8bit_Eingang[7]);
  not not_2 (not_2_out, Data_Jahr_8bit_Eingang[6]);
  not not_3 (not_3_out, Data_Jahr_8bit_Eingang[5]);
  not not_4 (not_4_out, Data_Jahr_8bit_Eingang[4]);
  not not_5 (not_5_out, Data_Jahr_8bit_Eingang[7]);
  not not_6 (not_6_out, Data_Jahr_8bit_Eingang[5]);
  not not_7 (not_7_out, Data_Jahr_8bit_Eingang[7]);
  not not_8 (not_8_out, Data_Jahr_8bit_Eingang[4]);
  not not_9 (not_9_out, Data_Jahr_8bit_Eingang[5]);
  not not_10 (not_10_out, Data_Jahr_8bit_Eingang[4]);
  not not_11 (not_11_out, Data_Jahr_8bit_Eingang[6]);
  not not_12 (not_12_out, Data_Jahr_8bit_Eingang[7]);
  not not_13 (not_13_out, Data_Jahr_8bit_Eingang[6]);
  not not_14 (not_14_out, Data_Jahr_8bit_Eingang[7]);
  not not_15 (not_15_out, Data_Jahr_8bit_Eingang[4]);
  not not_16 (not_16_out, Data_Jahr_8bit_Eingang[7]);
  not not_17 (not_17_out, Data_Jahr_8bit_Eingang[5]);
  not not_18 (not_18_out, Data_Jahr_8bit_Eingang[6]);
  not not_19 (not_19_out, Data_Jahr_8bit_Eingang[5]);
  not not_20 (not_20_out, Data_Jahr_8bit_Eingang[5]);
  not not_21 (not_21_out, Data_Jahr_8bit_Eingang[4]);
  not not_22 (not_22_out, Data_Jahr_8bit_Eingang[6]);
  not not_23 (not_23_out, Data_Jahr_8bit_Eingang[7]);
  not not_24 (not_24_out, Data_Jahr_8bit_Eingang[4]);
  not not_25 (not_25_out, Data_Jahr_8bit_Eingang[5]);
  not not_26 (not_26_out, Data_Jahr_8bit_Eingang[4]);
  or or_1 (or_1_out, and_1_out, and_2_out);
  and and_3 (and_3_out, not_1_out, Data_Jahr_8bit_Eingang[6], Data_Jahr_8bit_Eingang[5], Data_Jahr_8bit_Eingang[4]);
  and and_4 (and_4_out, Data_Jahr_8bit_Eingang[7], not_2_out);
  and and_5 (and_5_out, Data_Jahr_8bit_Eingang[7], not_3_out, not_4_out);
  and and_6 (and_6_out, not_5_out, Data_Jahr_8bit_Eingang[6], not_6_out);
  and and_7 (and_7_out, not_7_out, Data_Jahr_8bit_Eingang[6], not_8_out);
  and and_8 (and_8_out, Data_Jahr_8bit_Eingang[6], not_9_out, not_10_out);
  and and_9 (and_9_out, Data_Jahr_8bit_Eingang[7], not_11_out, Data_Jahr_8bit_Eingang[5]);
  and and_10 (and_10_out, not_12_out, not_13_out, Data_Jahr_8bit_Eingang[5]);
  and and_11 (and_11_out, not_14_out, Data_Jahr_8bit_Eingang[5], not_15_out);
  and and_12 (and_12_out, not_16_out, Data_Jahr_8bit_Eingang[6], not_17_out, Data_Jahr_8bit_Eingang[4]);
  and and_13 (and_13_out, Data_Jahr_8bit_Eingang[7], not_18_out, not_19_out);
  and and_14 (and_14_out, Data_Jahr_8bit_Eingang[7], not_20_out, not_21_out);
  and and_15 (and_15_out, Data_Jahr_8bit_Eingang[7], Data_Jahr_8bit_Eingang[6], Data_Jahr_8bit_Eingang[5]);
  and and_16 (and_16_out, not_22_out, Data_Jahr_8bit_Eingang[4]);
  and and_17 (and_17_out, not_23_out, Data_Jahr_8bit_Eingang[6], not_24_out);
  and and_18 (and_18_out, Data_Jahr_8bit_Eingang[6], not_25_out, not_26_out);
  or or_2 (or_2_out, and_3_out, and_4_out, and_5_out);
  or or_3 (or_3_out, and_6_out, and_7_out, and_8_out, and_9_out);
  or or_4 (or_4_out, and_10_out, and_11_out, and_12_out, and_13_out, and_14_out, and_15_out);
  or or_5 (or_5_out, and_16_out, and_17_out, and_18_out);
  add8bit add8bit_1 (
    .Minus(1'b0), .C_IN(1'b0), .A0(Data_Jahr_8bit_Eingang[0]), .A1(Data_Jahr_8bit_Eingang[1]),
    .A2(Data_Jahr_8bit_Eingang[2]), .A3(Data_Jahr_8bit_Eingang[3]), .A4(1'b0), .A5(1'b0), .A6(1'b0),
    .A7(1'b0), .B0(1'b0), .B1(Data_Jahr_8bit_Eingang[4]), .B2(Data_Jahr_8bit_Eingang[5]), .B3(or_5_out),
    .B4(or_4_out), .B5(or_3_out), .B6(or_2_out), .B7(or_1_out), .S0(Data_Jahr_8bit_Ausgang[0]),
    .S1(Data_Jahr_8bit_Ausgang[1]), .S2(Data_Jahr_8bit_Ausgang[2]), .S3(Data_Jahr_8bit_Ausgang[3]),
    .S4(Data_Jahr_8bit_Ausgang[4]), .S5(Data_Jahr_8bit_Ausgang[5]), .S6(Data_Jahr_8bit_Ausgang[6]),
    .S7(Data_Jahr_8bit_Ausgang[7]));  // open: C_OUT
endmodule

module test (
  input  in_1,
  input  in_2,
  input  in_3,
  input  in_4,
  output out_5,
  output out_6,
  output out_7,
  output out_8,
  output out_9,
  output out_10,
  output out_11,
  output out_12
);
endmodule

module Deode_Monat (
  input  [4:0] Data_Monat_5bit_Eingang,
  output [4:0] Data_Jahr_5bit_Ausgang
);

  add4bit add4bit_1 (
    .Minus(1'b0), .C_IN(1'b0), .A0(Data_Monat_5bit_Eingang[0]), .A1(Data_Monat_5bit_Eingang[1]),
    .A2(Data_Monat_5bit_Eingang[2]), .A3(Data_Monat_5bit_Eingang[3]), .B0(1'b0),
    .B1(Data_Monat_5bit_Eingang[4]), .B2(1'b0), .B3(Data_Monat_5bit_Eingang[4]),
    .S0(Data_Jahr_5bit_Ausgang[0]), .S1(Data_Jahr_5bit_Ausgang[1]), .S3(Data_Jahr_5bit_Ausgang[2]),
    .S4(Data_Jahr_5bit_Ausgang[3]), .C_OUT(Data_Jahr_5bit_Ausgang[4]));
endmodule

module Decode_Tag (
  input  [5:0] Data_Tag_6bit_Eingang,
  output [5:0] Data_Tag_6bit_Ausgang
);

  add5bit add5bit_1 (
    .Minus(1'b0), .C_IN(1'b0), .A0(Data_Tag_6bit_Eingang[0]), .A1(Data_Tag_6bit_Eingang[1]),
    .A2(Data_Tag_6bit_Eingang[2]), .A3(Data_Tag_6bit_Eingang[3]), .A4(1'b0), .B0(1'b0),
    .B1(Data_Tag_6bit_Eingang[4]), .B2(Data_Tag_6bit_Eingang[5]), .B3(Data_Tag_6bit_Eingang[4]),
    .B4(Data_Tag_6bit_Eingang[5]), .S0(Data_Tag_6bit_Ausgang[0]), .S1(Data_Tag_6bit_Ausgang[1]),
    .S2(Data_Tag_6bit_Ausgang[2]), .S3(Data_Tag_6bit_Ausgang[3]), .S4(Data_Tag_6bit_Ausgang[4]),
    .C_OUT(Data_Tag_6bit_Ausgang[5]));
endmodule

module Decode_Stunde (
  input  [5:0] Data_Stunde_6bit_Eingang,
  output [5:0] Data_Stunde_6bit_Ausgang
);

  add5bit add5bit_1 (
    .Minus(1'b0), .C_IN(1'b0), .A0(Data_Stunde_6bit_Eingang[0]), .A1(Data_Stunde_6bit_Eingang[1]),
    .A2(Data_Stunde_6bit_Eingang[2]), .A3(Data_Stunde_6bit_Eingang[3]), .A4(1'b0), .B0(1'b0),
    .B1(Data_Stunde_6bit_Eingang[4]), .B2(Data_Stunde_6bit_Eingang[5]), .B3(Data_Stunde_6bit_Eingang[4]),
    .B4(Data_Stunde_6bit_Eingang[5]), .S0(Data_Stunde_6bit_Ausgang[0]), .S1(Data_Stunde_6bit_Ausgang[1]),
    .S2(Data_Stunde_6bit_Ausgang[2]), .S3(Data_Stunde_6bit_Ausgang[3]), .S4(Data_Stunde_6bit_Ausgang[4]),
    .C_OUT(Data_Stunde_6bit_Ausgang[5]));
endmodule

module Decode_Minute (
  input  [6:0] Data_Minute_7bit_Eingang,
  output [6:0] Data_Minute_7bit_Ausgang
);

  wire and_1_out, and_2_out, and_3_out, and_4_out, and_5_out, not_1_out, not_2_out, not_3_out, not_4_out,
       not_5_out, or_1_out, or_2_out;

  not not_1 (not_1_out, Data_Minute_7bit_Eingang[6]);
  not not_2 (not_2_out, Data_Minute_7bit_Eingang[4]);
  not not_3 (not_3_out, Data_Minute_7bit_Eingang[5]);
  not not_4 (not_4_out, Data_Minute_7bit_Eingang[6]);
  not not_5 (not_5_out, Data_Minute_7bit_Eingang[4]);
  and and_1 (and_1_out, not_1_out, Data_Minute_7bit_Eingang[5]);
  and and_2 (and_2_out, Data_Minute_7bit_Eingang[5], not_2_out);
  and and_3 (and_3_out, Data_Minute_7bit_Eingang[6], not_3_out, Data_Minute_7bit_Eingang[4]);
  and and_4 (and_4_out, not_4_out, Data_Minute_7bit_Eingang[4]);
  and and_5 (and_5_out, Data_Minute_7bit_Eingang[6], not_5_out);
  or or_1 (or_1_out, and_1_out, and_2_out, and_3_out);
  or or_2 (or_2_out, and_4_out, and_5_out);
  add6bit add6bit_1 (
    .Minus(1'b0), .C_IN(1'b0), .A0(Data_Minute_7bit_Eingang[0]), .A1(Data_Minute_7bit_Eingang[1]),
    .A2(Data_Minute_7bit_Eingang[2]), .A3(Data_Minute_7bit_Eingang[3]), .A4(1'b0), .A5(1'b0), .B0(1'b0),
    .B1(Data_Minute_7bit_Eingang[4]), .B2(Data_Minute_7bit_Eingang[5]), .B3(or_2_out), .B4(or_1_out),
    .B5(Data_Minute_7bit_Eingang[6]), .S0(Data_Minute_7bit_Ausgang[0]), .S1(Data_Minute_7bit_Ausgang[1]),
    .S2(Data_Minute_7bit_Ausgang[2]), .S3(Data_Minute_7bit_Ausgang[3]), .S4(Data_Minute_7bit_Ausgang[4]),
    .S5(Data_Minute_7bit_Ausgang[5]), .C_OUT(Data_Minute_7bit_Ausgang[6]));
endmodule

module Counter_1ms (
  input  Clock_2kHz,
  output out_2
);

  T_Flip_Flop t_ff_1 (.T(1'b1), .clk(Clock_2kHz), .Q(out_2));  // open: Qn, reset, preset
endmodule

module Counter_2bit (
  input  in_1,
  input  in_2,
  output [1:0] out_3,
  output [1:0] out_4
);

  wire [1:0] add2bit_1_s0, multiplexer_2bit_1_out_5;

  add2bit add2bit_1 (
    .A0(out_3[0]), .A1(out_3[1]), .B0(1'b1), .B1(1'b0), .S0(add2bit_1_s0[0]), .S1(add2bit_1_s0[1]));  // open: Minus, C_IN, C_OUT
  Multiplexer_2bit multiplexer_2bit_1 (
    .in_1(add2bit_1_s0), .in_2(2'b00), .in_3(2'b00), .in_4({1'b0, in_2}), .out_5(multiplexer_2bit_1_out_5));
  D_Flip_Flop d_ff_1 (.D(multiplexer_2bit_1_out_5[0]), .clk(in_1), .Q(out_3[0]), .Qn(out_4[0]));  // open: preset, reset
  D_Flip_Flop d_ff_2 (.D(multiplexer_2bit_1_out_5[1]), .clk(in_1), .Q(out_3[1]), .Qn(out_4[1]));  // open: preset, reset
endmodule

module Multiplexer_2bit (
  input  [1:0] in_1,
  input  [1:0] in_2,
  input  [1:0] in_3,
  input  [1:0] in_4,
  output [1:0] out_5
);

  Multiplexer_1bit multiplexer_1bit_1 (
    .I_0(in_1[0]), .I_1(in_2[0]), .I_2(in_3[0]), .Umschalter(in_4), .Ausgang(out_5[0]));
  Multiplexer_1bit multiplexer_1bit_2 (
    .I_0(in_1[1]), .I_1(in_2[1]), .I_2(in_3[1]), .Umschalter(in_4), .Ausgang(out_5[1]));
endmodule

module Signalbreite_Zusammenzaehlen (
  input  Clock_2kHz,
  input  Data_Seriell,
  output [7:0] out_3
);

  wire counter_1ms_1_out_2;
  wire [9:0] schieberegister_200bit_1_out_3, schieberegister_200bit_1_out_4, schieberegister_200bit_1_out_5,
       schieberegister_200bit_1_out_6, schieberegister_200bit_1_out_7, schieberegister_200bit_1_out_8,
       schieberegister_200bit_1_out_9, schieberegister_200bit_1_out_10, schieberegister_200bit_1_out_11,
       schieberegister_200bit_1_out_12, schieberegister_200bit_1_out_13, schieberegister_200bit_1_out_14,
       schieberegister_200bit_1_out_15, schieberegister_200bit_1_out_16, schieberegister_200bit_1_out_17,
       schieberegister_200bit_1_out_18, schieberegister_200bit_1_out_19, schieberegister_200bit_1_out_20,
       schieberegister_200bit_1_out_21, schieberegister_200bit_1_out_22;

  Counter_1ms counter_1ms_1 (.Clock_2kHz(Clock_2kHz), .out_2(counter_1ms_1_out_2));
  Schieberegister_200bit schieberegister_200bit_1 (
    .in_1(counter_1ms_1_out_2), .in_2(Data_Seriell), .out_3(schieberegister_200bit_1_out_3),
    .out_4(schieberegister_200bit_1_out_4), .out_5(schieberegister_200bit_1_out_5),
    .out_6(schieberegister_200bit_1_out_6), .out_7(schieberegister_200bit_1_out_7),
    .out_8(schieberegister_200bit_1_out_8), .out_9(schieberegister_200bit_1_out_9),
    .out_10(schieberegister_200bit_1_out_10), .out_11(schieberegister_200bit_1_out_11),
    .out_12(schieberegister_200bit_1_out_12), .out_13(schieberegister_200bit_1_out_13),
    .out_14(schieberegister_200bit_1_out_14), .out_15(schieberegister_200bit_1_out_15),
    .out_16(schieberegister_200bit_1_out_16), .out_17(schieberegister_200bit_1_out_17),
    .out_18(schieberegister_200bit_1_out_18), .out_19(schieberegister_200bit_1_out_19),
    .out_20(schieberegister_200bit_1_out_20), .out_21(schieberegister_200bit_1_out_21),
    .out_22(schieberegister_200bit_1_out_22));
  Addierer_Bitweise_200bit addierer_bitweise_200bit_1 (
    .Data_10bit_Eingang_0(schieberegister_200bit_1_out_3),
    .Data_10bit_Eingang_1(schieberegister_200bit_1_out_4),
    .Data_10bit_Eingang_2(schieberegister_200bit_1_out_5),
    .Data_10bit_Eingang_3(schieberegister_200bit_1_out_6),
    .Data_10bit_Eingang_4(schieberegister_200bit_1_out_7),
    .Data_10bit_Eingang_5(schieberegister_200bit_1_out_8),
    .Data_10bit_Eingang_6(schieberegister_200bit_1_out_9),
    .Data_10bit_Eingang_7(schieberegister_200bit_1_out_10),
    .Data_10bit_Eingang_8(schieberegister_200bit_1_out_11),
    .Data_10bit_Eingang_9(schieberegister_200bit_1_out_12),
    .Data_10bit_Eingang_10(schieberegister_200bit_1_out_13),
    .Data_10bit_Eingang_11(schieberegister_200bit_1_out_14),
    .Data_10bit_Eingang_12(schieberegister_200bit_1_out_15),
    .Data_10bit_Eingang_13(schieberegister_200bit_1_out_16),
    .Data_10bit_Eingang_14(schieberegister_200bit_1_out_17),
    .Data_10bit_Eingang_15(schieberegister_200bit_1_out_18),
    .Data_10bit_Eingang_16(schieberegister_200bit_1_out_19),
    .Data_10bit_Eingang_17(schieberegister_200bit_1_out_20),
    .Data_10bit_Eingang_18(schieberegister_200bit_1_out_21),
    .Data_10bit_Eingang_19(schieberegister_200bit_1_out_22), .Data_8bit_Ausgang(out_3));
endmodule

module Schieberegister_200bit (
  input  in_1,
  input  in_2,
  output [9:0] out_3,
  output [9:0] out_4,
  output [9:0] out_5,
  output [9:0] out_6,
  output [9:0] out_7,
  output [9:0] out_8,
  output [9:0] out_9,
  output [9:0] out_10,
  output [9:0] out_11,
  output [9:0] out_12,
  output [9:0] out_13,
  output [9:0] out_14,
  output [9:0] out_15,
  output [9:0] out_16,
  output [9:0] out_17,
  output [9:0] out_18,
  output [9:0] out_19,
  output [9:0] out_20,
  output [9:0] out_21,
  output [9:0] out_22
);

  Schiebregister_100bit schiebregister_100bit_1 (
    .Clock_Eingang(in_1), .Data_Seriell_Eingang(in_2), .Data_Parallel_0x10bit_Ausgang(out_3),
    .Data_Parallel_1x10bit_Ausgang(out_4), .Data_Parallel_2x10bit_Ausgang(out_5),
    .Data_Parallel_3x10bit_Ausgang(out_6), .Data_Parallel_4x10bit_Ausgang(out_7),
    .Data_Parallel_5x10bit_Ausgang(out_8), .Data_Parallel_6x10bit_Ausgang(out_9),
    .Data_Parallel_7x10bit_Ausgang(out_10), .Data_Parallel_8x10bit_Ausgang(out_11),
    .Data_Parallel_9x10bit_Ausgang(out_12));
  Schiebregister_100bit schiebregister_100bit_2 (
    .Clock_Eingang(in_1), .Data_Seriell_Eingang(out_12[9]), .Data_Parallel_0x10bit_Ausgang(out_13),
    .Data_Parallel_1x10bit_Ausgang(out_14), .Data_Parallel_2x10bit_Ausgang(out_15),
    .Data_Parallel_3x10bit_Ausgang(out_16), .Data_Parallel_4x10bit_Ausgang(out_17),
    .Data_Parallel_5x10bit_Ausgang(out_18), .Data_Parallel_6x10bit_Ausgang(out_19),
    .Data_Parallel_7x10bit_Ausgang(out_20), .Data_Parallel_8x10bit_Ausgang(out_21),
    .Data_Parallel_9x10bit_Ausgang(out_22));
endmodule

module Decode_DCF77_Signal (
  input  in_1,
  input  in_2,
  output out_3,
  output out_4
);

  wire add8bit_1_c_out, add8bit_3_c_out, and_1_out, and_2_out, counter_300ms_1_out_2,
       multiplexer_1bit_1_ausgang;
  wire [0:0] or_1_out;
  wire [7:0] signalbreite_zusammenzaehlen_1_out_3;

  Signalbreite_Zusammenzaehlen signalbreite_zusammenzaehlen_1 (
    .Clock_2kHz(in_1), .Data_Seriell(in_2), .out_3(signalbreite_zusammenzaehlen_1_out_3));
  add8bit add8bit_1 (
    .A0(1'b1), .A1(1'b1), .A2(1'b1), .A3(1'b1), .A4(1'b1), .A5(1'b1), .A6(1'b1), .A7(1'b1),
    .B0(signalbreite_zusammenzaehlen_1_out_3[0]), .B1(signalbreite_zusammenzaehlen_1_out_3[1]),
    .B2(signalbreite_zusammenzaehlen_1_out_3[2]), .B3(signalbreite_zusammenzaehlen_1_out_3[3]),
    .B4(signalbreite_zusammenzaehlen_1_out_3[4]), .B5(signalbreite_zusammenzaehlen_1_out_3[5]),
    .B6(signalbreite_zusammenzaehlen_1_out_3[6]), .B7(signalbreite_zusammenzaehlen_1_out_3[7]),
    .C_OUT(add8bit_1_c_out));  // open: Minus, C_IN, S0, S1, S2, S3, S4, S5, S6, S7
  add8bit add8bit_2 (
    .A0(1'b1), .A1(1'b1), .A2(1'b1), .A3(1'b1), .A4(1'b1), .A5(1'b1), .A6(1'b1), .A7(1'b1),
    .B0(signalbreite_zusammenzaehlen_1_out_3[0]), .B1(signalbreite_zusammenzaehlen_1_out_3[1]),
    .B2(signalbreite_zusammenzaehlen_1_out_3[2]), .B3(signalbreite_zusammenzaehlen_1_out_3[3]),
    .B4(signalbreite_zusammenzaehlen_1_out_3[4]), .B5(signalbreite_zusammenzaehlen_1_out_3[5]),
    .B6(signalbreite_zusammenzaehlen_1_out_3[6]), .B7(signalbreite_zusammenzaehlen_1_out_3[7]), .C_OUT(out_4));  // open: Minus, C_IN, S0, S1, S2, S3, S4, S5, S6, S7
  add8bit add8bit_3 (
    .A0(signalbreite_zusammenzaehlen_1_out_3[0]), .A1(signalbreite_zusammenzaehlen_1_out_3[1]),
    .A2(signalbreite_zusammenzaehlen_1_out_3[2]), .A3(signalbreite_zusammenzaehlen_1_out_3[3]),
    .A4(signalbreite_zusammenzaehlen_1_out_3[4]), .A5(signalbreite_zusammenzaehlen_1_out_3[5]),
    .A6(signalbreite_zusammenzaehlen_1_out_3[6]), .A7(signalbreite_zusammenzaehlen_1_out_3[7]), .B0(1'b1),
    .B1(1'b1), .B2(1'b1), .B3(1'b1), .B4(1'b1), .B5(1'b1), .B6(1'b1), .B7(1'b1), .C_OUT(add8bit_3_c_out));  // open: Minus, C_IN, S0, S1, S2, S3, S4, S5, S6, S7
  and and_1 (and_1_out, ~counter_300ms_1_out_2, add8bit_1_c_out);  // AND_Gate
  and and_2 (and_2_out, ~counter_300ms_1_out_2, or_1_out[0]);  // AND_Gate
  or or_1 (or_1_out[0], and_1_out, and_2_out);
  Multiplexer_1bit multiplexer_1bit_1 (
    .I_0(in_1), .I_1(1'b0), .I_2(1'b0), .Umschalter({1'b0, or_1_out[0]}), .Ausgang(multiplexer_1bit_1_ausgang));
  Counter_300ms counter_300ms_1 (.in_1(multiplexer_1bit_1_ausgang), .out_2(counter_300ms_1_out_2));
  and and_3 (out_3, counter_300ms_1_out_2, add8bit_3_c_out);
endmodule

module Counter_9bit (
  input  in_1,
  input  in_2,
  input  in_3,
  input  [8:0] in_4,
  output [8:0] out_5,
  output [8:0] out_6
);

  wire [8:0] add9bit_1_out_5, multiplexer_9bit_1_out_5;

  add9bit add9bit_1 (.in_1(1'b0), .in_2(1'b0), .in_3(out_5), .in_4(9'h1), .out_5(add9bit_1_out_5));  // open: out_6
  Multiplexer_9bit multiplexer_9bit_1 (
    .in_1({in_3, in_2}), .in_2(add9bit_1_out_5), .in_3({9{1'b0}}), .in_4(in_4),
    .out_5(multiplexer_9bit_1_out_5));
  D_Flip_Flop d_ff_1 (.D(multiplexer_9bit_1_out_5[0]), .clk(in_1), .Q(out_5[0]), .Qn(out_6[0]));  // open: preset, reset
  D_Flip_Flop d_ff_2 (.D(multiplexer_9bit_1_out_5[1]), .clk(in_1), .Q(out_5[1]), .Qn(out_6[1]));  // open: preset, reset
  D_Flip_Flop d_ff_3 (.D(multiplexer_9bit_1_out_5[2]), .clk(in_1), .Q(out_5[2]), .Qn(out_6[2]));  // open: preset, reset
  D_Flip_Flop d_ff_4 (.D(multiplexer_9bit_1_out_5[3]), .clk(in_1), .Q(out_5[3]), .Qn(out_6[3]));  // open: preset, reset
  D_Flip_Flop d_ff_5 (.D(multiplexer_9bit_1_out_5[4]), .clk(in_1), .Q(out_5[4]), .Qn(out_6[4]));  // open: preset, reset
  D_Flip_Flop d_ff_6 (.D(multiplexer_9bit_1_out_5[5]), .clk(in_1), .Q(out_5[5]), .Qn(out_6[5]));  // open: preset, reset
  D_Flip_Flop d_ff_7 (.D(multiplexer_9bit_1_out_5[6]), .clk(in_1), .Q(out_5[6]), .Qn(out_6[6]));  // open: preset, reset
  D_Flip_Flop d_ff_8 (.D(multiplexer_9bit_1_out_5[7]), .clk(in_1), .Q(out_5[7]), .Qn(out_6[7]));  // open: preset, reset
  D_Flip_Flop d_ff_9 (.D(multiplexer_9bit_1_out_5[8]), .clk(in_1), .Q(out_5[8]), .Qn(out_6[8]));  // open: preset, reset
endmodule

module add9bit (
  input  in_1,
  input  in_2,
  input  [8:0] in_3,
  input  [8:0] in_4,
  output [8:0] out_5,
  output out_6
);

  wire add1bit_1_c_out, add1bit_2_c_out, add1bit_3_c_out, add1bit_4_c_out, add1bit_5_c_out, add1bit_6_c_out,
       add1bit_7_c_out, add1bit_8_c_out;

  add1bit add1bit_1 (.MINUS(in_1), .C_IN(in_2), .A(in_3[0]), .B(in_4[0]), .S(out_5[0]), .C_OUT(add1bit_1_c_out));
  add1bit add1bit_2 (
    .MINUS(in_1), .C_IN(add1bit_1_c_out), .A(in_3[1]), .B(in_4[1]), .S(out_5[1]), .C_OUT(add1bit_2_c_out));
  add1bit add1bit_3 (
    .MINUS(in_1), .C_IN(add1bit_2_c_out), .A(in_3[2]), .B(in_4[2]), .S(out_5[2]), .C_OUT(add1bit_3_c_out));
  add1bit add1bit_4 (
    .MINUS(in_1), .C_IN(add1bit_3_c_out), .A(in_3[3]), .B(in_4[3]), .S(out_5[3]), .C_OUT(add1bit_4_c_out));
  add1bit add1bit_5 (
    .MINUS(in_1), .C_IN(add1bit_4_c_out), .A(in_3[4]), .B(in_4[4]), .S(out_5[4]), .C_OUT(add1bit_5_c_out));
  add1bit add1bit_6 (
    .MINUS(in_1), .C_IN(add1bit_5_c_out), .A(in_3[5]), .B(in_4[5]), .S(out_5[5]), .C_OUT(add1bit_6_c_out));
  add1bit add1bit_7 (
    .MINUS(in_1), .C_IN(add1bit_6_c_out), .A(in_3[6]), .B(in_4[6]), .S(out_5[6]), .C_OUT(add1bit_7_c_out));
  add1bit add1bit_8 (
    .MINUS(add1bit_7_c_out), .C_IN(in_1), .A(in_3[7]), .B(in_4[7]), .S(out_5[7]), .C_OUT(add1bit_8_c_out));
  add1bit add1bit_9 (.MINUS(in_1), .C_IN(add1bit_8_c_out), .A(in_3[8]), .B(in_4[8]), .S(out_5[8]), .C_OUT(out_6));
endmodule

module Multiplexer_9bit (
  input  [1:0] in_1,
  input  [8:0] in_2,
  input  [8:0] in_3,
  input  [8:0] in_4,
  output [8:0] out_5
);

  Multiplexer_1bit multiplexer_1bit_1 (
    .I_0(in_2[0]), .I_1(in_3[0]), .I_2(in_4[0]), .Umschalter(in_1), .Ausgang(out_5[0]));
  Multiplexer_1bit multiplexer_1bit_2 (
    .I_0(in_2[1]), .I_1(in_3[1]), .I_2(in_4[1]), .Umschalter(in_1), .Ausgang(out_5[1]));
  Multiplexer_1bit multiplexer_1bit_3 (
    .I_0(in_2[2]), .I_1(in_3[2]), .I_2(in_4[2]), .Umschalter(in_1), .Ausgang(out_5[2]));
  Multiplexer_1bit multiplexer_1bit_4 (
    .I_0(in_2[3]), .I_1(in_3[3]), .I_2(in_4[3]), .Umschalter(in_1), .Ausgang(out_5[3]));
  Multiplexer_1bit multiplexer_1bit_5 (
    .I_0(in_2[4]), .I_1(in_3[4]), .I_2(in_4[4]), .Umschalter(in_1), .Ausgang(out_5[4]));
  Multiplexer_1bit multiplexer_1bit_6 (
    .I_0(in_2[5]), .I_1(in_3[5]), .I_2(in_4[5]), .Umschalter(in_1), .Ausgang(out_5[5]));
  Multiplexer_1bit multiplexer_1bit_7 (
    .I_0(in_2[6]), .I_1(in_3[6]), .I_2(in_4[6]), .Umschalter(in_1), .Ausgang(out_5[6]));
  Multiplexer_1bit multiplexer_1bit_8 (
    .I_0(in_2[7]), .I_1(in_3[7]), .I_2(in_4[7]), .Umschalter(in_1), .Ausgang(out_5[7]));
  Multiplexer_1bit multiplexer_1bit_9 (
    .I_0(in_2[8]), .I_1(in_3[8]), .I_2(in_4[8]), .Umschalter(in_1), .Ausgang(out_5[8]));
endmodule

module Counter_300ms (
  input  in_1,
  output out_2
);

  wire [8:0] counter_9bit_1_out_5, counter_9bit_1_out_6;

  Counter_9bit counter_9bit_1 (
    .in_1(in_1), .in_2(out_2), .in_3(1'b0), .in_4({9{1'b0}}), .out_5(counter_9bit_1_out_5),
    .out_6(counter_9bit_1_out_6));
  and and_1 (out_2, counter_9bit_1_out_5[8], counter_9bit_1_out_6[7], counter_9bit_1_out_6[6], counter_9bit_1_out_5[5], counter_9bit_1_out_6[4], counter_9bit_1_out_5[3], counter_9bit_1_out_5[2], counter_9bit_1_out_6[1], counter_9bit_1_out_6[0]);
endmodule

module Schieberegister_DCF77Data_59bit (
  input  Clock,
  input  Data_In,
  output [8:0] Data_Jahr,
  output [4:0] Data_Monat,
  output [2:0] Data_Wochentag,
  output [5:0] Data_Tag,
  output [6:0] Data_Stunden,
  output [7:0] Data_Minute,
  output [5:0] Data_Zeitsystem,
  output [13:0] Data_Wetter,
  output Bit_SekundeAnfang
);

  wire d_ff_1_q, d_ff_2_q, d_ff_3_q, d_ff_4_q, d_ff_5_q, d_ff_6_q, d_ff_7_q, d_ff_8_q, d_ff_9_q, d_ff_10_q,
       d_ff_11_q, d_ff_12_q, d_ff_13_q, d_ff_14_q, d_ff_15_q, d_ff_16_q, d_ff_17_q, d_ff_18_q, d_ff_19_q,
       d_ff_20_q, d_ff_21_q, d_ff_22_q, d_ff_23_q, d_ff_24_q, d_ff_25_q, d_ff_26_q, d_ff_27_q, d_ff_28_q,
       d_ff_29_q, d_ff_30_q, d_ff_31_q, d_ff_32_q, d_ff_33_q, d_ff_34_q, d_ff_35_q, d_ff_36_q, d_ff_37_q,
       d_ff_38_q, d_ff_39_q, d_ff_40_q, d_ff_41_q, d_ff_42_q, d_ff_43_q, d_ff_44_q, d_ff_45_q, d_ff_46_q,
       d_ff_47_q, d_ff_48_q, d_ff_49_q, d_ff_50_q, d_ff_51_q, d_ff_52_q, d_ff_53_q, d_ff_54_q, d_ff_55_q,
       d_ff_56_q, d_ff_57_q, d_ff_58_q, d_ff_59_q;

  D_Flip_Flop d_ff_1 (.D(Data_In), .clk(Clock), .Q(d_ff_1_q));  // open: Qn, preset, reset
  D_Flip_Flop d_ff_2 (.D(d_ff_1_q), .clk(Clock), .Q(d_ff_2_q));  // open: Qn, preset, reset
  D_Flip_Flop d_ff_3 (.D(d_ff_2_q), .clk(Clock), .Q(d_ff_3_q));  // open: Qn, preset, reset
  D_Flip_Flop d_ff_4 (.D(d_ff_3_q), .clk(Clock), .Q(d_ff_4_q));  // open: Qn, preset, reset
  D_Flip_Flop d_ff_5 (.D(d_ff_4_q), .clk(Clock), .Q(d_ff_5_q));  // open: Qn, preset, reset
  D_Flip_Flop d_ff_6 (.D(d_ff_5_q), .clk(Clock), .Q(d_ff_6_q));  // open: Qn, preset, reset
  D_Flip_Flop d_ff_7 (.D(d_ff_6_q), .clk(Clock), .Q(d_ff_7_q));  // open: Qn, preset, reset
  D_Flip_Flop d_ff_8 (.D(d_ff_7_q), .clk(Clock), .Q(d_ff_8_q));  // open: Qn, preset, reset
  D_Flip_Flop d_ff_9 (.D(d_ff_8_q), .clk(Clock), .Q(d_ff_9_q));  // open: Qn, preset, reset
  D_Flip_Flop d_ff_10 (.D(d_ff_9_q), .clk(Clock), .Q(d_ff_10_q));  // open: Qn, preset, reset
  D_Flip_Flop d_ff_11 (.D(d_ff_10_q), .clk(Clock), .Q(d_ff_11_q));  // open: Qn, preset, reset
  D_Flip_Flop d_ff_12 (.D(d_ff_11_q), .clk(Clock), .Q(d_ff_12_q));  // open: Qn, preset, reset
  D_Flip_Flop d_ff_13 (.D(d_ff_12_q), .clk(Clock), .Q(d_ff_13_q));  // open: Qn, preset, reset
  D_Flip_Flop d_ff_14 (.D(d_ff_13_q), .clk(Clock), .Q(d_ff_14_q));  // open: Qn, preset, reset
  D_Flip_Flop d_ff_15 (.D(d_ff_14_q), .clk(Clock), .Q(d_ff_15_q));  // open: Qn, preset, reset
  D_Flip_Flop d_ff_16 (.D(d_ff_15_q), .clk(Clock), .Q(d_ff_16_q));  // open: Qn, preset, reset
  D_Flip_Flop d_ff_17 (.D(d_ff_16_q), .clk(Clock), .Q(d_ff_17_q));  // open: Qn, preset, reset
  D_Flip_Flop d_ff_18 (.D(d_ff_17_q), .clk(Clock), .Q(d_ff_18_q));  // open: Qn, preset, reset
  D_Flip_Flop d_ff_19 (.D(d_ff_18_q), .clk(Clock), .Q(d_ff_19_q));  // open: Qn, preset, reset
  D_Flip_Flop d_ff_20 (.D(d_ff_19_q), .clk(Clock), .Q(d_ff_20_q));  // open: Qn, preset, reset
  D_Flip_Flop d_ff_21 (.D(d_ff_20_q), .clk(Clock), .Q(d_ff_21_q));  // open: Qn, preset, reset
  D_Flip_Flop d_ff_22 (.D(d_ff_21_q), .clk(Clock), .Q(d_ff_22_q));  // open: Qn, preset, reset
  D_Flip_Flop d_ff_23 (.D(d_ff_22_q), .clk(Clock), .Q(d_ff_23_q));  // open: Qn, preset, reset
  D_Flip_Flop d_ff_24 (.D(d_ff_23_q), .clk(Clock), .Q(d_ff_24_q));  // open: Qn, preset, reset
  D_Flip_Flop d_ff_25 (.D(d_ff_24_q), .clk(Clock), .Q(d_ff_25_q));  // open: Qn, preset, reset
  D_Flip_Flop d_ff_26 (.D(d_ff_25_q), .clk(Clock), .Q(d_ff_26_q));  // open: Qn, preset, reset
  D_Flip_Flop d_ff_27 (.D(d_ff_26_q), .clk(Clock), .Q(d_ff_27_q));  // open: Qn, preset, reset
  D_Flip_Flop d_ff_28 (.D(d_ff_27_q), .clk(Clock), .Q(d_ff_28_q));  // open: Qn, preset, reset
  D_Flip_Flop d_ff_29 (.D(d_ff_28_q), .clk(Clock), .Q(d_ff_29_q));  // open: Qn, preset, reset
  D_Flip_Flop d_ff_30 (.D(d_ff_29_q), .clk(Clock), .Q(d_ff_30_q));  // open: Qn, preset, reset
  D_Flip_Flop d_ff_31 (.D(d_ff_30_q), .clk(Clock), .Q(d_ff_31_q));  // open: Qn, preset, reset
  D_Flip_Flop d_ff_32 (.D(d_ff_31_q), .clk(Clock), .Q(d_ff_32_q));  // open: Qn, preset, reset
  D_Flip_Flop d_ff_33 (.D(d_ff_32_q), .clk(Clock), .Q(d_ff_33_q));  // open: Qn, preset, reset
  D_Flip_Flop d_ff_34 (.D(d_ff_33_q), .clk(Clock), .Q(d_ff_34_q));  // open: Qn, preset, reset
  D_Flip_Flop d_ff_35 (.D(d_ff_34_q), .clk(Clock), .Q(d_ff_35_q));  // open: Qn, preset, reset
  D_Flip_Flop d_ff_36 (.D(d_ff_35_q), .clk(Clock), .Q(d_ff_36_q));  // open: Qn, preset, reset
  D_Flip_Flop d_ff_37 (.D(d_ff_36_q), .clk(Clock), .Q(d_ff_37_q));  // open: Qn, preset, reset
  D_Flip_Flop d_ff_38 (.D(d_ff_37_q), .clk(Clock), .Q(d_ff_38_q));  // open: Qn, preset, reset
  D_Flip_Flop d_ff_39 (.D(d_ff_38_q), .clk(Clock), .Q(d_ff_39_q));  // open: Qn, preset, reset
  D_Flip_Flop d_ff_40 (.D(d_ff_39_q), .clk(Clock), .Q(d_ff_40_q));  // open: Qn, preset, reset
  D_Flip_Flop d_ff_41 (.D(d_ff_40_q), .clk(Clock), .Q(d_ff_41_q));  // open: Qn, preset, reset
  D_Flip_Flop d_ff_42 (.D(d_ff_41_q), .clk(Clock), .Q(d_ff_42_q));  // open: Qn, preset, reset
  D_Flip_Flop d_ff_43 (.D(d_ff_42_q), .clk(Clock), .Q(d_ff_43_q));  // open: Qn, preset, reset
  D_Flip_Flop d_ff_44 (.D(d_ff_43_q), .clk(Clock), .Q(d_ff_44_q));  // open: Qn, preset, reset
  D_Flip_Flop d_ff_45 (.D(d_ff_44_q), .clk(Clock), .Q(d_ff_45_q));  // open: Qn, preset, reset
  D_Flip_Flop d_ff_46 (.D(d_ff_45_q), .clk(Clock), .Q(d_ff_46_q));  // open: Qn, preset, reset
  D_Flip_Flop d_ff_47 (.D(d_ff_46_q), .clk(Clock), .Q(d_ff_47_q));  // open: Qn, preset, reset
  D_Flip_Flop d_ff_48 (.D(d_ff_47_q), .clk(Clock), .Q(d_ff_48_q));  // open: Qn, preset, reset
  D_Flip_Flop d_ff_49 (.D(d_ff_48_q), .clk(Clock), .Q(d_ff_49_q));  // open: Qn, preset, reset
  D_Flip_Flop d_ff_50 (.D(d_ff_49_q), .clk(Clock), .Q(d_ff_50_q));  // open: Qn, preset, reset
  D_Flip_Flop d_ff_51 (.D(d_ff_50_q), .clk(Clock), .Q(d_ff_51_q));  // open: Qn, preset, reset
  D_Flip_Flop d_ff_52 (.D(d_ff_51_q), .clk(Clock), .Q(d_ff_52_q));  // open: Qn, preset, reset
  D_Flip_Flop d_ff_53 (.D(d_ff_52_q), .clk(Clock), .Q(d_ff_53_q));  // open: Qn, preset, reset
  D_Flip_Flop d_ff_54 (.D(d_ff_53_q), .clk(Clock), .Q(d_ff_54_q));  // open: Qn, preset, reset
  D_Flip_Flop d_ff_55 (.D(d_ff_54_q), .clk(Clock), .Q(d_ff_55_q));  // open: Qn, preset, reset
  D_Flip_Flop d_ff_56 (.D(d_ff_55_q), .clk(Clock), .Q(d_ff_56_q));  // open: Qn, preset, reset
  D_Flip_Flop d_ff_57 (.D(d_ff_56_q), .clk(Clock), .Q(d_ff_57_q));  // open: Qn, preset, reset
  D_Flip_Flop d_ff_58 (.D(d_ff_57_q), .clk(Clock), .Q(d_ff_58_q));  // open: Qn, preset, reset
  D_Flip_Flop d_ff_59 (.D(d_ff_58_q), .clk(Clock), .Q(d_ff_59_q));  // open: Qn, preset, reset
endmodule
