// Logisim project Funkuhr_testing.circ as structural Verilog: 78 circuits, main circuit Test_Funkuhr
module Funkuhr_Main (
  input  Takt2kHz,
  input  Antenne,
  output [5:0] Sekunden,
  output [5:0] Minuten,
  output [4:0] Stunden,
  output [4:0] Tag,
  output [3:0] Monat,
  output [6:0] Jahr
);

  wire and_1_out, Counter_Second_0_ausgang_sekunde, DCF77Data_Pruefen_0_data_fehler,
       Decode_DCF77_Signal_0_bit_data, Decode_DCF77_Signal_0_bit_sekunde_erkannt, or_1_out,
       Parity_Check_0_data_fehler, Schieberegister_DCF77Data_59bit_0_bit_minuteanfang,
       Schieberegister_DCF77Data_59bit_0_parity3, Synchroerkenner_0_sync;
  wire [2:0] Schieberegister_DCF77Data_59bit_0_data_wochentag;
  wire [4:0] Decode_DCF77Data_0_data_monat_out, Schieberegister_DCF77Data_59bit_0_data_monat;
  wire [4:4] Storage_Time_Data_0_data_monat_out;
  wire [5:0] Decode_DCF77Data_0_data_stunde_out, Decode_DCF77Data_0_data_tag_out,
       Schieberegister_DCF77Data_59bit_0_data_stunden_2, Schieberegister_DCF77Data_59bit_0_data_tag;
  wire [5:5] Storage_Time_Data_0_data_tag_out;
  wire [6:0] Decode_DCF77Data_0_data_minute_out, Schieberegister_DCF77Data_59bit_0_data_minute_2;
  wire [6:6] Schieberegister_DCF77Data_59bit_0_data_stunden;
  wire [7:0] Decode_DCF77Data_0_data_jahr_out, Schieberegister_DCF77Data_59bit_0_data_jahr;
  wire [7:7] Schieberegister_DCF77Data_59bit_0_data_minute, Storage_Time_Data_0_data_jahr_out;

  Decode_DCF77_Signal Decode_DCF77_Signal_0 (
    .Clock_2kHz(Takt2kHz), .Data_Seriell(Antenne),
    .Bit_Sekunde_erkannt(Decode_DCF77_Signal_0_bit_sekunde_erkannt), .Bit_Data(Decode_DCF77_Signal_0_bit_data));
  Schieberegister_DCF77Data_59bit Schieberegister_DCF77Data_59bit_0 (
    .Clock(Takt2kHz), .Data_In(Decode_DCF77_Signal_0_bit_data),
    .Enable(Decode_DCF77_Signal_0_bit_sekunde_erkannt),
    .Bit_MinuteAnfang(Schieberegister_DCF77Data_59bit_0_bit_minuteanfang),
    .Data_Minute({Schieberegister_DCF77Data_59bit_0_data_minute[7], Schieberegister_DCF77Data_59bit_0_data_minute_2}),
    .Data_Stunden({Schieberegister_DCF77Data_59bit_0_data_stunden[6], Schieberegister_DCF77Data_59bit_0_data_stunden_2}),
    .Data_Tag(Schieberegister_DCF77Data_59bit_0_data_tag),
    .Data_Wochentag(Schieberegister_DCF77Data_59bit_0_data_wochentag),
    .Data_Monat(Schieberegister_DCF77Data_59bit_0_data_monat),
    .Data_Jahr(Schieberegister_DCF77Data_59bit_0_data_jahr),
    .Parity3(Schieberegister_DCF77Data_59bit_0_parity3));  // open: Data_Wetter, Data_Zeitsystem
  Counter_Second Counter_Second_0 (
    .Clock_2kHz(Takt2kHz), .Set(Decode_DCF77_Signal_0_bit_sekunde_erkannt), .Enable(1'b1),
    .Data_SetClock_13bit(13'h12c), .Ausgang_Sekunde(Counter_Second_0_ausgang_sekunde));
  Synchroerkenner Synchroerkenner_0 (
    .Clock(Takt2kHz), .sekunde_extern(Decode_DCF77_Signal_0_bit_sekunde_erkannt),
    .sekunde_intern(Counter_Second_0_ausgang_sekunde), .sync(Synchroerkenner_0_sync));  // open: offline
  Parity_Check Parity_Check_0 (
    .Data_Minute({Schieberegister_DCF77Data_59bit_0_data_minute[7], Schieberegister_DCF77Data_59bit_0_data_minute_2}),
    .Data_Stunde({Schieberegister_DCF77Data_59bit_0_data_stunden[6], Schieberegister_DCF77Data_59bit_0_data_stunden_2}),
    .Data_Tag(Schieberegister_DCF77Data_59bit_0_data_tag),
    .Data_Wochentag(Schieberegister_DCF77Data_59bit_0_data_wochentag),
    .Data_Monat(Schieberegister_DCF77Data_59bit_0_data_monat),
    .Data_Jahr(Schieberegister_DCF77Data_59bit_0_data_jahr),
    .Parity3(Schieberegister_DCF77Data_59bit_0_parity3), .Data_Fehler(Parity_Check_0_data_fehler));
  Decode_DCF77Data Decode_DCF77Data_0 (
    .Data_Minute_IN(Schieberegister_DCF77Data_59bit_0_data_minute_2),
    .Data_Stunde_IN(Schieberegister_DCF77Data_59bit_0_data_stunden_2),
    .Data_Tag_IN(Schieberegister_DCF77Data_59bit_0_data_tag),
    .Data_Monat_IN(Schieberegister_DCF77Data_59bit_0_data_monat),
    .Data_Jahr_IN(Schieberegister_DCF77Data_59bit_0_data_jahr),
    .Data_Minute_OUT(Decode_DCF77Data_0_data_minute_out),
    .Data_Stunde_OUT(Decode_DCF77Data_0_data_stunde_out), .Data_Tag_OUT(Decode_DCF77Data_0_data_tag_out),
    .Data_Monat_OUT(Decode_DCF77Data_0_data_monat_out), .Data_Jahr_OUT(Decode_DCF77Data_0_data_jahr_out));
  DCF77Data_Pruefen DCF77Data_Pruefen_0 (
    .Data_Minute_bin(Decode_DCF77Data_0_data_minute_out),
    .Data_Stunde_bin(Decode_DCF77Data_0_data_stunde_out), .Data_Tag_bin(Decode_DCF77Data_0_data_tag_out),
    .Data_Monat_bin(Decode_DCF77Data_0_data_monat_out), .Data_Jahr_bin(Decode_DCF77Data_0_data_jahr_out),
    .Data_Fehler(DCF77Data_Pruefen_0_data_fehler));
  or or_1 (or_1_out, Parity_Check_0_data_fehler, DCF77Data_Pruefen_0_data_fehler, Schieberegister_DCF77Data_59bit_0_bit_minuteanfang);
  and and_1 (and_1_out, ~or_1_out, Synchroerkenner_0_sync);  // AND_Gate
  Storage_Time_Data Storage_Time_Data_0 (
    .Clock(Takt2kHz), .Load(and_1_out), .Sekunde_IN(Counter_Second_0_ausgang_sekunde),
    .Data_Minute_IN(Decode_DCF77Data_0_data_minute_out[5:0]),
    .Data_Stunde_IN(Decode_DCF77Data_0_data_stunde_out[4:0]), .Data_Tag_IN(Decode_DCF77Data_0_data_tag_out),
    .Data_Wochentag_IN(Schieberegister_DCF77Data_59bit_0_data_wochentag),
    .Data_Monat_IN(Decode_DCF77Data_0_data_monat_out), .Data_Jahr_IN(Decode_DCF77Data_0_data_jahr_out),
    .Data_Sekunde_OUT(Sekunden), .Data_Minute_OUT(Minuten), .Data_Stunde_OUT(Stunden),
    .Data_Tag_OUT({Storage_Time_Data_0_data_tag_out[5], Tag}),
    .Data_Monat_OUT({Storage_Time_Data_0_data_monat_out[4], Monat}),
    .Data_Jahr_OUT({Storage_Time_Data_0_data_jahr_out[7], Jahr}));  // open: Data_Wochentag_OUT
endmodule

module Counter_Second (
  input  Clock_2kHz,
  input  Set,
  input  Enable,
  input  [12:0] Data_SetClock_13bit,
  output Ausgang_Sekunde
);

  wire and_1_out;
  wire [12:0] Counter_13bit_0_ausgang_counter, Counter_13bit_0_ausgang_counter_negiert;

  and and_1 (and_1_out, Ausgang_Sekunde, ~Set);  // AND_Gate
  Counter_13bit Counter_13bit_0 (
    .Clock(Clock_2kHz), .Reset(and_1_out), .Load(Set), .Enable(Enable),
    .Data_Load_13bit(Data_SetClock_13bit), .Ausgang_Counter(Counter_13bit_0_ausgang_counter),
    .Ausgang_Counter_Negiert(Counter_13bit_0_ausgang_counter_negiert));
  and and_2 (Ausgang_Sekunde, Counter_13bit_0_ausgang_counter[0], Counter_13bit_0_ausgang_counter[1], Counter_13bit_0_ausgang_counter[2], Counter_13bit_0_ausgang_counter[3], Counter_13bit_0_ausgang_counter[4], Counter_13bit_0_ausgang_counter[5], Counter_13bit_0_ausgang_counter[6], Counter_13bit_0_ausgang_counter[7], Counter_13bit_0_ausgang_counter[8], Counter_13bit_0_ausgang_counter[9], Counter_13bit_0_ausgang_counter_negiert[10], Counter_13bit_0_ausgang_counter_negiert[11], Counter_13bit_0_ausgang_counter_negiert[12]);
endmodule

module Multiplexer_13bit (
  input  [1:0] Umschalter,
  input  [12:0] Eingang_0,
  input  [12:0] Eingang_1,
  input  [12:0] Eingang_2,
  output [12:0] Ausgang_0
);

  Multiplexer_1bit Multiplexer_bit0 (
    .I_0(Eingang_0[0]), .I_1(Eingang_1[0]), .I_2(Eingang_2[0]), .Umschalter(Umschalter),
    .Ausgang(Ausgang_0[0]));
  Multiplexer_1bit Multiplexer_bit1 (
    .I_0(Eingang_0[1]), .I_1(Eingang_1[1]), .I_2(Eingang_2[1]), .Umschalter(Umschalter),
    .Ausgang(Ausgang_0[1]));
  Multiplexer_1bit Multiplexer_bit2 (
    .I_0(Eingang_0[2]), .I_1(Eingang_1[2]), .I_2(Eingang_2[2]), .Umschalter(Umschalter),
    .Ausgang(Ausgang_0[2]));
  Multiplexer_1bit Multiplexer_bit3 (
    .I_0(Eingang_0[3]), .I_1(Eingang_1[3]), .I_2(Eingang_2[3]), .Umschalter(Umschalter),
    .Ausgang(Ausgang_0[3]));
  Multiplexer_1bit Multiplexer_bit4 (
    .I_0(Eingang_0[4]), .I_1(Eingang_1[4]), .I_2(Eingang_2[4]), .Umschalter(Umschalter),
    .Ausgang(Ausgang_0[4]));
  Multiplexer_1bit Multiplexer_bit5 (
    .I_0(Eingang_0[5]), .I_1(Eingang_1[5]), .I_2(Eingang_2[5]), .Umschalter(Umschalter),
    .Ausgang(Ausgang_0[5]));
  Multiplexer_1bit Multiplexer_bit6 (
    .I_0(Eingang_0[6]), .I_1(Eingang_1[6]), .I_2(Eingang_2[6]), .Umschalter(Umschalter),
    .Ausgang(Ausgang_0[6]));
  Multiplexer_1bit Multiplexer_bit7 (
    .I_0(Eingang_0[7]), .I_1(Eingang_1[7]), .I_2(Eingang_2[7]), .Umschalter(Umschalter),
    .Ausgang(Ausgang_0[7]));
  Multiplexer_1bit Multiplexer_bit8 (
    .I_0(Eingang_0[8]), .I_1(Eingang_1[8]), .I_2(Eingang_2[8]), .Umschalter(Umschalter),
    .Ausgang(Ausgang_0[8]));
  Multiplexer_1bit Multiplexer_bit9 (
    .I_0(Eingang_0[9]), .I_1(Eingang_1[9]), .I_2(Eingang_2[9]), .Umschalter(Umschalter),
    .Ausgang(Ausgang_0[9]));
  Multiplexer_1bit Multiplexer_bit10 (
    .I_0(Eingang_0[10]), .I_1(Eingang_1[10]), .I_2(Eingang_2[10]), .Umschalter(Umschalter),
    .Ausgang(Ausgang_0[10]));
  Multiplexer_1bit Multiplexer_bit11 (
    .I_0(Eingang_0[11]), .I_1(Eingang_1[11]), .I_2(Eingang_2[11]), .Umschalter(Umschalter),
    .Ausgang(Ausgang_0[11]));
  Multiplexer_1bit Multiplexer_bit12 (
    .I_0(Eingang_0[12]), .I_1(Eingang_1[12]), .I_2(Eingang_2[12]), .Umschalter(Umschalter),
    .Ausgang(Ausgang_0[12]));
endmodule

module Multiplexer_1bit (
  input  I_0,
  input  I_1,
  input  I_2,
  input  [1:0] Umschalter,
  output Ausgang
);

  wire and_1_out, and_2_out, and_3_out;

  and and_1 (and_1_out, I_0, ~Umschalter[0], ~Umschalter[1]);  // AND_Gate
  and and_2 (and_2_out, I_1, Umschalter[0], ~Umschalter[1]);  // AND_Gate
  and and_3 (and_3_out, I_2, ~Umschalter[0], Umschalter[1]);  // AND_Gate
  or or_1 (Ausgang, and_1_out, and_2_out, and_3_out);
endmodule

module seg7 (
  input  A3,
  input  A2,
  input  A1,
  input  A0,
  output SEG_A,
  output SEG_B,
  output SEG_C,
  output SEG_D,
  output SEG_E,
  output SEG_F,
  output SEG_G
);

  wire nand_1_out, nand_2_out, nand_3_out, nand_4_out, nor_1_out, nor_2_out, nor_3_out, nor_4_out, nor_5_out,
       nor_6_out, nor_7_out, nor_8_out, nor_9_out, nor_10_out, nor_11_out, nor_12_out, nor_13_out,
       nor_14_out, nor_15_out, nor_16_out, nor_17_out, nor_18_out, nor_19_out, nor_20_out, nor_21_out,
       nor_22_out, nor_23_out, nor_24_out, nor_25_out, nor_26_out, nor_27_out, nor_28_out, nor_29_out,
       nor_31_out;

  nor nor_1 (nor_1_out, A0, A0);
  nor nor_2 (nor_2_out, A2, A2);
  nor nor_3 (nor_3_out, A0, A0);
  nor nor_4 (nor_4_out, A2, A2);
  nor nor_5 (nor_5_out, A1, A1);
  nor nor_6 (nor_6_out, A2, A2);
  nor nor_7 (nor_7_out, A1, A1);
  nor nor_8 (nor_8_out, A0, A0);
  nor nor_9 (nor_9_out, A2, A2);
  nor nor_10 (nor_10_out, A0, A0);
  nor nor_11 (nor_11_out, A1, A1);
  nor nor_12 (nor_12_out, A2, A2);
  nand nand_1 (nand_1_out, A0, A0);
  nand nand_2 (nand_2_out, A2, A2);
  nor nor_13 (nor_13_out, A1, A1);
  nor nor_14 (nor_14_out, A0, A0);
  nor nor_15 (nor_15_out, A1, A2, A3);
  nor nor_16 (nor_16_out, A0, A0);
  nor nor_17 (nor_17_out, A1, A1);
  nor nor_18 (nor_18_out, A2, A2);
  nor nor_19 (nor_19_out, nor_1_out, A1, A2, A3);
  nor nor_20 (nor_20_out, A3, A0, A1, nor_2_out);
  nand nand_3 (nand_3_out, A1, nand_1_out);
  nand nand_4 (nand_4_out, nand_1_out, nand_2_out);
  nor nor_21 (nor_21_out, A2, nor_13_out);
  nor nor_22 (nor_22_out, nor_13_out, nor_14_out);
  nor nor_23 (nor_23_out, nor_14_out, A2, A3);
  nor nor_24 (nor_24_out, nor_3_out, A1, A3, nor_4_out);
  nor nor_25 (nor_25_out, nor_5_out, nor_6_out, A0, A3);
  nor nor_26 (nor_26_out, nor_7_out, A0, A2, A3);
  nor nor_27 (nor_27_out, nor_8_out, A1, A2, A3);
  nor nor_28 (nor_28_out, nor_9_out, A0, A1, A3);
  nor nor_29 (nor_29_out, nor_10_out, nor_11_out, nor_12_out, A3);
  nand nand_5 (SEG_E, nand_3_out, nand_4_out);
  nor nor_30 (SEG_F, nor_21_out, nor_22_out, nor_23_out);
  nor nor_31 (nor_31_out, nor_16_out, nor_17_out, nor_18_out);
  nor nor_32 (SEG_A, nor_19_out, nor_20_out);
  nor nor_33 (SEG_B, nor_24_out, nor_25_out);
  nor nor_34 (SEG_C, nor_26_out, nor_26_out);
  nor nor_35 (SEG_D, nor_27_out, nor_28_out, nor_29_out);
  nor nor_36 (SEG_G, nor_15_out, nor_31_out);
endmodule

module add1bit (
  input  MINUS,
  input  C_IN,
  input  A,
  input  B,
  output S,
  output C_OUT
);

  wire and_1_out, and_2_out, and_3_out, xor_1_out, xor_2_out;

  xor xor_1 (xor_1_out, MINUS, A);
  xor xor_2 (xor_2_out, A, B);
  and and_1 (and_1_out, xor_1_out, B);
  and and_2 (and_2_out, C_IN, B);
  and and_3 (and_3_out, xor_1_out, C_IN);
  xor xor_3 (S, xor_2_out, C_IN);
  or or_1 (C_OUT, and_1_out, and_2_out, and_3_out);
endmodule

module sub1bit (
  input  C_IN,
  input  A,
  input  B,
  output S,
  output C_OUT
);

  wire and_1_out, and_2_out, and_3_out, nand_1_out, xor_1_out;

  nand nand_1 (nand_1_out, A, A);
  xor xor_1 (xor_1_out, A, B);
  xor xor_2 (S, xor_1_out, C_IN);
  and and_1 (and_1_out, nand_1_out, B);
  and and_2 (and_2_out, C_IN, B);
  and and_3 (and_3_out, nand_1_out, C_IN);
  or or_1 (C_OUT, and_1_out, and_2_out, and_3_out);
endmodule

module add13bit (
  input  MINUS,
  input  C_IN,
  input  [12:0] Eingang_0,
  input  [12:0] Eingang_1,
  output [12:0] Ausgangbus,
  output C_OUT
);

  wire add1bit_0_c_out, add1bit_1_c_out, add1bit_2_c_out, add1bit_3_c_out, add1bit_4_c_out, add1bit_5_c_out,
       add1bit_6_c_out, add1bit_7_c_out, add1bit_8_c_out, add1bit_9_c_out, add1bit_10_c_out, add1bit_11_c_out;

  add1bit add1bit_0 (
    .MINUS(MINUS), .C_IN(C_IN), .A(Eingang_0[0]), .B(Eingang_1[0]), .S(Ausgangbus[0]), .C_OUT(add1bit_0_c_out));
  add1bit add1bit_1 (
    .MINUS(MINUS), .C_IN(add1bit_0_c_out), .A(Eingang_0[1]), .B(Eingang_1[1]), .S(Ausgangbus[1]),
    .C_OUT(add1bit_1_c_out));
  add1bit add1bit_2 (
    .MINUS(MINUS), .C_IN(add1bit_1_c_out), .A(Eingang_0[2]), .B(Eingang_1[2]), .S(Ausgangbus[2]),
    .C_OUT(add1bit_2_c_out));
  add1bit add1bit_3 (
    .MINUS(MINUS), .C_IN(add1bit_2_c_out), .A(Eingang_0[3]), .B(Eingang_1[3]), .S(Ausgangbus[3]),
    .C_OUT(add1bit_3_c_out));
  add1bit add1bit_4 (
    .MINUS(MINUS), .C_IN(add1bit_3_c_out), .A(Eingang_0[4]), .B(Eingang_1[4]), .S(Ausgangbus[4]),
    .C_OUT(add1bit_4_c_out));
  add1bit add1bit_5 (
    .MINUS(MINUS), .C_IN(add1bit_4_c_out), .A(Eingang_0[5]), .B(Eingang_1[5]), .S(Ausgangbus[5]),
    .C_OUT(add1bit_5_c_out));
  add1bit add1bit_6 (
    .MINUS(MINUS), .C_IN(add1bit_5_c_out), .A(Eingang_0[6]), .B(Eingang_1[6]), .S(Ausgangbus[6]),
    .C_OUT(add1bit_6_c_out));
  add1bit add1bit_7 (
    .MINUS(MINUS), .C_IN(add1bit_6_c_out), .A(Eingang_0[7]), .B(Eingang_1[7]), .S(Ausgangbus[7]),
    .C_OUT(add1bit_7_c_out));
  add1bit add1bit_8 (
    .MINUS(MINUS), .C_IN(add1bit_7_c_out), .A(Eingang_0[8]), .B(Eingang_1[8]), .S(Ausgangbus[8]),
    .C_OUT(add1bit_8_c_out));
  add1bit add1bit_9 (
    .MINUS(MINUS), .C_IN(add1bit_8_c_out), .A(Eingang_0[9]), .B(Eingang_1[9]), .S(Ausgangbus[9]),
    .C_OUT(add1bit_9_c_out));
  add1bit add1bit_10 (
    .MINUS(MINUS), .C_IN(add1bit_9_c_out), .A(Eingang_0[10]), .B(Eingang_1[10]), .S(Ausgangbus[10]),
    .C_OUT(add1bit_10_c_out));
  add1bit add1bit_11 (
    .MINUS(MINUS), .C_IN(add1bit_10_c_out), .A(Eingang_0[11]), .B(Eingang_1[11]), .S(Ausgangbus[11]),
    .C_OUT(add1bit_11_c_out));
  add1bit add1bit_12 (
    .MINUS(MINUS), .C_IN(add1bit_11_c_out), .A(Eingang_0[12]), .B(Eingang_1[12]), .S(Ausgangbus[12]),
    .C_OUT(C_OUT));
endmodule

module sub8bit (
  input  C_IN,
  input  A0,
  input  B0,
  input  A1,
  input  B1,
  input  A2,
  input  B2,
  input  A3,
  input  B3,
  input  A4,
  input  B4,
  input  A5,
  input  B5,
  input  A6,
  input  B6,
  input  A7,
  input  B7,
  output S0,
  output S1,
  output S2,
  output S3,
  output S4,
  output S5,
  output S6,
  output S7,
  output C_OUT
);

  wire add1bit_3_c_out, add1bit_4_c_out, add1bit_5_c_out, add1bit_6_c_out, add1bit_7_c_out, add1bit_8_c_out,
       subb1_bit_0_c_out;

  sub1bit subb1_bit_0 (.C_IN(C_IN), .A(A0), .B(B0), .S(S0), .C_OUT(subb1_bit_0_c_out));
  add1bit add1bit_3 (.C_IN(subb1_bit_0_c_out), .A(A1), .B(B1), .S(S1), .C_OUT(add1bit_3_c_out));  // open: MINUS
  add1bit add1bit_8 (.C_IN(add1bit_3_c_out), .A(A2), .B(B2), .S(S2), .C_OUT(add1bit_8_c_out));  // open: MINUS
  add1bit add1bit_5 (.C_IN(add1bit_8_c_out), .A(A3), .B(B3), .S(S3), .C_OUT(add1bit_5_c_out));  // open: MINUS
  add1bit add1bit_4 (.C_IN(add1bit_5_c_out), .A(A4), .B(B4), .S(S4), .C_OUT(add1bit_4_c_out));  // open: MINUS
  add1bit add1bit_7 (.C_IN(add1bit_4_c_out), .A(A5), .B(B5), .S(S5), .C_OUT(add1bit_7_c_out));  // open: MINUS
  add1bit add1bit_6 (.C_IN(add1bit_7_c_out), .A(A6), .B(B6), .S(S6), .C_OUT(add1bit_6_c_out));  // open: MINUS
  add1bit add1bit_2 (.C_IN(add1bit_6_c_out), .A(A7), .B(B7), .S(S7), .C_OUT(C_OUT));  // open: MINUS
endmodule

module bcd_part (
  input  A0,
  input  A1,
  input  A2,
  input  A3,
  output S0,
  output S1,
  output S2,
  output S3
);

  wire and_1_out, and_2_out, and_3_out, and_4_out, and_5_out, and_6_out, and_7_out, not_1_out, not_2_out,
       not_3_out, not_4_out, or_1_out, or_2_out, or_3_out;

  not not_1 (not_1_out, A0);
  not not_2 (not_2_out, A1);
  not not_3 (not_3_out, A2);
  not not_4 (not_4_out, A3);
  and and_1 (and_1_out, A0, not_3_out, not_4_out);
  and and_2 (and_2_out, not_1_out, A3);
  and and_3 (and_3_out, not_1_out, A1, A2);
  or or_1 (or_1_out, A1, A3);
  or or_2 (or_2_out, A0, not_3_out);
  or or_3 (or_3_out, not_1_out, not_4_out);
  and and_4 (and_4_out, not_1_out, not_2_out, A2);
  and and_5 (and_5_out, A0, A3);
  and and_6 (and_6_out, A0, A2);
  and and_7 (and_7_out, A1, A2);
  or or_4 (S0, and_1_out, and_2_out, and_3_out);
  and and_8 (S1, or_1_out, or_2_out, or_3_out);
  or or_5 (S2, and_4_out, and_5_out);
  or or_6 (S3, and_6_out, and_7_out, A3);
endmodule

module bcd (
  input  A0,
  input  A1,
  input  A2,
  input  A3,
  input  A4,
  input  A5,
  input  A6,
  input  A7,
  input  A8,
  output U1,
  output U2,
  output U3,
  output U4,
  output D1,
  output D2,
  output D3,
  output D4,
  output C1,
  output C2,
  output C3
);

  wire bcd_part_1_s0, bcd_part_1_s1, bcd_part_1_s2, bcd_part_1_s3, bcd_part_2_s0, bcd_part_2_s1,
       bcd_part_2_s2, bcd_part_2_s3, bcd_part_3_s0, bcd_part_3_s1, bcd_part_3_s2, bcd_part_3_s3,
       bcd_part_4_s0, bcd_part_4_s1, bcd_part_4_s2, bcd_part_4_s3, bcd_part_5_s0, bcd_part_5_s1,
       bcd_part_5_s2, bcd_part_5_s3, bcd_part_6_s0, bcd_part_6_s1, bcd_part_6_s2, bcd_part_6_s3,
       bcd_part_7_s0, bcd_part_7_s1, bcd_part_7_s2, bcd_part_7_s3, bcd_part_8_s0, bcd_part_8_s1,
       bcd_part_8_s2;

  bcd_part bcd_part_2 (
    .A0(A6), .A1(A7), .A2(A8), .S0(bcd_part_2_s0), .S1(bcd_part_2_s1), .S2(bcd_part_2_s2), .S3(bcd_part_2_s3));  // open: A3
  bcd_part bcd_part_5 (
    .A0(A5), .A1(bcd_part_2_s0), .A2(bcd_part_2_s1), .A3(bcd_part_2_s2), .S0(bcd_part_5_s0),
    .S1(bcd_part_5_s1), .S2(bcd_part_5_s2), .S3(bcd_part_5_s3));
  bcd_part bcd_part_1 (
    .A0(A4), .A1(bcd_part_5_s0), .A2(bcd_part_5_s1), .A3(bcd_part_5_s2), .S0(bcd_part_1_s0),
    .S1(bcd_part_1_s1), .S2(bcd_part_1_s2), .S3(bcd_part_1_s3));
  bcd_part bcd_part_6 (
    .A0(bcd_part_1_s3), .A1(bcd_part_5_s3), .A2(bcd_part_2_s3), .S0(bcd_part_6_s0), .S1(bcd_part_6_s1),
    .S2(bcd_part_6_s2), .S3(bcd_part_6_s3));  // open: A3
  bcd_part bcd_part_8 (
    .A0(bcd_part_6_s3), .S0(bcd_part_8_s0), .S1(bcd_part_8_s1), .S2(bcd_part_8_s2));  // open: A1, A2, A3, S3
  bcd_part bcd_part_4 (
    .A0(bcd_part_3_s3), .A1(bcd_part_6_s0), .A2(bcd_part_6_s1), .A3(bcd_part_6_s2), .S0(bcd_part_4_s0),
    .S1(bcd_part_4_s1), .S2(bcd_part_4_s2), .S3(bcd_part_4_s3));
  bcd_part bcd_part_10 (
    .A0(bcd_part_4_s3), .A1(bcd_part_8_s0), .A2(bcd_part_8_s1), .A3(bcd_part_8_s2), .S0(C2), .S1(C3));  // open: S2, S3
  bcd_part bcd_part_11 (
    .A0(bcd_part_7_s3), .A1(bcd_part_4_s0), .A2(bcd_part_4_s1), .A3(bcd_part_4_s2), .S0(D2), .S1(D3),
    .S2(D4), .S3(C1));
  bcd_part bcd_part_3 (
    .A0(A3), .A1(bcd_part_1_s0), .A2(bcd_part_1_s1), .A3(bcd_part_1_s2), .S0(bcd_part_3_s0),
    .S1(bcd_part_3_s1), .S2(bcd_part_3_s2), .S3(bcd_part_3_s3));
  bcd_part bcd_part_7 (
    .A0(A2), .A1(bcd_part_3_s0), .A2(bcd_part_3_s1), .A3(bcd_part_3_s2), .S0(bcd_part_7_s0),
    .S1(bcd_part_7_s1), .S2(bcd_part_7_s2), .S3(bcd_part_7_s3));
  bcd_part bcd_part_12 (
    .A0(A1), .A1(bcd_part_7_s0), .A2(bcd_part_7_s1), .A3(bcd_part_7_s2), .S0(U2), .S1(U3), .S2(U4), .S3(D1));

  assign U1 = A0;
endmodule

module Counter_13bit (
  input  Clock,
  input  Reset,
  input  Load,
  input  Enable,
  input  [12:0] Data_Load_13bit,
  output [12:0] Ausgang_Counter,
  output [12:0] Ausgang_Counter_Negiert
);

  wire [12:0] add13bit_0_ausgangbus, Multiplexer_13bit_0_ausgang_0;

  add13bit add13bit_0 (
    .MINUS(1'b0), .C_IN(1'b0), .Eingang_0(Ausgang_Counter), .Eingang_1({{12{1'b0}}, Enable}),
    .Ausgangbus(add13bit_0_ausgangbus));  // open: C_OUT
  Multiplexer_13bit Multiplexer_13bit_0 (
    .Umschalter({Load, Reset}), .Eingang_0(add13bit_0_ausgangbus), .Eingang_1({13{1'b0}}),
    .Eingang_2(Data_Load_13bit), .Ausgang_0(Multiplexer_13bit_0_ausgang_0));
  D_Flip_Flop d_ff_1 (
    .D(Multiplexer_13bit_0_ausgang_0[0]), .clk(Clock), .Q(Ausgang_Counter[0]), .Qn(Ausgang_Counter_Negiert[0]));  // open: preset, reset
  D_Flip_Flop d_ff_2 (
    .D(Multiplexer_13bit_0_ausgang_0[1]), .clk(Clock), .Q(Ausgang_Counter[1]), .Qn(Ausgang_Counter_Negiert[1]));  // open: preset, reset
  D_Flip_Flop d_ff_3 (
    .D(Multiplexer_13bit_0_ausgang_0[2]), .clk(Clock), .Q(Ausgang_Counter[2]), .Qn(Ausgang_Counter_Negiert[2]));  // open: preset, reset
  D_Flip_Flop d_ff_4 (
    .D(Multiplexer_13bit_0_ausgang_0[3]), .clk(Clock), .Q(Ausgang_Counter[3]), .Qn(Ausgang_Counter_Negiert[3]));  // open: preset, reset
  D_Flip_Flop d_ff_5 (
    .D(Multiplexer_13bit_0_ausgang_0[4]), .clk(Clock), .Q(Ausgang_Counter[4]), .Qn(Ausgang_Counter_Negiert[4]));  // open: preset, reset
  D_Flip_Flop d_ff_6 (
    .D(Multiplexer_13bit_0_ausgang_0[5]), .clk(Clock), .Q(Ausgang_Counter[5]), .Qn(Ausgang_Counter_Negiert[5]));  // open: preset, reset
  D_Flip_Flop d_ff_7 (
    .D(Multiplexer_13bit_0_ausgang_0[6]), .clk(Clock), .Q(Ausgang_Counter[6]), .Qn(Ausgang_Counter_Negiert[6]));  // open: preset, reset
  D_Flip_Flop d_ff_8 (
    .D(Multiplexer_13bit_0_ausgang_0[7]), .clk(Clock), .Q(Ausgang_Counter[7]), .Qn(Ausgang_Counter_Negiert[7]));  // open: preset, reset
  D_Flip_Flop d_ff_9 (
    .D(Multiplexer_13bit_0_ausgang_0[8]), .clk(Clock), .Q(Ausgang_Counter[8]), .Qn(Ausgang_Counter_Negiert[8]));  // open: preset, reset
  D_Flip_Flop d_ff_10 (
    .D(Multiplexer_13bit_0_ausgang_0[9]), .clk(Clock), .Q(Ausgang_Counter[9]), .Qn(Ausgang_Counter_Negiert[9]));  // open: preset, reset
  D_Flip_Flop d_ff_11 (
    .D(Multiplexer_13bit_0_ausgang_0[10]), .clk(Clock), .Q(Ausgang_Counter[10]),
    .Qn(Ausgang_Counter_Negiert[10]));  // open: preset, reset
  D_Flip_Flop d_ff_12 (
    .D(Multiplexer_13bit_0_ausgang_0[11]), .clk(Clock), .Q(Ausgang_Counter[11]),
    .Qn(Ausgang_Counter_Negiert[11]));  // open: preset, reset
  D_Flip_Flop d_ff_13 (
    .D(Multiplexer_13bit_0_ausgang_0[12]), .clk(Clock), .Q(Ausgang_Counter[12]),
    .Qn(Ausgang_Counter_Negiert[12]));  // open: preset, reset
endmodule

module Schieberegister_10bit (
  input  Clock_Eingang,
  input  Enable_Eingang,
  input  Data_Seriell_Eingang,
  output [9:0] Data_Parallel_Ausgang
);

  wire Multiplexer_1bit_0_ausgang, Multiplexer_1bit_1_ausgang, Multiplexer_1bit_2_ausgang,
       Multiplexer_1bit_3_ausgang, Multiplexer_1bit_4_ausgang, Multiplexer_1bit_5_ausgang,
       Multiplexer_1bit_6_ausgang, Multiplexer_1bit_7_ausgang, Multiplexer_1bit_8_ausgang,
       Multiplexer_1bit_9_ausgang;

  Multiplexer_1bit Multiplexer_1bit_0 (
    .I_0(Data_Parallel_Ausgang[0]), .I_1(Data_Seriell_Eingang), .I_2(1'b0),
    .Umschalter({1'b0, Enable_Eingang}), .Ausgang(Multiplexer_1bit_0_ausgang));
  Multiplexer_1bit Multiplexer_1bit_1 (
    .I_0(Data_Parallel_Ausgang[1]), .I_1(Data_Parallel_Ausgang[0]), .I_2(1'b0),
    .Umschalter({1'b0, Enable_Eingang}), .Ausgang(Multiplexer_1bit_1_ausgang));
  Multiplexer_1bit Multiplexer_1bit_2 (
    .I_0(Data_Parallel_Ausgang[2]), .I_1(Data_Parallel_Ausgang[1]), .I_2(1'b0),
    .Umschalter({1'b0, Enable_Eingang}), .Ausgang(Multiplexer_1bit_2_ausgang));
  Multiplexer_1bit Multiplexer_1bit_3 (
    .I_0(Data_Parallel_Ausgang[3]), .I_1(Data_Parallel_Ausgang[2]), .I_2(1'b0),
    .Umschalter({1'b0, Enable_Eingang}), .Ausgang(Multiplexer_1bit_3_ausgang));
  Multiplexer_1bit Multiplexer_1bit_4 (
    .I_0(Data_Parallel_Ausgang[4]), .I_1(Data_Parallel_Ausgang[3]), .I_2(1'b0),
    .Umschalter({1'b0, Enable_Eingang}), .Ausgang(Multiplexer_1bit_4_ausgang));
  Multiplexer_1bit Multiplexer_1bit_5 (
    .I_0(Data_Parallel_Ausgang[5]), .I_1(Data_Parallel_Ausgang[4]), .I_2(1'b0),
    .Umschalter({1'b0, Enable_Eingang}), .Ausgang(Multiplexer_1bit_5_ausgang));
  Multiplexer_1bit Multiplexer_1bit_6 (
    .I_0(Data_Parallel_Ausgang[6]), .I_1(Data_Parallel_Ausgang[5]), .I_2(1'b0),
    .Umschalter({1'b0, Enable_Eingang}), .Ausgang(Multiplexer_1bit_6_ausgang));
  Multiplexer_1bit Multiplexer_1bit_7 (
    .I_0(Data_Parallel_Ausgang[7]), .I_1(Data_Parallel_Ausgang[6]), .I_2(1'b0),
    .Umschalter({1'b0, Enable_Eingang}), .Ausgang(Multiplexer_1bit_7_ausgang));
  Multiplexer_1bit Multiplexer_1bit_8 (
    .I_0(Data_Parallel_Ausgang[8]), .I_1(Data_Parallel_Ausgang[7]), .I_2(1'b0),
    .Umschalter({1'b0, Enable_Eingang}), .Ausgang(Multiplexer_1bit_8_ausgang));
  Multiplexer_1bit Multiplexer_1bit_9 (
    .I_0(Data_Parallel_Ausgang[9]), .I_1(Data_Parallel_Ausgang[8]), .I_2(1'b0),
    .Umschalter({1'b0, Enable_Eingang}), .Ausgang(Multiplexer_1bit_9_ausgang));
  D_Flip_Flop d_ff_1 (
    .D(Multiplexer_1bit_0_ausgang), .clk(Clock_Eingang), .Q(Data_Parallel_Ausgang[0]));  // open: Qn, preset, reset
  D_Flip_Flop d_ff_2 (
    .D(Multiplexer_1bit_1_ausgang), .clk(Clock_Eingang), .Q(Data_Parallel_Ausgang[1]));  // open: Qn, preset, reset
  D_Flip_Flop d_ff_3 (
    .D(Multiplexer_1bit_2_ausgang), .clk(Clock_Eingang), .Q(Data_Parallel_Ausgang[2]));  // open: Qn, preset, reset
  D_Flip_Flop d_ff_4 (
    .D(Multiplexer_1bit_3_ausgang), .clk(Clock_Eingang), .Q(Data_Parallel_Ausgang[3]));  // open: Qn, preset, reset
  D_Flip_Flop d_ff_5 (
    .D(Multiplexer_1bit_4_ausgang), .clk(Clock_Eingang), .Q(Data_Parallel_Ausgang[4]));  // open: Qn, preset, reset
  D_Flip_Flop d_ff_6 (
    .D(Multiplexer_1bit_5_ausgang), .clk(Clock_Eingang), .Q(Data_Parallel_Ausgang[5]));  // open: Qn, preset, reset
  D_Flip_Flop d_ff_7 (
    .D(Multiplexer_1bit_6_ausgang), .clk(Clock_Eingang), .Q(Data_Parallel_Ausgang[6]));  // open: Qn, preset, reset
  D_Flip_Flop d_ff_8 (
    .D(Multiplexer_1bit_7_ausgang), .clk(Clock_Eingang), .Q(Data_Parallel_Ausgang[7]));  // open: Qn, preset, reset
  D_Flip_Flop d_ff_9 (
    .D(Multiplexer_1bit_8_ausgang), .clk(Clock_Eingang), .Q(Data_Parallel_Ausgang[8]));  // open: Qn, preset, reset
  D_Flip_Flop d_ff_10 (
    .D(Multiplexer_1bit_9_ausgang), .clk(Clock_Eingang), .Q(Data_Parallel_Ausgang[9]));  // open: Qn, preset, reset
endmodule

module Schiebregister_100bit (
  input  Clock_Eingang,
  input  Data_Seriell_Eingang,
  input  Enable_Eingang,
  output [9:0] Data_Parallel_0x10bit_Ausgang,
  output [9:0] Data_Parallel_1x10bit_Ausgang,
  output [9:0] Data_Parallel_2x10bit_Ausgang,
  output [9:0] Data_Parallel_3x10bit_Ausgang,
  output [9:0] Data_Parallel_4x10bit_Ausgang,
  output [9:0] Data_Parallel_5x10bit_Ausgang,
  output [9:0] Data_Parallel_6x10bit_Ausgang,
  output [9:0] Data_Parallel_7x10bit_Ausgang,
  output [9:0] Data_Parallel_8x10bit_Ausgang,
  output [9:0] Data_Parallel_9x10bit_Ausgang
);

  Schieberegister_10bit Schieberegister_10bit_0 (
    .Clock_Eingang(Clock_Eingang), .Enable_Eingang(Enable_Eingang),
    .Data_Seriell_Eingang(Data_Seriell_Eingang), .Data_Parallel_Ausgang(Data_Parallel_0x10bit_Ausgang));
  Schieberegister_10bit Schieberegister_10bit_1 (
    .Clock_Eingang(Clock_Eingang), .Enable_Eingang(Enable_Eingang),
    .Data_Seriell_Eingang(Data_Parallel_0x10bit_Ausgang[9]),
    .Data_Parallel_Ausgang(Data_Parallel_1x10bit_Ausgang));
  Schieberegister_10bit Schieberegister_10bit_2 (
    .Clock_Eingang(Clock_Eingang), .Enable_Eingang(Enable_Eingang),
    .Data_Seriell_Eingang(Data_Parallel_1x10bit_Ausgang[9]),
    .Data_Parallel_Ausgang(Data_Parallel_2x10bit_Ausgang));
  Schieberegister_10bit Schieberegister_10bit_3 (
    .Clock_Eingang(Clock_Eingang), .Enable_Eingang(Enable_Eingang),
    .Data_Seriell_Eingang(Data_Parallel_2x10bit_Ausgang[9]),
    .Data_Parallel_Ausgang(Data_Parallel_3x10bit_Ausgang));
  Schieberegister_10bit Schieberegister_10bit_4 (
    .Clock_Eingang(Clock_Eingang), .Enable_Eingang(Enable_Eingang),
    .Data_Seriell_Eingang(Data_Parallel_3x10bit_Ausgang[9]),
    .Data_Parallel_Ausgang(Data_Parallel_4x10bit_Ausgang));
  Schieberegister_10bit Schieberegister_10bit_5 (
    .Clock_Eingang(Clock_Eingang), .Enable_Eingang(Enable_Eingang),
    .Data_Seriell_Eingang(Data_Parallel_4x10bit_Ausgang[9]),
    .Data_Parallel_Ausgang(Data_Parallel_5x10bit_Ausgang));
  Schieberegister_10bit Schieberegister_10bit_6 (
    .Clock_Eingang(Clock_Eingang), .Enable_Eingang(Enable_Eingang),
    .Data_Seriell_Eingang(Data_Parallel_5x10bit_Ausgang[9]),
    .Data_Parallel_Ausgang(Data_Parallel_6x10bit_Ausgang));
  Schieberegister_10bit Schieberegister_10bit_7 (
    .Clock_Eingang(Clock_Eingang), .Enable_Eingang(Enable_Eingang),
    .Data_Seriell_Eingang(Data_Parallel_6x10bit_Ausgang[9]),
    .Data_Parallel_Ausgang(Data_Parallel_7x10bit_Ausgang));
  Schieberegister_10bit Schieberegister_10bit_8 (
    .Clock_Eingang(Clock_Eingang), .Enable_Eingang(Enable_Eingang),
    .Data_Seriell_Eingang(Data_Parallel_7x10bit_Ausgang[9]),
    .Data_Parallel_Ausgang(Data_Parallel_8x10bit_Ausgang));
  Schieberegister_10bit Schieberegister_10bit_9 (
    .Clock_Eingang(Clock_Eingang), .Enable_Eingang(Enable_Eingang),
    .Data_Seriell_Eingang(Data_Parallel_8x10bit_Ausgang[9]),
    .Data_Parallel_Ausgang(Data_Parallel_9x10bit_Ausgang));
endmodule

module Addierer_Bitweise_10bit (
  input  [9:0] Data_10bit_Eingang,
  output [3:0] Data_4bit_Ausgang
);

  wire add1bit5_c_out, add1bit5_s, add1bit_0_c_out, add1bit_0_s, add1bit_1_c_out, add1bit_1_s,
       add1bit_2_c_out, add1bit_2_s, add1bit_3_c_out, add1bit_3_s, add2bit_0_c_out, add2bit_0_s0,
       add2bit_0_s1, add2bit_1_c_out, add2bit_1_s0, add2bit_1_s1, add3bit_0_s0, add3bit_0_s1, add3bit_0_s2,
       add3bit_0_s3;

  add1bit add1bit_0 (
    .MINUS(1'b0), .C_IN(1'b0), .A(Data_10bit_Eingang[0]), .B(Data_10bit_Eingang[1]), .S(add1bit_0_s),
    .C_OUT(add1bit_0_c_out));
  add1bit add1bit_1 (
    .MINUS(1'b0), .C_IN(1'b0), .A(Data_10bit_Eingang[2]), .B(Data_10bit_Eingang[3]), .S(add1bit_1_s),
    .C_OUT(add1bit_1_c_out));
  add1bit add1bit_2 (
    .MINUS(1'b0), .C_IN(1'b0), .A(Data_10bit_Eingang[4]), .B(Data_10bit_Eingang[5]), .S(add1bit_2_s),
    .C_OUT(add1bit_2_c_out));
  add1bit add1bit_3 (
    .MINUS(1'b0), .C_IN(1'b0), .A(Data_10bit_Eingang[6]), .B(Data_10bit_Eingang[7]), .S(add1bit_3_s),
    .C_OUT(add1bit_3_c_out));
  add1bit add1bit5 (
    .MINUS(1'b0), .C_IN(1'b0), .A(Data_10bit_Eingang[8]), .B(Data_10bit_Eingang[9]), .S(add1bit5_s),
    .C_OUT(add1bit5_c_out));
  add2bit add2bit_0 (
    .Minus(1'b0), .C_IN(1'b0), .A0(add1bit_0_s), .A1(add1bit_0_c_out), .B0(add1bit_1_s),
    .B1(add1bit_1_c_out), .S0(add2bit_0_s0), .S1(add2bit_0_s1), .C_OUT(add2bit_0_c_out));
  add2bit add2bit_1 (
    .Minus(1'b0), .C_IN(1'b0), .A0(add1bit_2_s), .A1(add1bit_2_c_out), .B0(add1bit_3_s),
    .B1(add1bit_3_c_out), .S0(add2bit_1_s0), .S1(add2bit_1_s1), .C_OUT(add2bit_1_c_out));
  add3bit add3bit_0 (
    .Minus(1'b0), .C_IN(1'b0), .A0(add2bit_0_s0), .A1(add2bit_0_s1), .A2(add2bit_0_c_out), .B0(add2bit_1_s0),
    .B1(add2bit_1_s1), .B2(add2bit_1_c_out), .S0(add3bit_0_s0), .S1(add3bit_0_s1), .S2(add3bit_0_s2),
    .S3(add3bit_0_s3));
  add4bit add4bit_0 (
    .Minus(1'b0), .C_IN(1'b0), .A0(add3bit_0_s0), .A1(add3bit_0_s1), .A2(add3bit_0_s2), .A3(add3bit_0_s3),
    .B0(add1bit5_s), .B1(add1bit5_c_out), .B2(1'b0), .B3(1'b0), .S0(Data_4bit_Ausgang[0]),
    .S1(Data_4bit_Ausgang[1]), .S3(Data_4bit_Ausgang[2]), .S4(Data_4bit_Ausgang[3]));  // open: C_OUT
endmodule

module add2bit (
  input  Minus,
  input  C_IN,
  input  A0,
  input  A1,
  input  B0,
  input  B1,
  output S0,
  output S1,
  output C_OUT
);

  wire add1bit_0_c_out;

  add1bit add1bit_0 (.MINUS(Minus), .C_IN(C_IN), .A(A0), .B(B0), .S(S0), .C_OUT(add1bit_0_c_out));
  add1bit add1bit_1 (.MINUS(Minus), .C_IN(add1bit_0_c_out), .A(A1), .B(B1), .S(S1), .C_OUT(C_OUT));
endmodule

module add3bit (
  input  Minus,
  input  C_IN,
  input  A0,
  input  A1,
  input  A2,
  input  B0,
  input  B1,
  input  B2,
  output S0,
  output S1,
  output S2,
  output S3
);

  wire add1bit_0_c_out, add1bit_1_c_out;

  add1bit add1bit_0 (.MINUS(Minus), .C_IN(C_IN), .A(A0), .B(B0), .S(S0), .C_OUT(add1bit_0_c_out));
  add1bit add1bit_1 (.MINUS(Minus), .C_IN(add1bit_0_c_out), .A(A1), .B(B1), .S(S1), .C_OUT(add1bit_1_c_out));
  add1bit add1bit_2 (.MINUS(Minus), .C_IN(add1bit_1_c_out), .A(A2), .B(B2), .S(S2), .C_OUT(S3));
endmodule

module add4bit (
  input  Minus,
  input  C_IN,
  input  A0,
  input  A1,
  input  A2,
  input  A3,
  input  B0,
  input  B1,
  input  B2,
  input  B3,
  output S0,
  output S1,
  output S3,
  output S4,
  output C_OUT
);

  wire add1bit_0_c_out, add1bit_1_c_out, add1bit_2_c_out;

  add1bit add1bit_0 (.MINUS(Minus), .C_IN(C_IN), .A(A0), .B(B0), .S(S0), .C_OUT(add1bit_0_c_out));
  add1bit add1bit_1 (.MINUS(Minus), .C_IN(add1bit_0_c_out), .A(A1), .B(B1), .S(S1), .C_OUT(add1bit_1_c_out));
  add1bit add1bit_2 (.MINUS(Minus), .C_IN(add1bit_1_c_out), .A(A2), .B(B2), .S(S3), .C_OUT(add1bit_2_c_out));
  add1bit add1bit_3 (.MINUS(Minus), .C_IN(add1bit_2_c_out), .A(A3), .B(B3), .S(S4), .C_OUT(C_OUT));
endmodule

module Addierer_Bitweise_100bit (
  input  [9:0] Data_10bit_Eingang_0,
  input  [9:0] Data_10bit_Eingang_1,
  input  [9:0] Data_10bit_Eingang_2,
  input  [9:0] Data_10bit_Eingang_3,
  input  [9:0] Data_10bit_Eingang_4,
  input  [9:0] Data_10bit_Eingang_5,
  input  [9:0] Data_10bit_Eingang_6,
  input  [9:0] Data_10bit_Eingang_7,
  input  [9:0] Data_10bit_Eingang_8,
  input  [9:0] Data_10bit_Eingang_9,
  output [7:0] Data_8bit_Ausgang
);

  wire add4bit_0_c_out, add4bit_0_s0, add4bit_0_s1, add4bit_0_s3, add4bit_0_s4, add4bit_1_c_out,
       add4bit_1_s0, add4bit_1_s1, add4bit_1_s3, add4bit_1_s4, add4bit_2_c_out, add4bit_2_s0, add4bit_2_s1,
       add4bit_2_s3, add4bit_2_s4, add4bit_3_c_out, add4bit_3_s0, add4bit_3_s1, add4bit_3_s3, add4bit_3_s4,
       add4bit_4_c_out, add4bit_4_s0, add4bit_4_s1, add4bit_4_s3, add4bit_4_s4, add5bit_0_c_out,
       add5bit_0_s0, add5bit_0_s1, add5bit_0_s2, add5bit_0_s3, add5bit_0_s4, add5bit_1_c_out, add5bit_1_s0,
       add5bit_1_s1, add5bit_1_s2, add5bit_1_s3, add5bit_1_s4, add6bit_0_c_out, add6bit_0_s0, add6bit_0_s1,
       add6bit_0_s2, add6bit_0_s3, add6bit_0_s4, add6bit_0_s5;
  wire [3:0] Addierer_Bitweise_10bit_0_data_4bit_ausgang, Addierer_Bitweise_10bit_1_data_4bit_ausgang,
       Addierer_Bitweise_10bit_2_data_4bit_ausgang, Addierer_Bitweise_10bit_3_data_4bit_ausgang,
       Addierer_Bitweise_10bit_4_data_4bit_ausgang, Addierer_Bitweise_10bit_5_data_4bit_ausgang,
       Addierer_Bitweise_10bit_6_data_4bit_ausgang, Addierer_Bitweise_10bit_7_data_4bit_ausgang,
       Addierer_Bitweise_10bit_8_data_4bit_ausgang, Addierer_Bitweise_10bit_9_data_4bit_ausgang;

  Addierer_Bitweise_10bit Addierer_Bitweise_10bit_0 (
    .Data_10bit_Eingang(Data_10bit_Eingang_0), .Data_4bit_Ausgang(Addierer_Bitweise_10bit_0_data_4bit_ausgang));
  Addierer_Bitweise_10bit Addierer_Bitweise_10bit_1 (
    .Data_10bit_Eingang(Data_10bit_Eingang_1), .Data_4bit_Ausgang(Addierer_Bitweise_10bit_1_data_4bit_ausgang));
  Addierer_Bitweise_10bit Addierer_Bitweise_10bit_2 (
    .Data_10bit_Eingang(Data_10bit_Eingang_2), .Data_4bit_Ausgang(Addierer_Bitweise_10bit_2_data_4bit_ausgang));
  Addierer_Bitweise_10bit Addierer_Bitweise_10bit_3 (
    .Data_10bit_Eingang(Data_10bit_Eingang_3), .Data_4bit_Ausgang(Addierer_Bitweise_10bit_3_data_4bit_ausgang));
  Addierer_Bitweise_10bit Addierer_Bitweise_10bit_4 (
    .Data_10bit_Eingang(Data_10bit_Eingang_4), .Data_4bit_Ausgang(Addierer_Bitweise_10bit_4_data_4bit_ausgang));
  Addierer_Bitweise_10bit Addierer_Bitweise_10bit_5 (
    .Data_10bit_Eingang(Data_10bit_Eingang_5), .Data_4bit_Ausgang(Addierer_Bitweise_10bit_5_data_4bit_ausgang));
  Addierer_Bitweise_10bit Addierer_Bitweise_10bit_6 (
    .Data_10bit_Eingang(Data_10bit_Eingang_6), .Data_4bit_Ausgang(Addierer_Bitweise_10bit_6_data_4bit_ausgang));
  Addierer_Bitweise_10bit Addierer_Bitweise_10bit_7 (
    .Data_10bit_Eingang(Data_10bit_Eingang_7), .Data_4bit_Ausgang(Addierer_Bitweise_10bit_7_data_4bit_ausgang));
  Addierer_Bitweise_10bit Addierer_Bitweise_10bit_8 (
    .Data_10bit_Eingang(Data_10bit_Eingang_8), .Data_4bit_Ausgang(Addierer_Bitweise_10bit_8_data_4bit_ausgang));
  Addierer_Bitweise_10bit Addierer_Bitweise_10bit_9 (
    .Data_10bit_Eingang(Data_10bit_Eingang_9), .Data_4bit_Ausgang(Addierer_Bitweise_10bit_9_data_4bit_ausgang));
  add4bit add4bit_0 (
    .Minus(1'b0), .C_IN(1'b0), .A0(Addierer_Bitweise_10bit_0_data_4bit_ausgang[0]),
    .A1(Addierer_Bitweise_10bit_0_data_4bit_ausgang[1]), .A2(Addierer_Bitweise_10bit_0_data_4bit_ausgang[2]),
    .A3(Addierer_Bitweise_10bit_0_data_4bit_ausgang[3]), .B0(Addierer_Bitweise_10bit_1_data_4bit_ausgang[0]),
    .B1(Addierer_Bitweise_10bit_1_data_4bit_ausgang[1]), .B2(Addierer_Bitweise_10bit_1_data_4bit_ausgang[2]),
    .B3(Addierer_Bitweise_10bit_1_data_4bit_ausgang[3]), .S0(add4bit_0_s0), .S1(add4bit_0_s1),
    .S3(add4bit_0_s3), .S4(add4bit_0_s4), .C_OUT(add4bit_0_c_out));
  add4bit add4bit_1 (
    .Minus(1'b0), .C_IN(1'b0), .A0(Addierer_Bitweise_10bit_2_data_4bit_ausgang[0]),
    .A1(Addierer_Bitweise_10bit_2_data_4bit_ausgang[1]), .A2(Addierer_Bitweise_10bit_2_data_4bit_ausgang[2]),
    .A3(Addierer_Bitweise_10bit_2_data_4bit_ausgang[3]), .B0(Addierer_Bitweise_10bit_3_data_4bit_ausgang[0]),
    .B1(Addierer_Bitweise_10bit_3_data_4bit_ausgang[1]), .B2(Addierer_Bitweise_10bit_3_data_4bit_ausgang[2]),
    .B3(Addierer_Bitweise_10bit_3_data_4bit_ausgang[3]), .S0(add4bit_1_s0), .S1(add4bit_1_s1),
    .S3(add4bit_1_s3), .S4(add4bit_1_s4), .C_OUT(add4bit_1_c_out));
  add4bit add4bit_2 (
    .Minus(1'b0), .C_IN(1'b0), .A0(Addierer_Bitweise_10bit_4_data_4bit_ausgang[0]),
    .A1(Addierer_Bitweise_10bit_4_data_4bit_ausgang[1]), .A2(Addierer_Bitweise_10bit_4_data_4bit_ausgang[2]),
    .A3(Addierer_Bitweise_10bit_4_data_4bit_ausgang[3]), .B0(Addierer_Bitweise_10bit_5_data_4bit_ausgang[0]),
    .B1(Addierer_Bitweise_10bit_5_data_4bit_ausgang[1]), .B2(Addierer_Bitweise_10bit_5_data_4bit_ausgang[2]),
    .B3(Addierer_Bitweise_10bit_5_data_4bit_ausgang[3]), .S0(add4bit_2_s0), .S1(add4bit_2_s1),
    .S3(add4bit_2_s3), .S4(add4bit_2_s4), .C_OUT(add4bit_2_c_out));
  add4bit add4bit_3 (
    .Minus(1'b0), .C_IN(1'b0), .A0(Addierer_Bitweise_10bit_6_data_4bit_ausgang[0]),
    .A1(Addierer_Bitweise_10bit_6_data_4bit_ausgang[1]), .A2(Addierer_Bitweise_10bit_6_data_4bit_ausgang[2]),
    .A3(Addierer_Bitweise_10bit_6_data_4bit_ausgang[3]), .B0(Addierer_Bitweise_10bit_7_data_4bit_ausgang[0]),
    .B1(Addierer_Bitweise_10bit_7_data_4bit_ausgang[1]), .B2(Addierer_Bitweise_10bit_7_data_4bit_ausgang[2]),
    .B3(Addierer_Bitweise_10bit_7_data_4bit_ausgang[3]), .S0(add4bit_3_s0), .S1(add4bit_3_s1),
    .S3(add4bit_3_s3), .S4(add4bit_3_s4), .C_OUT(add4bit_3_c_out));
  add4bit add4bit_4 (
    .Minus(1'b0), .C_IN(1'b0), .A0(Addierer_Bitweise_10bit_8_data_4bit_ausgang[0]),
    .A1(Addierer_Bitweise_10bit_8_data_4bit_ausgang[1]), .A2(Addierer_Bitweise_10bit_8_data_4bit_ausgang[2]),
    .A3(Addierer_Bitweise_10bit_8_data_4bit_ausgang[3]), .B0(Addierer_Bitweise_10bit_9_data_4bit_ausgang[0]),
    .B1(Addierer_Bitweise_10bit_9_data_4bit_ausgang[1]), .B2(Addierer_Bitweise_10bit_9_data_4bit_ausgang[2]),
    .B3(Addierer_Bitweise_10bit_9_data_4bit_ausgang[3]), .S0(add4bit_4_s0), .S1(add4bit_4_s1),
    .S3(add4bit_4_s3), .S4(add4bit_4_s4), .C_OUT(add4bit_4_c_out));
  add5bit add5bit_0 (
    .Minus(1'b0), .C_IN(1'b0), .A0(add4bit_0_s0), .A1(add4bit_0_s1), .A2(add4bit_0_s3), .A3(add4bit_0_s4),
    .A4(add4bit_0_c_out), .B0(add4bit_1_s0), .B1(add4bit_1_s1), .B2(add4bit_1_s3), .B3(add4bit_1_s4),
    .B4(add4bit_1_c_out), .S0(add5bit_0_s0), .S1(add5bit_0_s1), .S2(add5bit_0_s2), .S3(add5bit_0_s3),
    .S4(add5bit_0_s4), .C_OUT(add5bit_0_c_out));
  add5bit add5bit_1 (
    .Minus(1'b0), .C_IN(1'b0), .A0(add4bit_2_s0), .A1(add4bit_2_s1), .A2(add4bit_2_s3), .A3(add4bit_2_s4),
    .A4(add4bit_2_c_out), .B0(add4bit_3_s0), .B1(add4bit_3_s1), .B2(add4bit_3_s3), .B3(add4bit_3_s4),
    .B4(add4bit_3_c_out), .S0(add5bit_1_s0), .S1(add5bit_1_s1), .S2(add5bit_1_s2), .S3(add5bit_1_s3),
    .S4(add5bit_1_s4), .C_OUT(add5bit_1_c_out));
  add6bit add6bit_0 (
    .Minus(1'b0), .C_IN(1'b0), .A0(add5bit_0_s0), .A1(add5bit_0_s1), .A2(add5bit_0_s2), .A3(add5bit_0_s3),
    .A4(add5bit_0_s4), .A5(add5bit_0_c_out), .B0(add5bit_1_s0), .B1(add5bit_1_s1), .B2(add5bit_1_s2),
    .B3(add5bit_1_s3), .B4(add5bit_1_s4), .B5(add5bit_1_c_out), .S0(add6bit_0_s0), .S1(add6bit_0_s1),
    .S2(add6bit_0_s2), .S3(add6bit_0_s3), .S4(add6bit_0_s4), .S5(add6bit_0_s5), .C_OUT(add6bit_0_c_out));
  add7bit add7bit_0 (
    .Minus(1'b0), .C_IN(1'b0), .A0(add6bit_0_s0), .A1(add6bit_0_s1), .A2(add6bit_0_s2), .A3(add6bit_0_s3),
    .A4(add6bit_0_s4), .A5(add6bit_0_s5), .A6(add6bit_0_c_out), .B0(add4bit_4_s0), .B1(add4bit_4_s1),
    .B2(add4bit_4_s3), .B3(add4bit_4_s4), .B4(add4bit_4_c_out), .S0(Data_8bit_Ausgang[0]),
    .S1(Data_8bit_Ausgang[1]), .S2(Data_8bit_Ausgang[2]), .S3(Data_8bit_Ausgang[3]),
    .S4(Data_8bit_Ausgang[4]), .S5(Data_8bit_Ausgang[5]), .S6(Data_8bit_Ausgang[6]), .S7(Data_8bit_Ausgang[7]));  // open: B5, B7
endmodule

module add5bit (
  input  Minus,
  input  C_IN,
  input  A0,
  input  A1,
  input  A2,
  input  A3,
  input  A4,
  input  B0,
  input  B1,
  input  B2,
  input  B3,
  input  B4,
  output S0,
  output S1,
  output S2,
  output S3,
  output S4,
  output C_OUT
);

  wire add1bit_0_c_out, add1bit_1_c_out, add1bit_2_c_out, add1bit_3_c_out;

  add1bit add1bit_0 (.MINUS(Minus), .C_IN(C_IN), .A(A0), .B(B0), .S(S0), .C_OUT(add1bit_0_c_out));
  add1bit add1bit_1 (.MINUS(Minus), .C_IN(add1bit_0_c_out), .A(A1), .B(B1), .S(S1), .C_OUT(add1bit_1_c_out));
  add1bit add1bit_2 (.MINUS(Minus), .C_IN(add1bit_1_c_out), .A(A2), .B(B2), .S(S2), .C_OUT(add1bit_2_c_out));
  add1bit add1bit_3 (.MINUS(Minus), .C_IN(add1bit_2_c_out), .A(A3), .B(B3), .S(S3), .C_OUT(add1bit_3_c_out));
  add1bit add1bit_4 (.MINUS(Minus), .C_IN(add1bit_3_c_out), .A(A4), .B(B4), .S(S4), .C_OUT(C_OUT));
endmodule

module add6bit (
  input  Minus,
  input  C_IN,
  input  A0,
  input  A1,
  input  A2,
  input  A3,
  input  A4,
  input  A5,
  input  B0,
  input  B1,
  input  B2,
  input  B3,
  input  B4,
  input  B5,
  output S0,
  output S1,
  output S2,
  output S3,
  output S4,
  output S5,
  output C_OUT
);

  wire add1bit_0_c_out, add1bit_1_c_out, add1bit_2_c_out, add1bit_3_c_out, add1bit_4_c_out;

  add1bit add1bit_0 (.MINUS(Minus), .C_IN(C_IN), .A(A0), .B(B0), .S(S0), .C_OUT(add1bit_0_c_out));
  add1bit add1bit_1 (.MINUS(Minus), .C_IN(add1bit_0_c_out), .A(A1), .B(B1), .S(S1), .C_OUT(add1bit_1_c_out));
  add1bit add1bit_2 (.MINUS(Minus), .C_IN(add1bit_1_c_out), .A(A2), .B(B2), .S(S2), .C_OUT(add1bit_2_c_out));
  add1bit add1bit_3 (.MINUS(Minus), .C_IN(add1bit_2_c_out), .A(A3), .B(B3), .S(S3), .C_OUT(add1bit_3_c_out));
  add1bit add1bit_4 (.MINUS(Minus), .C_IN(add1bit_3_c_out), .A(A4), .B(B4), .S(S4), .C_OUT(add1bit_4_c_out));
  add1bit add1bit_5 (.MINUS(Minus), .C_IN(add1bit_4_c_out), .A(A5), .B(B5), .S(S5), .C_OUT(C_OUT));
endmodule

module add7bit (
  input  Minus,
  input  C_IN,
  input  A0,
  input  A1,
  input  A2,
  input  A3,
  input  A4,
  input  A5,
  input  A6,
  input  B0,
  input  B1,
  input  B2,
  input  B3,
  input  B4,
  input  B5,
  input  B7,
  output S0,
  output S1,
  output S2,
  output S3,
  output S4,
  output S5,
  output S6,
  output S7
);

  wire add1bit_0_c_out, add1bit_1_c_out, add1bit_2_c_out, add1bit_3_c_out, add1bit_4_c_out, add1bit_5_c_out;

  add1bit add1bit_0 (.MINUS(Minus), .C_IN(C_IN), .A(A0), .B(B0), .S(S0), .C_OUT(add1bit_0_c_out));
  add1bit add1bit_1 (.MINUS(Minus), .C_IN(add1bit_0_c_out), .A(A1), .B(B1), .S(S1), .C_OUT(add1bit_1_c_out));
  add1bit add1bit_2 (.MINUS(Minus), .C_IN(add1bit_1_c_out), .A(A2), .B(B2), .S(S2), .C_OUT(add1bit_2_c_out));
  add1bit add1bit_3 (.MINUS(Minus), .C_IN(add1bit_2_c_out), .A(A3), .B(B3), .S(S3), .C_OUT(add1bit_3_c_out));
  add1bit add1bit_4 (.MINUS(Minus), .C_IN(add1bit_3_c_out), .A(A4), .B(B4), .S(S4), .C_OUT(add1bit_4_c_out));
  add1bit add1bit_5 (.MINUS(Minus), .C_IN(add1bit_4_c_out), .A(A5), .B(B5), .S(S5), .C_OUT(add1bit_5_c_out));
  add1bit add1bit_6 (.MINUS(Minus), .C_IN(add1bit_5_c_out), .A(A6), .B(B7), .S(S6), .C_OUT(S7));
endmodule

module add8bit (
  input  Minus,
  input  C_IN,
  input  A0,
  input  A1,
  input  A2,
  input  A3,
  input  A4,
  input  A5,
  input  A6,
  input  A7,
  input  B0,
  input  B1,
  input  B2,
  input  B3,
  input  B4,
  input  B5,
  input  B6,
  input  B7,
  output S0,
  output S1,
  output S2,
  output S3,
  output S4,
  output S5,
  output S6,
  output S7,
  output C_OUT
);

  wire add1bit_0_c_out, add1bit_1_c_out, add1bit_2_c_out, add1bit_3_c_out, add1bit_4_c_out, add1bit_6_c_out,
       add1bit_7_c_out;

  add1bit add1bit_0 (.MINUS(Minus), .C_IN(C_IN), .A(A0), .B(B0), .S(S0), .C_OUT(add1bit_0_c_out));
  add1bit add1bit_1 (.MINUS(Minus), .C_IN(add1bit_0_c_out), .A(A1), .B(B1), .S(S1), .C_OUT(add1bit_1_c_out));
  add1bit add1bit_2 (.MINUS(Minus), .C_IN(add1bit_1_c_out), .A(A2), .B(B2), .S(S2), .C_OUT(add1bit_2_c_out));
  add1bit add1bit_3 (.MINUS(Minus), .C_IN(add1bit_2_c_out), .A(A3), .B(B3), .S(S3), .C_OUT(add1bit_3_c_out));
  add1bit add1bit_4 (.MINUS(Minus), .C_IN(add1bit_3_c_out), .A(A4), .B(B4), .S(S4), .C_OUT(add1bit_4_c_out));
  add1bit add1bit_6 (.MINUS(Minus), .C_IN(add1bit_4_c_out), .A(A5), .B(B5), .S(S5), .C_OUT(add1bit_6_c_out));
  add1bit add1bit_7 (.MINUS(Minus), .C_IN(add1bit_6_c_out), .A(A6), .B(B6), .S(S6), .C_OUT(add1bit_7_c_out));
  add1bit add1bit_8 (.MINUS(Minus), .C_IN(add1bit_7_c_out), .A(A7), .B(B7), .S(S7), .C_OUT(C_OUT));
endmodule

module Addierer_Bitweise_200bit (
  input  [9:0] Data_10bit_Eingang_0,
  input  [9:0] Data_10bit_Eingang_1,
  input  [9:0] Data_10bit_Eingang_2,
  input  [9:0] Data_10bit_Eingang_3,
  input  [9:0] Data_10bit_Eingang_4,
  input  [9:0] Data_10bit_Eingang_5,
  input  [9:0] Data_10bit_Eingang_6,
  input  [9:0] Data_10bit_Eingang_7,
  input  [9:0] Data_10bit_Eingang_8,
  input  [9:0] Data_10bit_Eingang_9,
  input  [9:0] Data_10bit_Eingang_10,
  input  [9:0] Data_10bit_Eingang_11,
  input  [9:0] Data_10bit_Eingang_12,
  input  [9:0] Data_10bit_Eingang_13,
  input  [9:0] Data_10bit_Eingang_14,
  input  [9:0] Data_10bit_Eingang_15,
  input  [9:0] Data_10bit_Eingang_16,
  input  [9:0] Data_10bit_Eingang_17,
  input  [9:0] Data_10bit_Eingang_18,
  input  [9:0] Data_10bit_Eingang_19,
  output [7:0] Data_8bit_Ausgang
);

  wire [7:0] Addierer_Bitweise_100bit_0_data_8bit_ausgang, Addierer_Bitweise_100bit_1_data_8bit_ausgang;

  Addierer_Bitweise_100bit Addierer_Bitweise_100bit_0 (
    .Data_10bit_Eingang_0(Data_10bit_Eingang_0), .Data_10bit_Eingang_1(Data_10bit_Eingang_1),
    .Data_10bit_Eingang_2(Data_10bit_Eingang_2), .Data_10bit_Eingang_3(Data_10bit_Eingang_3),
    .Data_10bit_Eingang_4(Data_10bit_Eingang_4), .Data_10bit_Eingang_5(Data_10bit_Eingang_5),
    .Data_10bit_Eingang_6(Data_10bit_Eingang_6), .Data_10bit_Eingang_7(Data_10bit_Eingang_7),
    .Data_10bit_Eingang_8(Data_10bit_Eingang_8), .Data_10bit_Eingang_9(Data_10bit_Eingang_9),
    .Data_8bit_Ausgang(Addierer_Bitweise_100bit_0_data_8bit_ausgang));
  Addierer_Bitweise_100bit Addierer_Bitweise_100bit_1 (
    .Data_10bit_Eingang_0(Data_10bit_Eingang_10), .Data_10bit_Eingang_1(Data_10bit_Eingang_11),
    .Data_10bit_Eingang_2(Data_10bit_Eingang_12), .Data_10bit_Eingang_3(Data_10bit_Eingang_13),
    .Data_10bit_Eingang_4(Data_10bit_Eingang_14), .Data_10bit_Eingang_5(Data_10bit_Eingang_15),
    .Data_10bit_Eingang_6(Data_10bit_Eingang_16), .Data_10bit_Eingang_7(Data_10bit_Eingang_17),
    .Data_10bit_Eingang_8(Data_10bit_Eingang_18), .Data_10bit_Eingang_9(Data_10bit_Eingang_19),
    .Data_8bit_Ausgang(Addierer_Bitweise_100bit_1_data_8bit_ausgang));
  add8bit add8bit_0 (
    .Minus(1'b0), .C_IN(1'b0), .A0(Addierer_Bitweise_100bit_0_data_8bit_ausgang[0]),
    .A1(Addierer_Bitweise_100bit_0_data_8bit_ausgang[1]),
    .A2(Addierer_Bitweise_100bit_0_data_8bit_ausgang[2]),
    .A3(Addierer_Bitweise_100bit_0_data_8bit_ausgang[3]),
    .A4(Addierer_Bitweise_100bit_0_data_8bit_ausgang[4]),
    .A5(Addierer_Bitweise_100bit_0_data_8bit_ausgang[5]),
    .A6(Addierer_Bitweise_100bit_0_data_8bit_ausgang[6]),
    .A7(Addierer_Bitweise_100bit_0_data_8bit_ausgang[7]),
    .B0(Addierer_Bitweise_100bit_1_data_8bit_ausgang[0]),
    .B1(Addierer_Bitweise_100bit_1_data_8bit_ausgang[1]),
    .B2(Addierer_Bitweise_100bit_1_data_8bit_ausgang[2]),
    .B3(Addierer_Bitweise_100bit_1_data_8bit_ausgang[3]),
    .B4(Addierer_Bitweise_100bit_1_data_8bit_ausgang[4]),
    .B5(Addierer_Bitweise_100bit_1_data_8bit_ausgang[5]),
    .B6(Addierer_Bitweise_100bit_1_data_8bit_ausgang[6]),
    .B7(Addierer_Bitweise_100bit_1_data_8bit_ausgang[7]), .S0(Data_8bit_Ausgang[0]),
    .S1(Data_8bit_Ausgang[1]), .S2(Data_8bit_Ausgang[2]), .S3(Data_8bit_Ausgang[3]),
    .S4(Data_8bit_Ausgang[4]), .S5(Data_8bit_Ausgang[5]), .S6(Data_8bit_Ausgang[6]), .S7(Data_8bit_Ausgang[7]));  // open: C_OUT
endmodule

module Decode_Jahr (
  input  [7:0] Data_Jahr_8bit_Eingang,
  output [7:0] Data_Jahr_8bit_Ausgang
);

  wire and_1_out, and_2_out, and_3_out, and_4_out, and_5_out, and_6_out, and_7_out, and_8_out, and_9_out,
       and_10_out, and_11_out, and_12_out, and_13_out, and_14_out, and_15_out, and_16_out, and_17_out,
       and_18_out, not_1_out, not_2_out, not_3_out, not_4_out, not_5_out, not_6_out, not_7_out, not_8_out,
       not_9_out, not_10_out, not_11_out, not_12_out, not_13_out, not_14_out, not_15_out, not_16_out,
       not_17_out, not_18_out, not_19_out, not_20_out, not_21_out, not_22_out, not_23_out, not_24_out,
       not_25_out, not_26_out, or_1_out, or_2_out, or_3_out, or_4_out, or_5_out;

  and and_1 (and_1_out, Data_Jahr_8bit_Eingang[7], Data_Jahr_8bit_Eingang[6], Data_Jahr_8bit_Eingang[4]);
  and and_2 (and_2_out, Data_Jahr_8bit_Eingang[7], Data_Jahr_8bit_Eingang[6], Data_Jahr_8bit_Eingang[5]);
  not not_1 (not_1_out, Data_Jahr_8bit_Eingang[7]);
  not not_2 (not_2_out, Data_Jahr_8bit_Eingang[6]);
  not not_3 (not_3_out, Data_Jahr_8bit_Eingang[5]);
  not not_4 (not_4_out, Data_Jahr_8bit_Eingang[4]);
  not not_5 (not_5_out, Data_Jahr_8bit_Eingang[7]);
  not not_6 (not_6_out, Data_Jahr_8bit_Eingang[5]);
  not not_7 (not_7_out, Data_Jahr_8bit_Eingang[7]);
  not not_8 (not_8_out, Data_Jahr_8bit_Eingang[4]);
  not not_9 (not_9_out, Data_Jahr_8bit_Eingang[5]);
  not not_10 (not_10_out, Data_Jahr_8bit_Eingang[4]);
  not not_11 (not_11_out, Data_Jahr_8bit_Eingang[6]);
  not not_12 (not_12_out, Data_Jahr_8bit_Eingang[7]);
  not not_13 (not_13_out, Data_Jahr_8bit_Eingang[6]);
  not not_14 (not_14_out, Data_Jahr_8bit_Eingang[7]);
  not not_15 (not_15_out, Data_Jahr_8bit_Eingang[4]);
  not not_16 (not_16_out, Data_Jahr_8bit_Eingang[7]);
  not not_17 (not_17_out, Data_Jahr_8bit_Eingang[5]);
  not not_18 (not_18_out, Data_Jahr_8bit_Eingang[6]);
  not not_19 (not_19_out, Data_Jahr_8bit_Eingang[5]);
  not not_20 (not_20_out, Data_Jahr_8bit_Eingang[5]);
  not not_21 (not_21_out, Data_Jahr_8bit_Eingang[4]);
  not not_22 (not_22_out, Data_Jahr_8bit_Eingang[6]);
  not not_23 (not_23_out, Data_Jahr_8bit_Eingang[7]);
  not not_24 (not_24_out, Data_Jahr_8bit_Eingang[4]);
  not not_25 (not_25_out, Data_Jahr_8bit_Eingang[5]);
  not not_26 (not_26_out, Data_Jahr_8bit_Eingang[4]);
  or or_1 (or_1_out, and_1_out, and_2_out);
  and and_3 (and_3_out, not_1_out, Data_Jahr_8bit_Eingang[6], Data_Jahr_8bit_Eingang[5], Data_Jahr_8bit_Eingang[4]);
  and and_4 (and_4_out, Data_Jahr_8bit_Eingang[7], not_2_out);
  and and_5 (and_5_out, Data_Jahr_8bit_Eingang[7], not_3_out, not_4_out);
  and and_6 (and_6_out, not_5_out, Data_Jahr_8bit_Eingang[6], not_6_out);
  and and_7 (and_7_out, not_7_out, Data_Jahr_8bit_Eingang[6], not_8_out);
  and and_8 (and_8_out, Data_Jahr_8bit_Eingang[6], not_9_out, not_10_out);
  and and_9 (and_9_out, Data_Jahr_8bit_Eingang[7], not_11_out, Data_Jahr_8bit_Eingang[5]);
  and and_10 (and_10_out, not_12_out, not_13_out, Data_Jahr_8bit_Eingang[5]);
  and and_11 (and_11_out, not_14_out, Data_Jahr_8bit_Eingang[5], not_15_out);
  and and_12 (and_12_out, not_16_out, Data_Jahr_8bit_Eingang[6], not_17_out, Data_Jahr_8bit_Eingang[4]);
  and and_13 (and_13_out, Data_Jahr_8bit_Eingang[7], not_18_out, not_19_out);
  and and_14 (and_14_out, Data_Jahr_8bit_Eingang[7], not_20_out, not_21_out);
  and and_15 (and_15_out, Data_Jahr_8bit_Eingang[7], Data_Jahr_8bit_Eingang[6], Data_Jahr_8bit_Eingang[5]);
  and and_16 (and_16_out, not_22_out, Data_Jahr_8bit_Eingang[4]);
  and and_17 (and_17_out, not_23_out, Data_Jahr_8bit_Eingang[6], not_24_out);
  and and_18 (and_18_out, Data_Jahr_8bit_Eingang[6], not_25_out, not_26_out);
  or or_2 (or_2_out, and_3_out, and_4_out, and_5_out);
  or or_3 (or_3_out, and_6_out, and_7_out, and_8_out, and_9_out);
  or or_4 (or_4_out, and_10_out, and_11_out, and_12_out, and_13_out, and_14_out, and_15_out);
  or or_5 (or_5_out, and_16_out, and_17_out, and_18_out);
  add8bit add8bit_0 (
    .Minus(1'b0), .C_IN(1'b0), .A0(Data_Jahr_8bit_Eingang[0]), .A1(Data_Jahr_8bit_Eingang[1]),
    .A2(Data_Jahr_8bit_Eingang[2]), .A3(Data_Jahr_8bit_Eingang[3]), .A4(1'b0), .A5(1'b0), .A6(1'b0),
    .A7(1'b0), .B0(1'b0), .B1(Data_Jahr_8bit_Eingang[4]), .B2(Data_Jahr_8bit_Eingang[5]), .B3(or_5_out),
    .B4(or_4_out), .B5(or_3_out), .B6(or_2_out), .B7(or_1_out), .S0(Data_Jahr_8bit_Ausgang[0]),
    .S1(Data_Jahr_8bit_Ausgang[1]), .S2(Data_Jahr_8bit_Ausgang[2]), .S3(Data_Jahr_8bit_Ausgang[3]),
    .S4(Data_Jahr_8bit_Ausgang[4]), .S5(Data_Jahr_8bit_Ausgang[5]), .S6(Data_Jahr_8bit_Ausgang[6]),
    .S7(Data_Jahr_8bit_Ausgang[7]));  // open: C_OUT
endmodule

module Deode_Monat (
  input  [4:0] Data_Monat_5bit_Eingang,
  output [4:0] Data_Jahr_5bit_Ausgang
);

  add4bit add4bit_0 (
    .Minus(1'b0), .C_IN(1'b0), .A0(Data_Monat_5bit_Eingang[0]), .A1(Data_Monat_5bit_Eingang[1]),
    .A2(Data_Monat_5bit_Eingang[2]), .A3(Data_Monat_5bit_Eingang[3]), .B0(1'b0),
    .B1(Data_Monat_5bit_Eingang[4]), .B2(1'b0), .B3(Data_Monat_5bit_Eingang[4]),
    .S0(Data_Jahr_5bit_Ausgang[0]), .S1(Data_Jahr_5bit_Ausgang[1]), .S3(Data_Jahr_5bit_Ausgang[2]),
    .S4(Data_Jahr_5bit_Ausgang[3]), .C_OUT(Data_Jahr_5bit_Ausgang[4]));
endmodule

module Decode_Tag (
  input  [5:0] Data_Tag_6bit_Eingang,
  output [5:0] Data_Tag_6bit_Ausgang
);

  add5bit add5bit_0 (
    .Minus(1'b0), .C_IN(1'b0), .A0(Data_Tag_6bit_Eingang[0]), .A1(Data_Tag_6bit_Eingang[1]),
    .A2(Data_Tag_6bit_Eingang[2]), .A3(Data_Tag_6bit_Eingang[3]), .A4(1'b0), .B0(1'b0),
    .B1(Data_Tag_6bit_Eingang[4]), .B2(Data_Tag_6bit_Eingang[5]), .B3(Data_Tag_6bit_Eingang[4]),
    .B4(Data_Tag_6bit_Eingang[5]), .S0(Data_Tag_6bit_Ausgang[0]), .S1(Data_Tag_6bit_Ausgang[1]),
    .S2(Data_Tag_6bit_Ausgang[2]), .S3(Data_Tag_6bit_Ausgang[3]), .S4(Data_Tag_6bit_Ausgang[4]),
    .C_OUT(Data_Tag_6bit_Ausgang[5]));
endmodule

module Decode_Stunde (
  input  [5:0] Data_Stunde_6bit_Eingang,
  output [5:0] Data_Stunde_6bit_Ausgang
);

  add5bit add5bit_0 (
    .Minus(1'b0), .C_IN(1'b0), .A0(Data_Stunde_6bit_Eingang[0]), .A1(Data_Stunde_6bit_Eingang[1]),
    .A2(Data_Stunde_6bit_Eingang[2]), .A3(Data_Stunde_6bit_Eingang[3]), .A4(1'b0), .B0(1'b0),
    .B1(Data_Stunde_6bit_Eingang[4]), .B2(Data_Stunde_6bit_Eingang[5]), .B3(Data_Stunde_6bit_Eingang[4]),
    .B4(Data_Stunde_6bit_Eingang[5]), .S0(Data_Stunde_6bit_Ausgang[0]), .S1(Data_Stunde_6bit_Ausgang[1]),
    .S2(Data_Stunde_6bit_Ausgang[2]), .S3(Data_Stunde_6bit_Ausgang[3]), .S4(Data_Stunde_6bit_Ausgang[4]),
    .C_OUT(Data_Stunde_6bit_Ausgang[5]));
endmodule

module Decode_Minute (
  input  [6:0] Data_Minute_7bit_Eingang,
  output [6:0] Data_Minute_7bit_Ausgang
);

  wire and_1_out, and_2_out, and_3_out, and_4_out, and_5_out, not_1_out, not_2_out, not_3_out, not_4_out,
       not_5_out, or_1_out, or_2_out;

  not not_1 (not_1_out, Data_Minute_7bit_Eingang[6]);
  not not_2 (not_2_out, Data_Minute_7bit_Eingang[4]);
  not not_3 (not_3_out, Data_Minute_7bit_Eingang[5]);
  not not_4 (not_4_out, Data_Minute_7bit_Eingang[6]);
  not not_5 (not_5_out, Data_Minute_7bit_Eingang[4]);
  and and_1 (and_1_out, not_1_out, Data_Minute_7bit_Eingang[5]);
  and and_2 (and_2_out, Data_Minute_7bit_Eingang[5], not_2_out);
  and and_3 (and_3_out, Data_Minute_7bit_Eingang[6], not_3_out, Data_Minute_7bit_Eingang[4]);
  and and_4 (and_4_out, not_4_out, Data_Minute_7bit_Eingang[4]);
  and and_5 (and_5_out, Data_Minute_7bit_Eingang[6], not_5_out);
  or or_1 (or_1_out, and_1_out, and_2_out, and_3_out);
  or or_2 (or_2_out, and_4_out, and_5_out);
  add6bit add6bit_0 (
    .Minus(1'b0), .C_IN(1'b0), .A0(Data_Minute_7bit_Eingang[0]), .A1(Data_Minute_7bit_Eingang[1]),
    .A2(Data_Minute_7bit_Eingang[2]), .A3(Data_Minute_7bit_Eingang[3]), .A4(1'b0), .A5(1'b0), .B0(1'b0),
    .B1(Data_Minute_7bit_Eingang[4]), .B2(Data_Minute_7bit_Eingang[5]), .B3(or_2_out), .B4(or_1_out),
    .B5(Data_Minute_7bit_Eingang[6]), .S0(Data_Minute_7bit_Ausgang[0]), .S1(Data_Minute_7bit_Ausgang[1]),
    .S2(Data_Minute_7bit_Ausgang[2]), .S3(Data_Minute_7bit_Ausgang[3]), .S4(Data_Minute_7bit_Ausgang[4]),
    .S5(Data_Minute_7bit_Ausgang[5]), .C_OUT(Data_Minute_7bit_Ausgang[6]));
endmodule

module Counter_1ms (
  input  Clock_2kHz,
  input  Enable,
  output Ausgang_1ms
);

  wire [1:0] Counter_2bit_0_ausgang_counter;

  Counter_2bit Counter_2bit_0 (
    .Clock(Clock_2kHz), .Enable(Enable), .Reset(Ausgang_1ms), .Ausgang_Counter(Counter_2bit_0_ausgang_counter));  // open: Ausgang_Counter_negiert
  and and_1 (Ausgang_1ms, Counter_2bit_0_ausgang_counter[0], ~Counter_2bit_0_ausgang_counter[1]);  // AND_Gate
endmodule

module Counter_2bit (
  input  Clock,
  input  Enable,
  input  Reset,
  output [1:0] Ausgang_Counter,
  output [1:0] Ausgang_Counter_negiert
);

  wire [1:0] add2bit_0_s0, Multiplexer_2bit_0_ausgang_2bit;

  add2bit add2bit_0 (
    .Minus(1'b0), .C_IN(1'b0), .A0(Ausgang_Counter[0]), .A1(Ausgang_Counter[1]), .B0(Enable), .B1(1'b0),
    .S0(add2bit_0_s0[0]), .S1(add2bit_0_s0[1]));  // open: C_OUT
  Multiplexer_2bit Multiplexer_2bit_0 (
    .Eingang_2bit_0(add2bit_0_s0), .Eingang_2bit_2(2'b00), .Eingang_2bit_3(2'b00),
    .Eingang_Umschalter({1'b0, Reset}), .Ausgang_2bit(Multiplexer_2bit_0_ausgang_2bit));
  D_Flip_Flop d_ff_1 (
    .D(Multiplexer_2bit_0_ausgang_2bit[0]), .clk(Clock), .Q(Ausgang_Counter[0]),
    .Qn(Ausgang_Counter_negiert[0]));  // open: preset, reset
  D_Flip_Flop d_ff_2 (
    .D(Multiplexer_2bit_0_ausgang_2bit[1]), .clk(Clock), .Q(Ausgang_Counter[1]),
    .Qn(Ausgang_Counter_negiert[1]));  // open: preset, reset
endmodule

module Multiplexer_2bit (
  input  [1:0] Eingang_2bit_0,
  input  [1:0] Eingang_2bit_2,
  input  [1:0] Eingang_2bit_3,
  input  [1:0] Eingang_Umschalter,
  output [1:0] Ausgang_2bit
);

  Multiplexer_1bit Multiplexer_1bit_0 (
    .I_0(Eingang_2bit_0[0]), .I_1(Eingang_2bit_2[0]), .I_2(Eingang_2bit_3[0]),
    .Umschalter(Eingang_Umschalter), .Ausgang(Ausgang_2bit[0]));
  Multiplexer_1bit Multiplexer_1bit_1 (
    .I_0(Eingang_2bit_0[1]), .I_1(Eingang_2bit_2[1]), .I_2(Eingang_2bit_3[1]),
    .Umschalter(Eingang_Umschalter), .Ausgang(Ausgang_2bit[1]));
endmodule

module Signalbreite_Zusammenzaehlen (
  input  Clock_2kHz,
  input  Data_Seriell,
  output [7:0] Signalbreite
);

  wire [9:0] Schieberegister_200bit_0_data_parallel_10bit_0, Schieberegister_200bit_0_data_parallel_10bit_1,
       Schieberegister_200bit_0_data_parallel_10bit_2, Schieberegister_200bit_0_data_parallel_10bit_3,
       Schieberegister_200bit_0_data_parallel_10bit_4, Schieberegister_200bit_0_data_parallel_10bit_5,
       Schieberegister_200bit_0_data_parallel_10bit_6, Schieberegister_200bit_0_data_parallel_10bit_7,
       Schieberegister_200bit_0_data_parallel_10bit_8, Schieberegister_200bit_0_data_parallel_10bit_9,
       Schieberegister_200bit_0_data_parallel_10bit_10, Schieberegister_200bit_0_data_parallel_10bit_11,
       Schieberegister_200bit_0_data_parallel_10bit_12, Schieberegister_200bit_0_data_parallel_10bit_13,
       Schieberegister_200bit_0_data_parallel_10bit_14, Schieberegister_200bit_0_data_parallel_10bit_15,
       Schieberegister_200bit_0_data_parallel_10bit_16, Schieberegister_200bit_0_data_parallel_10bit_17,
       Schieberegister_200bit_0_data_parallel_10bit_18, Schieberegister_200bit_0_data_parallel_10bit_19;

  Schieberegister_200bit Schieberegister_200bit_0 (
    .Clock_Eingang(Clock_2kHz), .Data_Seriell_Eingang(Data_Seriell), .Enable_Eingang(1'b1),
    .Data_Parallel_10bit_0(Schieberegister_200bit_0_data_parallel_10bit_0),
    .Data_Parallel_10bit_1(Schieberegister_200bit_0_data_parallel_10bit_1),
    .Data_Parallel_10bit_2(Schieberegister_200bit_0_data_parallel_10bit_2),
    .Data_Parallel_10bit_3(Schieberegister_200bit_0_data_parallel_10bit_3),
    .Data_Parallel_10bit_4(Schieberegister_200bit_0_data_parallel_10bit_4),
    .Data_Parallel_10bit_5(Schieberegister_200bit_0_data_parallel_10bit_5),
    .Data_Parallel_10bit_6(Schieberegister_200bit_0_data_parallel_10bit_6),
    .Data_Parallel_10bit_7(Schieberegister_200bit_0_data_parallel_10bit_7),
    .Data_Parallel_10bit_8(Schieberegister_200bit_0_data_parallel_10bit_8),
    .Data_Parallel_10bit_9(Schieberegister_200bit_0_data_parallel_10bit_9),
    .Data_Parallel_10bit_10(Schieberegister_200bit_0_data_parallel_10bit_10),
    .Data_Parallel_10bit_11(Schieberegister_200bit_0_data_parallel_10bit_11),
    .Data_Parallel_10bit_12(Schieberegister_200bit_0_data_parallel_10bit_12),
    .Data_Parallel_10bit_13(Schieberegister_200bit_0_data_parallel_10bit_13),
    .Data_Parallel_10bit_14(Schieberegister_200bit_0_data_parallel_10bit_14),
    .Data_Parallel_10bit_15(Schieberegister_200bit_0_data_parallel_10bit_15),
    .Data_Parallel_10bit_16(Schieberegister_200bit_0_data_parallel_10bit_16),
    .Data_Parallel_10bit_17(Schieberegister_200bit_0_data_parallel_10bit_17),
    .Data_Parallel_10bit_18(Schieberegister_200bit_0_data_parallel_10bit_18),
    .Data_Parallel_10bit_19(Schieberegister_200bit_0_data_parallel_10bit_19));
  Addierer_Bitweise_200bit Addierer_Bitweise_200bit_0 (
    .Data_10bit_Eingang_0(Schieberegister_200bit_0_data_parallel_10bit_0),
    .Data_10bit_Eingang_1(Schieberegister_200bit_0_data_parallel_10bit_1),
    .Data_10bit_Eingang_2(Schieberegister_200bit_0_data_parallel_10bit_2),
    .Data_10bit_Eingang_3(Schieberegister_200bit_0_data_parallel_10bit_3),
    .Data_10bit_Eingang_4(Schieberegister_200bit_0_data_parallel_10bit_4),
    .Data_10bit_Eingang_5(Schieberegister_200bit_0_data_parallel_10bit_5),
    .Data_10bit_Eingang_6(Schieberegister_200bit_0_data_parallel_10bit_6),
    .Data_10bit_Eingang_7(Schieberegister_200bit_0_data_parallel_10bit_7),
    .Data_10bit_Eingang_8(Schieberegister_200bit_0_data_parallel_10bit_8),
    .Data_10bit_Eingang_9(Schieberegister_200bit_0_data_parallel_10bit_9),
    .Data_10bit_Eingang_10(Schieberegister_200bit_0_data_parallel_10bit_10),
    .Data_10bit_Eingang_11(Schieberegister_200bit_0_data_parallel_10bit_11),
    .Data_10bit_Eingang_12(Schieberegister_200bit_0_data_parallel_10bit_12),
    .Data_10bit_Eingang_13(Schieberegister_200bit_0_data_parallel_10bit_13),
    .Data_10bit_Eingang_14(Schieberegister_200bit_0_data_parallel_10bit_14),
    .Data_10bit_Eingang_15(Schieberegister_200bit_0_data_parallel_10bit_15),
    .Data_10bit_Eingang_16(Schieberegister_200bit_0_data_parallel_10bit_16),
    .Data_10bit_Eingang_17(Schieberegister_200bit_0_data_parallel_10bit_17),
    .Data_10bit_Eingang_18(Schieberegister_200bit_0_data_parallel_10bit_18),
    .Data_10bit_Eingang_19(Schieberegister_200bit_0_data_parallel_10bit_19), .Data_8bit_Ausgang(Signalbreite));
endmodule

module Schieberegister_200bit (
  input  Clock_Eingang,
  input  Data_Seriell_Eingang,
  input  Enable_Eingang,
  output [9:0] Data_Parallel_10bit_0,
  output [9:0] Data_Parallel_10bit_1,
  output [9:0] Data_Parallel_10bit_2,
  output [9:0] Data_Parallel_10bit_3,
  output [9:0] Data_Parallel_10bit_4,
  output [9:0] Data_Parallel_10bit_5,
  output [9:0] Data_Parallel_10bit_6,
  output [9:0] Data_Parallel_10bit_7,
  output [9:0] Data_Parallel_10bit_8,
  output [9:0] Data_Parallel_10bit_9,
  output [9:0] Data_Parallel_10bit_10,
  output [9:0] Data_Parallel_10bit_11,
  output [9:0] Data_Parallel_10bit_12,
  output [9:0] Data_Parallel_10bit_13,
  output [9:0] Data_Parallel_10bit_14,
  output [9:0] Data_Parallel_10bit_15,
  output [9:0] Data_Parallel_10bit_16,
  output [9:0] Data_Parallel_10bit_17,
  output [9:0] Data_Parallel_10bit_18,
  output [9:0] Data_Parallel_10bit_19
);

  Schiebregister_100bit Schieberegister_100bit_0 (
    .Clock_Eingang(Clock_Eingang), .Data_Seriell_Eingang(Data_Seriell_Eingang),
    .Enable_Eingang(Enable_Eingang), .Data_Parallel_0x10bit_Ausgang(Data_Parallel_10bit_0),
    .Data_Parallel_1x10bit_Ausgang(Data_Parallel_10bit_1),
    .Data_Parallel_2x10bit_Ausgang(Data_Parallel_10bit_2),
    .Data_Parallel_3x10bit_Ausgang(Data_Parallel_10bit_3),
    .Data_Parallel_4x10bit_Ausgang(Data_Parallel_10bit_4),
    .Data_Parallel_5x10bit_Ausgang(Data_Parallel_10bit_5),
    .Data_Parallel_6x10bit_Ausgang(Data_Parallel_10bit_6),
    .Data_Parallel_7x10bit_Ausgang(Data_Parallel_10bit_7),
    .Data_Parallel_8x10bit_Ausgang(Data_Parallel_10bit_8),
    .Data_Parallel_9x10bit_Ausgang(Data_Parallel_10bit_9));
  Schiebregister_100bit Schieberegister_100bit_1 (
    .Clock_Eingang(Clock_Eingang), .Data_Seriell_Eingang(Data_Parallel_10bit_9[9]),
    .Enable_Eingang(Enable_Eingang), .Data_Parallel_0x10bit_Ausgang(Data_Parallel_10bit_10),
    .Data_Parallel_1x10bit_Ausgang(Data_Parallel_10bit_11),
    .Data_Parallel_2x10bit_Ausgang(Data_Parallel_10bit_12),
    .Data_Parallel_3x10bit_Ausgang(Data_Parallel_10bit_13),
    .Data_Parallel_4x10bit_Ausgang(Data_Parallel_10bit_14),
    .Data_Parallel_5x10bit_Ausgang(Data_Parallel_10bit_15),
    .Data_Parallel_6x10bit_Ausgang(Data_Parallel_10bit_16),
    .Data_Parallel_7x10bit_Ausgang(Data_Parallel_10bit_17),
    .Data_Parallel_8x10bit_Ausgang(Data_Parallel_10bit_18),
    .Data_Parallel_9x10bit_Ausgang(Data_Parallel_10bit_19));
endmodule

module Decode_DCF77_Signal (
  input  Clock_2kHz,
  input  Data_Seriell,
  output Bit_Sekunde_erkannt,
  output Bit_Data
);

  wire Bit_Threshhold1_c_out, Bit_Threshhold2_c_out, Bitdata_c_out, Counter_300ms_0_counter_300ms_out,
       Decode_DCF77_Signal_counting_0_counting_out, not_1_out, not_2_out;
  wire [7:0] Signalbreite_Zusammensaehlen_0_signalbreite;

  Signalbreite_Zusammenzaehlen Signalbreite_Zusammensaehlen_0 (
    .Clock_2kHz(Clock_2kHz), .Data_Seriell(Data_Seriell),
    .Signalbreite(Signalbreite_Zusammensaehlen_0_signalbreite));
  not not_1 (not_1_out, 1'b0);
  add8bit Bit_Threshhold1 (
    .Minus(not_1_out), .C_IN(1'b0), .A0(1'b0), .A1(1'b1), .A2(1'b0), .A3(1'b0), .A4(1'b1), .A5(1'b1),
    .A6(1'b0), .A7(1'b0), .B0(Signalbreite_Zusammensaehlen_0_signalbreite[0]),
    .B1(Signalbreite_Zusammensaehlen_0_signalbreite[1]), .B2(Signalbreite_Zusammensaehlen_0_signalbreite[2]),
    .B3(Signalbreite_Zusammensaehlen_0_signalbreite[3]), .B4(Signalbreite_Zusammensaehlen_0_signalbreite[4]),
    .B5(Signalbreite_Zusammensaehlen_0_signalbreite[5]), .B6(Signalbreite_Zusammensaehlen_0_signalbreite[6]),
    .B7(Signalbreite_Zusammensaehlen_0_signalbreite[7]), .C_OUT(Bit_Threshhold1_c_out));  // open: S0, S1, S2, S3, S4, S5, S6, S7
  add8bit Bitdata (
    .Minus(not_1_out), .C_IN(1'b0), .A0(1'b0), .A1(1'b0), .A2(1'b1), .A3(1'b1), .A4(1'b0), .A5(1'b0),
    .A6(1'b0), .A7(1'b1), .B0(Signalbreite_Zusammensaehlen_0_signalbreite[0]),
    .B1(Signalbreite_Zusammensaehlen_0_signalbreite[1]), .B2(Signalbreite_Zusammensaehlen_0_signalbreite[2]),
    .B3(Signalbreite_Zusammensaehlen_0_signalbreite[3]), .B4(Signalbreite_Zusammensaehlen_0_signalbreite[4]),
    .B5(Signalbreite_Zusammensaehlen_0_signalbreite[5]), .B6(Signalbreite_Zusammensaehlen_0_signalbreite[6]),
    .B7(Signalbreite_Zusammensaehlen_0_signalbreite[7]), .C_OUT(Bitdata_c_out));  // open: S0, S1, S2, S3, S4, S5, S6, S7
  add8bit Bit_Threshhold2 (
    .Minus(not_1_out), .C_IN(1'b0), .A0(Signalbreite_Zusammensaehlen_0_signalbreite[0]),
    .A1(Signalbreite_Zusammensaehlen_0_signalbreite[1]), .A2(Signalbreite_Zusammensaehlen_0_signalbreite[2]),
    .A3(Signalbreite_Zusammensaehlen_0_signalbreite[3]), .A4(Signalbreite_Zusammensaehlen_0_signalbreite[4]),
    .A5(Signalbreite_Zusammensaehlen_0_signalbreite[5]), .A6(Signalbreite_Zusammensaehlen_0_signalbreite[6]),
    .A7(Signalbreite_Zusammensaehlen_0_signalbreite[7]), .B0(1'b0), .B1(1'b1), .B2(1'b0), .B3(1'b0),
    .B4(1'b1), .B5(1'b1), .B6(1'b0), .B7(1'b0), .C_OUT(Bit_Threshhold2_c_out));  // open: S0, S1, S2, S3, S4, S5, S6, S7
  Decode_DCF77_Signal_counting Decode_DCF77_Signal_counting_0 (
    .Clock(Clock_2kHz), .Bit_threshhold1(Bit_Threshhold1_c_out),
    .Counter_300ms(Counter_300ms_0_counter_300ms_out),
    .counting_OUT(Decode_DCF77_Signal_counting_0_counting_out));
  Decode_DCF77_Signal_Bitdata Decode_DCF77_Signal_Bitdata_0 (
    .Clock(Clock_2kHz), .Counting(Decode_DCF77_Signal_counting_0_counting_out),
    .Bit_threshhold1(Bit_Threshhold1_c_out), .Bitdata(Bitdata_c_out), .BitData_OUT(Bit_Data));
  not not_2 (not_2_out, Decode_DCF77_Signal_counting_0_counting_out);
  Counter_300ms Counter_300ms_0 (
    .Clock_1kHz(Clock_2kHz), .Enable(Decode_DCF77_Signal_counting_0_counting_out), .Reset(not_2_out),
    .Counter_300ms_OUT(Counter_300ms_0_counter_300ms_out));
  and and_1 (Bit_Sekunde_erkannt, Counter_300ms_0_counter_300ms_out, Bit_Threshhold2_c_out);
endmodule

module Counter_9bit (
  input  Clock,
  input  Reset,
  input  Load,
  input  Enable,
  input  [8:0] Data_Load,
  output [8:0] Counter_Ausgang,
  output [8:0] Counter_Ausgang_negiert
);

  wire [8:0] add9bit_0_ausgang_0, Multiplexer_9bit_0_ausgang_0;

  add9bit add9bit_0 (
    .MINUS(1'b0), .Carry_IN(1'b0), .Eingang_0(Counter_Ausgang), .Eingang_1({{8{1'b0}}, Enable}),
    .Ausgang_0(add9bit_0_ausgang_0));  // open: Carry_OUT
  Multiplexer_9bit Multiplexer_9bit_0 (
    .Umschalter({Load, Reset}), .Eingang_0(add9bit_0_ausgang_0), .Eingang_1({9{1'b0}}),
    .Eingang_2(Data_Load), .Ausgang_0(Multiplexer_9bit_0_ausgang_0));
  D_Flip_Flop d_ff_1 (
    .D(Multiplexer_9bit_0_ausgang_0[0]), .clk(Clock), .Q(Counter_Ausgang[0]), .Qn(Counter_Ausgang_negiert[0]));  // open: preset, reset
  D_Flip_Flop d_ff_2 (
    .D(Multiplexer_9bit_0_ausgang_0[1]), .clk(Clock), .Q(Counter_Ausgang[1]), .Qn(Counter_Ausgang_negiert[1]));  // open: preset, reset
  D_Flip_Flop d_ff_3 (
    .D(Multiplexer_9bit_0_ausgang_0[2]), .clk(Clock), .Q(Counter_Ausgang[2]), .Qn(Counter_Ausgang_negiert[2]));  // open: preset, reset
  D_Flip_Flop d_ff_4 (
    .D(Multiplexer_9bit_0_ausgang_0[3]), .clk(Clock), .Q(Counter_Ausgang[3]), .Qn(Counter_Ausgang_negiert[3]));  // open: preset, reset
  D_Flip_Flop d_ff_5 (
    .D(Multiplexer_9bit_0_ausgang_0[4]), .clk(Clock), .Q(Counter_Ausgang[4]), .Qn(Counter_Ausgang_negiert[4]));  // open: preset, reset
  D_Flip_Flop d_ff_6 (
    .D(Multiplexer_9bit_0_ausgang_0[5]), .clk(Clock), .Q(Counter_Ausgang[5]), .Qn(Counter_Ausgang_negiert[5]));  // open: preset, reset
  D_Flip_Flop d_ff_7 (
    .D(Multiplexer_9bit_0_ausgang_0[6]), .clk(Clock), .Q(Counter_Ausgang[6]), .Qn(Counter_Ausgang_negiert[6]));  // open: preset, reset
  D_Flip_Flop d_ff_8 (
    .D(Multiplexer_9bit_0_ausgang_0[7]), .clk(Clock), .Q(Counter_Ausgang[7]), .Qn(Counter_Ausgang_negiert[7]));  // open: preset, reset
  D_Flip_Flop d_ff_9 (
    .D(Multiplexer_9bit_0_ausgang_0[8]), .clk(Clock), .Q(Counter_Ausgang[8]), .Qn(Counter_Ausgang_negiert[8]));  // open: preset, reset
endmodule

module add9bit (
  input  MINUS,
  input  Carry_IN,
  input  [8:0] Eingang_0,
  input  [8:0] Eingang_1,
  output [8:0] Ausgang_0,
  output Carry_OUT
);

  wire add1bit_0_c_out, add1bit_1_c_out, add1bit_2_c_out, add1bit_3_c_out, add1bit_4_c_out, add1bit_5_c_out,
       add1bit_6_c_out, add1bit_7_c_out;

  add1bit add1bit_0 (
    .MINUS(MINUS), .C_IN(Carry_IN), .A(Eingang_0[0]), .B(Eingang_1[0]), .S(Ausgang_0[0]),
    .C_OUT(add1bit_0_c_out));
  add1bit add1bit_1 (
    .MINUS(MINUS), .C_IN(add1bit_0_c_out), .A(Eingang_0[1]), .B(Eingang_1[1]), .S(Ausgang_0[1]),
    .C_OUT(add1bit_1_c_out));
  add1bit add1bit_2 (
    .MINUS(MINUS), .C_IN(add1bit_1_c_out), .A(Eingang_0[2]), .B(Eingang_1[2]), .S(Ausgang_0[2]),
    .C_OUT(add1bit_2_c_out));
  add1bit add1bit_3 (
    .MINUS(MINUS), .C_IN(add1bit_2_c_out), .A(Eingang_0[3]), .B(Eingang_1[3]), .S(Ausgang_0[3]),
    .C_OUT(add1bit_3_c_out));
  add1bit add1bit_4 (
    .MINUS(MINUS), .C_IN(add1bit_3_c_out), .A(Eingang_0[4]), .B(Eingang_1[4]), .S(Ausgang_0[4]),
    .C_OUT(add1bit_4_c_out));
  add1bit add1bit_5 (
    .MINUS(MINUS), .C_IN(add1bit_4_c_out), .A(Eingang_0[5]), .B(Eingang_1[5]), .S(Ausgang_0[5]),
    .C_OUT(add1bit_5_c_out));
  add1bit add1bit_6 (
    .MINUS(MINUS), .C_IN(add1bit_5_c_out), .A(Eingang_0[6]), .B(Eingang_1[6]), .S(Ausgang_0[6]),
    .C_OUT(add1bit_6_c_out));
  add1bit add1bit_7 (
    .MINUS(MINUS), .C_IN(add1bit_6_c_out), .A(Eingang_0[7]), .B(Eingang_1[7]), .S(Ausgang_0[7]),
    .C_OUT(add1bit_7_c_out));
  add1bit add1bit_8 (
    .MINUS(MINUS), .C_IN(add1bit_7_c_out), .A(Eingang_0[8]), .B(Eingang_1[8]), .S(Ausgang_0[8]),
    .C_OUT(Carry_OUT));
endmodule

module Multiplexer_9bit (
  input  [1:0] Umschalter,
  input  [8:0] Eingang_0,
  input  [8:0] Eingang_1,
  input  [8:0] Eingang_2,
  output [8:0] Ausgang_0
);

  Multiplexer_1bit Multiplexer_1bit_0 (
    .I_0(Eingang_0[0]), .I_1(Eingang_1[0]), .I_2(Eingang_2[0]), .Umschalter(Umschalter),
    .Ausgang(Ausgang_0[0]));
  Multiplexer_1bit Multiplexer_1bit_1 (
    .I_0(Eingang_0[1]), .I_1(Eingang_1[1]), .I_2(Eingang_2[1]), .Umschalter(Umschalter),
    .Ausgang(Ausgang_0[1]));
  Multiplexer_1bit Multiplexer_1bit_2 (
    .I_0(Eingang_0[2]), .I_1(Eingang_1[2]), .I_2(Eingang_2[2]), .Umschalter(Umschalter),
    .Ausgang(Ausgang_0[2]));
  Multiplexer_1bit Multiplexer_1bit_3 (
    .I_0(Eingang_0[3]), .I_1(Eingang_1[3]), .I_2(Eingang_2[3]), .Umschalter(Umschalter),
    .Ausgang(Ausgang_0[3]));
  Multiplexer_1bit Multiplexer_1bit_4 (
    .I_0(Eingang_0[4]), .I_1(Eingang_1[4]), .I_2(Eingang_2[4]), .Umschalter(Umschalter),
    .Ausgang(Ausgang_0[4]));
  Multiplexer_1bit Multiplexer_1bit_5 (
    .I_0(Eingang_0[5]), .I_1(Eingang_1[5]), .I_2(Eingang_2[5]), .Umschalter(Umschalter),
    .Ausgang(Ausgang_0[5]));
  Multiplexer_1bit Multiplexer_1bit_6 (
    .I_0(Eingang_0[6]), .I_1(Eingang_1[6]), .I_2(Eingang_2[6]), .Umschalter(Umschalter),
    .Ausgang(Ausgang_0[6]));
  Multiplexer_1bit Multiplexer_1bit_7 (
    .I_0(Eingang_0[7]), .I_1(Eingang_1[7]), .I_2(Eingang_2[7]), .Umschalter(Umschalter),
    .Ausgang(Ausgang_0[7]));
  Multiplexer_1bit Multiplexer_1bit_8 (
    .I_0(Eingang_0[8]), .I_1(Eingang_1[8]), .I_2(Eingang_2[8]), .Umschalter(Umschalter),
    .Ausgang(Ausgang_0[8]));
endmodule

module Counter_300ms (
  input  Clock_1kHz,
  input  Enable,
  input  Reset,
  output Counter_300ms_OUT
);

  wire or_1_out;
  wire [8:0] Counter_9bit_0_counter_ausgang, Counter_9bit_0_counter_ausgang_negiert;

  or or_1 (or_1_out, Reset, Counter_300ms_OUT);
  Counter_9bit Counter_9bit_0 (
    .Clock(Clock_1kHz), .Reset(or_1_out), .Load(1'b0), .Enable(Enable), .Data_Load({9{1'b0}}),
    .Counter_Ausgang(Counter_9bit_0_counter_ausgang),
    .Counter_Ausgang_negiert(Counter_9bit_0_counter_ausgang_negiert));
  and and_1 (Counter_300ms_OUT, Counter_9bit_0_counter_ausgang[8], Counter_9bit_0_counter_ausgang_negiert[7], Counter_9bit_0_counter_ausgang_negiert[6], Counter_9bit_0_counter_ausgang[5], Counter_9bit_0_counter_ausgang_negiert[4], Counter_9bit_0_counter_ausgang[3], Counter_9bit_0_counter_ausgang[2], Counter_9bit_0_counter_ausgang_negiert[1], Counter_9bit_0_counter_ausgang_negiert[0]);
endmodule

module Schieberegister_DCF77Data_59bit (
  input  Clock,
  input  Data_In,
  input  Enable,
  output Bit_MinuteAnfang,
  output [13:0] Data_Wetter,
  output [5:0] Data_Zeitsystem,
  output [7:0] Data_Minute,
  output [6:0] Data_Stunden,
  output [5:0] Data_Tag,
  output [2:0] Data_Wochentag,
  output [4:0] Data_Monat,
  output [7:0] Data_Jahr,
  output Parity3
);

  wire Schieberegister_1_data_seriell_out, Schieberegister_2_data_seriell_out,
       Schieberegister_3_data_seriell_out, Schieberegister_4_data_seriell_out,
       Schieberegister_5_data_seriell_out, Schieberegister_6_data_seriell_out,
       Schieberegister_7_data_seriell_out, Schieberegister_8_data_seriell_out;

  SR_1bit Schieberegister_9 (
    .Clock(Clock), .Enable(Enable), .Data_Seriell_IN(Schieberegister_8_data_seriell_out),
    .Data_Seriell_OUT(Bit_MinuteAnfang));
  SR_1bit Schieberegister_0 (.Clock(Clock), .Enable(Enable), .Data_Seriell_IN(Data_In), .Data_Seriell_OUT(Parity3));
  SR_8bit Schieberegister_1 (
    .Clock(Clock), .Enable(Enable), .Data_Seriell_IN(Parity3),
    .Data_Parallel_OUT({Data_Jahr[0], Data_Jahr[1], Data_Jahr[2], Data_Jahr[3], Data_Jahr[4], Data_Jahr[5], Data_Jahr[6], Data_Jahr[7]}),
    .Data_Seriell_OUT(Schieberegister_1_data_seriell_out));
  SR_5bit Schieberegister_2 (
    .Clock(Clock), .Enable(Enable), .Data_Seriell_IN(Schieberegister_1_data_seriell_out),
    .Data_Parallel_OUT({Data_Monat[0], Data_Monat[1], Data_Monat[2], Data_Monat[3], Data_Monat[4]}),
    .Data_Seriell_OUT(Schieberegister_2_data_seriell_out));
  SR_3bit Schieberegister_3 (
    .Clock(Clock), .Enable(Enable), .Data_Seriell_IN(Schieberegister_2_data_seriell_out),
    .Data_Parallel_OUT({Data_Wochentag[0], Data_Wochentag[1], Data_Wochentag[2]}),
    .Data_Seriell_OUT(Schieberegister_3_data_seriell_out));
  SR_6bit Schieberegister_4 (
    .Clock(Clock), .Enable(Enable), .Data_Seriell_IN(Schieberegister_3_data_seriell_out),
    .Data_Parallel_OUT({Data_Tag[0], Data_Tag[1], Data_Tag[2], Data_Tag[3], Data_Tag[4], Data_Tag[5]}),
    .Data_Seriell_OUT(Schieberegister_4_data_seriell_out));
  SR_7bit Schieberegister_5 (
    .Clock(Clock), .Enable(Enable), .Data_Seriell_IN(Schieberegister_4_data_seriell_out),
    .Data_Parallel_OUT({Data_Stunden[0], Data_Stunden[1], Data_Stunden[2], Data_Stunden[3], Data_Stunden[4], Data_Stunden[5], Data_Stunden[6]}),
    .Data_Seriell_OUT(Schieberegister_5_data_seriell_out));
  SR_8bit Schieberegister_6 (
    .Clock(Clock), .Enable(Enable), .Data_Seriell_IN(Schieberegister_5_data_seriell_out),
    .Data_Parallel_OUT({Data_Minute[0], Data_Minute[1], Data_Minute[2], Data_Minute[3], Data_Minute[4], Data_Minute[5], Data_Minute[6], Data_Minute[7]}),
    .Data_Seriell_OUT(Schieberegister_6_data_seriell_out));
  SR_6bit Schieberegister_7 (
    .Clock(Clock), .Enable(Enable), .Data_Seriell_IN(Schieberegister_6_data_seriell_out),
    .Data_Parallel_OUT({Data_Zeitsystem[0], Data_Zeitsystem[1], Data_Zeitsystem[2], Data_Zeitsystem[3], Data_Zeitsystem[4], Data_Zeitsystem[5]}),
    .Data_Seriell_OUT(Schieberegister_7_data_seriell_out));
  SR_14bit Schieberegister_8 (
    .Clock(Clock), .Enable(Enable), .Data_Seriell_IN(Schieberegister_7_data_seriell_out),
    .Data_Parallel_OUT({Data_Wetter[0], Data_Wetter[1], Data_Wetter[2], Data_Wetter[3], Data_Wetter[4], Data_Wetter[5], Data_Wetter[6], Data_Wetter[7], Data_Wetter[8], Data_Wetter[9], Data_Wetter[10], Data_Wetter[11], Data_Wetter[12], Data_Wetter[13]}),
    .Data_Seriell_OUT(Schieberegister_8_data_seriell_out));
endmodule

module Paritycheck_Even_8bit (
  input  [7:0] Data_IN,
  output Data_Fehler
);

  wire xor_1_out, xor_2_out, xor_3_out, xor_4_out, xor_5_out, xor_6_out;

  xor xor_1 (xor_1_out, Data_IN[0], Data_IN[1]);
  xor xor_2 (xor_2_out, xor_1_out, Data_IN[2]);
  xor xor_3 (xor_3_out, xor_2_out, Data_IN[3]);
  xor xor_4 (xor_4_out, xor_3_out, Data_IN[4]);
  xor xor_5 (xor_5_out, xor_4_out, Data_IN[5]);
  xor xor_6 (xor_6_out, xor_5_out, Data_IN[6]);
  xor xor_7 (Data_Fehler, xor_6_out, Data_IN[7]);
endmodule

module Paritycheck_Even_7bit (
  input  [6:0] Data_IN,
  output Data_Fehler
);

  wire xor_1_out, xor_2_out, xor_3_out, xor_4_out, xor_5_out;

  xor xor_1 (xor_1_out, Data_IN[0], Data_IN[1]);
  xor xor_2 (xor_2_out, xor_1_out, Data_IN[2]);
  xor xor_3 (xor_3_out, xor_2_out, Data_IN[3]);
  xor xor_4 (xor_4_out, xor_3_out, Data_IN[4]);
  xor xor_5 (xor_5_out, xor_4_out, Data_IN[5]);
  xor xor_6 (Data_Fehler, xor_5_out, Data_IN[6]);
endmodule

module Paritycheck_Even_23bit (
  input  [22:0] Data_IN,
  output Data_Fehler
);

  wire xor_1_out, xor_2_out, xor_3_out, xor_4_out, xor_5_out, xor_6_out, xor_7_out, xor_8_out, xor_9_out,
       xor_10_out, xor_11_out, xor_12_out, xor_13_out, xor_14_out, xor_15_out, xor_16_out, xor_17_out,
       xor_18_out, xor_19_out, xor_20_out, xor_21_out;

  xor xor_1 (xor_1_out, Data_IN[0], Data_IN[1]);
  xor xor_2 (xor_2_out, xor_1_out, Data_IN[2]);
  xor xor_3 (xor_3_out, xor_2_out, Data_IN[3]);
  xor xor_4 (xor_4_out, xor_3_out, Data_IN[4]);
  xor xor_5 (xor_5_out, xor_4_out, Data_IN[5]);
  xor xor_6 (xor_6_out, xor_5_out, Data_IN[6]);
  xor xor_7 (xor_7_out, xor_6_out, Data_IN[7]);
  xor xor_8 (xor_8_out, xor_7_out, Data_IN[8]);
  xor xor_9 (xor_9_out, xor_8_out, Data_IN[9]);
  xor xor_10 (xor_10_out, xor_9_out, Data_IN[10]);
  xor xor_11 (xor_11_out, xor_10_out, Data_IN[11]);
  xor xor_12 (xor_12_out, xor_11_out, Data_IN[12]);
  xor xor_13 (xor_13_out, xor_12_out, Data_IN[13]);
  xor xor_14 (xor_14_out, xor_13_out, Data_IN[14]);
  xor xor_15 (xor_15_out, xor_14_out, Data_IN[15]);
  xor xor_16 (xor_16_out, xor_15_out, Data_IN[16]);
  xor xor_17 (xor_17_out, xor_16_out, Data_IN[17]);
  xor xor_18 (xor_18_out, xor_17_out, Data_IN[18]);
  xor xor_19 (xor_19_out, xor_18_out, Data_IN[19]);
  xor xor_20 (xor_20_out, xor_19_out, Data_IN[20]);
  xor xor_21 (xor_21_out, xor_20_out, Data_IN[21]);
  xor xor_22 (Data_Fehler, xor_21_out, Data_IN[22]);
endmodule

module Decode_DCF77_Signal_Bitdata (
  input  Clock,
  input  Counting,
  input  Bit_threshhold1,
  input  Bitdata,
  output BitData_OUT
);

  wire and_1_out, and_2_out, and_3_out, not_1_out, or_1_out;

  not not_1 (not_1_out, Bit_threshhold1);
  and and_1 (and_1_out, not_1_out, BitData_OUT);
  and and_2 (and_2_out, Counting, BitData_OUT);
  and and_3 (and_3_out, Counting, Bitdata);
  or or_1 (or_1_out, and_1_out, and_2_out, and_3_out);
  D_Flip_Flop d_ff_1 (.D(or_1_out), .clk(Clock), .Q(BitData_OUT));  // open: Qn, preset, reset
endmodule

module Decode_DCF77_Signal_counting (
  input  Clock,
  input  Bit_threshhold1,
  input  Counter_300ms,
  output counting_OUT
);

  wire and_1_out, and_2_out, not_1_out, not_2_out, or_1_out;

  not not_1 (not_1_out, Counter_300ms);
  not not_2 (not_2_out, Counter_300ms);
  and and_1 (and_1_out, not_1_out, counting_OUT);
  and and_2 (and_2_out, Bit_threshhold1, not_2_out);
  or or_1 (or_1_out, and_1_out, and_2_out);
  D_Flip_Flop d_ff_1 (.D(or_1_out), .clk(Clock), .Q(counting_OUT));  // open: Qn, preset, reset
endmodule

module Decode_DCF77Data (
  input  [6:0] Data_Minute_IN,
  input  [5:0] Data_Stunde_IN,
  input  [5:0] Data_Tag_IN,
  input  [4:0] Data_Monat_IN,
  input  [7:0] Data_Jahr_IN,
  output [6:0] Data_Minute_OUT,
  output [5:0] Data_Stunde_OUT,
  output [5:0] Data_Tag_OUT,
  output [4:0] Data_Monat_OUT,
  output [7:0] Data_Jahr_OUT
);

  Decode_Minute Decode_Minute_0 (.Data_Minute_7bit_Eingang(Data_Minute_IN), .Data_Minute_7bit_Ausgang(Data_Minute_OUT));
  Decode_Stunde Decode_Stunde_0 (.Data_Stunde_6bit_Eingang(Data_Stunde_IN), .Data_Stunde_6bit_Ausgang(Data_Stunde_OUT));
  Decode_Tag Decode_Tag_0 (.Data_Tag_6bit_Eingang(Data_Tag_IN), .Data_Tag_6bit_Ausgang(Data_Tag_OUT));
  Deode_Monat Decode_Monat_0 (.Data_Monat_5bit_Eingang(Data_Monat_IN), .Data_Jahr_5bit_Ausgang(Data_Monat_OUT));
  Decode_Jahr Decode_Jahr_0 (.Data_Jahr_8bit_Eingang(Data_Jahr_IN), .Data_Jahr_8bit_Ausgang(Data_Jahr_OUT));
endmodule

module Parity_Check (
  input  [7:0] Data_Minute,
  input  [6:0] Data_Stunde,
  input  [5:0] Data_Tag,
  input  [2:0] Data_Wochentag,
  input  [4:0] Data_Monat,
  input  [7:0] Data_Jahr,
  input  Parity3,
  output Data_Fehler
);

  wire Paritycheck_0_data_fehler, Paritycheck_1_data_fehler, Paritycheck_2_data_fehler;

  Paritycheck_Even_8bit Paritycheck_0 (.Data_IN(Data_Minute), .Data_Fehler(Paritycheck_0_data_fehler));
  Paritycheck_Even_7bit Paritycheck_1 (.Data_IN(Data_Stunde), .Data_Fehler(Paritycheck_1_data_fehler));
  Paritycheck_Even_23bit Paritycheck_2 (
    .Data_IN({Parity3, Data_Jahr, Data_Monat, Data_Wochentag, Data_Tag}),
    .Data_Fehler(Paritycheck_2_data_fehler));
  or or_1 (Data_Fehler, Paritycheck_0_data_fehler, Paritycheck_1_data_fehler, Paritycheck_2_data_fehler);
endmodule

module DCF77Data_Pruefen (
  input  [6:0] Data_Minute_bin,
  input  [5:0] Data_Stunde_bin,
  input  [5:0] Data_Tag_bin,
  input  [4:0] Data_Monat_bin,
  input  [7:0] Data_Jahr_bin,
  output Data_Fehler
);

  wire add5bit_0_c_out, add6bit_0_c_out, add6bit_1_c_out, add7bit_0_s7, add8bit_0_c_out;

  add7bit add7bit_0 (
    .Minus(1'b1), .C_IN(1'b0), .A0(1'b1), .A1(1'b1), .A2(1'b0), .A3(1'b1), .A4(1'b1), .A5(1'b1), .A6(1'b0),
    .B0(Data_Minute_bin[0]), .B1(Data_Minute_bin[1]), .B2(Data_Minute_bin[2]), .B3(Data_Minute_bin[3]),
    .B4(Data_Minute_bin[4]), .B5(Data_Minute_bin[5]), .B7(Data_Minute_bin[6]), .S7(add7bit_0_s7));  // open: S0, S1, S2, S3, S4, S5, S6
  add6bit add6bit_0 (
    .Minus(1'b1), .C_IN(1'b0), .A0(1'b1), .A1(1'b1), .A2(1'b1), .A3(1'b0), .A4(1'b1), .A5(1'b0),
    .B0(Data_Stunde_bin[0]), .B1(Data_Stunde_bin[1]), .B2(Data_Stunde_bin[2]), .B3(Data_Stunde_bin[3]),
    .B4(Data_Stunde_bin[4]), .B5(Data_Stunde_bin[5]), .C_OUT(add6bit_0_c_out));  // open: S0, S1, S2, S3, S4, S5
  add6bit add6bit_1 (
    .Minus(1'b1), .C_IN(1'b0), .A0(1'b0), .A1(1'b0), .A2(1'b0), .A3(1'b0), .A4(1'b0), .A5(1'b1),
    .B0(Data_Tag_bin[0]), .B1(Data_Tag_bin[1]), .B2(Data_Tag_bin[2]), .B3(Data_Tag_bin[3]),
    .B4(Data_Tag_bin[4]), .B5(Data_Tag_bin[5]), .C_OUT(add6bit_1_c_out));  // open: S0, S1, S2, S3, S4, S5
  add5bit add5bit_0 (
    .Minus(1'b1), .C_IN(1'b0), .A0(1'b0), .A1(1'b0), .A2(1'b1), .A3(1'b1), .A4(1'b0), .B0(Data_Monat_bin[0]),
    .B1(Data_Monat_bin[1]), .B2(Data_Monat_bin[2]), .B3(Data_Monat_bin[3]), .B4(Data_Monat_bin[4]),
    .C_OUT(add5bit_0_c_out));  // open: S0, S1, S2, S3, S4
  add8bit add8bit_0 (
    .Minus(1'b1), .C_IN(1'b0), .A0(1'b1), .A1(1'b1), .A2(1'b0), .A3(1'b0), .A4(1'b0), .A5(1'b1), .A6(1'b1),
    .A7(1'b0), .B0(Data_Jahr_bin[0]), .B1(Data_Jahr_bin[1]), .B2(Data_Jahr_bin[2]), .B3(Data_Jahr_bin[3]),
    .B4(Data_Jahr_bin[4]), .B5(Data_Jahr_bin[5]), .B6(Data_Jahr_bin[6]), .B7(Data_Jahr_bin[7]),
    .C_OUT(add8bit_0_c_out));  // open: S0, S1, S2, S3, S4, S5, S6, S7
  or or_1 (Data_Fehler, add7bit_0_s7, add6bit_0_c_out, add6bit_1_c_out, add5bit_0_c_out, add8bit_0_c_out);
endmodule

module Storage_Time_Data (
  input  Clock,
  input  Load,
  input  Sekunde_IN,
  input  [5:0] Data_Minute_IN,
  input  [4:0] Data_Stunde_IN,
  input  [5:0] Data_Tag_IN,
  input  [2:0] Data_Wochentag_IN,
  input  [4:0] Data_Monat_IN,
  input  [7:0] Data_Jahr_IN,
  output [5:0] Data_Sekunde_OUT,
  output [5:0] Data_Minute_OUT,
  output [4:0] Data_Stunde_OUT,
  output [5:0] Data_Tag_OUT,
  output [2:0] Data_Wochentag_OUT,
  output [4:0] Data_Monat_OUT,
  output [7:0] Data_Jahr_OUT
);

  wire Storage_Counter_Minute_Data_0_carry_stunde, Storage_Counter_Second_Data_0_carry_minute;

  Storage_Tag_Data Storage_Tag_Data_0 (
    .Clock(Clock), .Load(Load), .Data_Tag_IN(Data_Tag_IN), .Data_Tag_OUT(Data_Tag_OUT));
  Storage_Counter_Second_Data Storage_Counter_Second_Data_0 (
    .Clock(Clock), .Load(Load), .Enable(Sekunde_IN), .Data_Sekunde_Load({6{1'b0}}),
    .Data_Sekunde_OUT(Data_Sekunde_OUT), .Carry_Minute(Storage_Counter_Second_Data_0_carry_minute));
  Storage_Counter_Minute_Data Storage_Counter_Minute_Data_0 (
    .Clock(Clock), .Load(Load), .Enable(Storage_Counter_Second_Data_0_carry_minute),
    .Data_Minute_Load(Data_Minute_IN), .Data_Minute_OUT(Data_Minute_OUT),
    .Carry_Stunde(Storage_Counter_Minute_Data_0_carry_stunde));
  Storage_Counter_Stunde_Data Storage_Counter_Stunde_Data_0 (
    .Clock(Clock), .Load(Load), .Enable(Storage_Counter_Minute_Data_0_carry_stunde),
    .Data_Stunde_Load(Data_Stunde_IN), .Data_Stunde_IN(Data_Stunde_OUT));  // open: Stunde_Carry
  Storage_Monat_Data Storage_Monat_Data_0 (
    .Clock(Clock), .Load(Load), .Data_Monat_IN(Data_Monat_IN), .Data_Monat_OUT(Data_Monat_OUT));
  Storage_Jahr_Data Storage_Jahr_Data_0 (
    .Clock(Clock), .Load(Load), .Data_Jahr_IN(Data_Jahr_IN), .Data_Jahr_OUT(Data_Jahr_OUT));
  Storage_Wochentag_Data Storage_Wochentag_Data_0 (
    .Clock(Clock), .Load(Load), .Data_Wochentag_IN(Data_Wochentag_IN), .Data_Wochentag_OUT(Data_Wochentag_OUT));
endmodule

module Storage_Counter_Second_Data (
  input  Clock,
  input  Load,
  input  Enable,
  input  [5:0] Data_Sekunde_Load,
  output [5:0] Data_Sekunde_OUT,
  output Carry_Minute
);

  wire and_2_out, and_3_out;
  wire [0:0] and_1_out;
  wire [5:0] add6bit_0_s0, Multiplexer_6bit_0_ausgang_0;

  and and_1 (and_1_out[0], ~Load, Enable, and_2_out);  // AND_Gate
  add6bit add6bit_0 (
    .Minus(1'b0), .C_IN(1'b0), .A0(Data_Sekunde_OUT[0]), .A1(Data_Sekunde_OUT[1]), .A2(Data_Sekunde_OUT[2]),
    .A3(Data_Sekunde_OUT[3]), .A4(Data_Sekunde_OUT[4]), .A5(Data_Sekunde_OUT[5]), .B0(Enable), .B1(1'b0),
    .B2(1'b0), .B3(1'b0), .B4(1'b0), .B5(1'b0), .S0(add6bit_0_s0[0]), .S1(add6bit_0_s0[1]),
    .S2(add6bit_0_s0[2]), .S3(add6bit_0_s0[3]), .S4(add6bit_0_s0[4]), .S5(add6bit_0_s0[5]));  // open: C_OUT
  Multiplexer_6bit Multiplexer_6bit_0 (
    .Umschalter({Load, and_1_out[0]}), .Eingang_0(add6bit_0_s0), .Eingang_1({6{1'b0}}),
    .Eingnag_2(Data_Sekunde_Load), .Ausgang_0(Multiplexer_6bit_0_ausgang_0));
  D_Flip_Flop d_ff_1 (
    .D(Multiplexer_6bit_0_ausgang_0[0]), .clk(Clock), .Q(Data_Sekunde_OUT[0]));  // open: Qn, preset, reset
  D_Flip_Flop d_ff_2 (
    .D(Multiplexer_6bit_0_ausgang_0[1]), .clk(Clock), .Q(Data_Sekunde_OUT[1]));  // open: Qn, preset, reset
  D_Flip_Flop d_ff_3 (
    .D(Multiplexer_6bit_0_ausgang_0[2]), .clk(Clock), .Q(Data_Sekunde_OUT[2]));  // open: Qn, preset, reset
  D_Flip_Flop d_ff_4 (
    .D(Multiplexer_6bit_0_ausgang_0[3]), .clk(Clock), .Q(Data_Sekunde_OUT[3]));  // open: Qn, preset, reset
  D_Flip_Flop d_ff_5 (
    .D(Multiplexer_6bit_0_ausgang_0[4]), .clk(Clock), .Q(Data_Sekunde_OUT[4]));  // open: Qn, preset, reset
  D_Flip_Flop d_ff_6 (
    .D(Multiplexer_6bit_0_ausgang_0[5]), .clk(Clock), .Q(Data_Sekunde_OUT[5]));  // open: Qn, preset, reset
  and and_2 (and_2_out, Data_Sekunde_OUT[0], Data_Sekunde_OUT[1], ~Data_Sekunde_OUT[2], Data_Sekunde_OUT[3], Data_Sekunde_OUT[4], Data_Sekunde_OUT[5]);  // AND_Gate
  and and_3 (and_3_out, and_2_out, ~Carry_Minute, Enable, ~Load);  // AND_Gate
  D_Flip_Flop d_ff_7 (.D(and_3_out), .clk(Clock), .Q(Carry_Minute));  // open: Qn, preset, reset
endmodule

module Storage_Counter_Minute_Data (
  input  Clock,
  input  Load,
  input  Enable,
  input  [5:0] Data_Minute_Load,
  output [5:0] Data_Minute_OUT,
  output Carry_Stunde
);

  wire and_2_out, and_3_out;
  wire [0:0] and_1_out;
  wire [5:0] add6bit_0_s0, Multiplexer_6bit_0_ausgang_0;

  and and_1 (and_1_out[0], ~Load, Enable, and_2_out);  // AND_Gate
  add6bit add6bit_0 (
    .Minus(1'b0), .C_IN(1'b0), .A0(Data_Minute_OUT[0]), .A1(Data_Minute_OUT[1]), .A2(Data_Minute_OUT[2]),
    .A3(Data_Minute_OUT[3]), .A4(Data_Minute_OUT[4]), .A5(Data_Minute_OUT[5]), .B0(Enable), .B1(1'b0),
    .B2(1'b0), .B3(1'b0), .B4(1'b0), .B5(1'b0), .S0(add6bit_0_s0[0]), .S1(add6bit_0_s0[1]),
    .S2(add6bit_0_s0[2]), .S3(add6bit_0_s0[3]), .S4(add6bit_0_s0[4]), .S5(add6bit_0_s0[5]));  // open: C_OUT
  Multiplexer_6bit Multiplexer_6bit_0 (
    .Umschalter({Load, and_1_out[0]}), .Eingang_0(add6bit_0_s0), .Eingang_1({6{1'b0}}),
    .Eingnag_2(Data_Minute_Load), .Ausgang_0(Multiplexer_6bit_0_ausgang_0));
  D_Flip_Flop d_ff_1 (
    .D(Multiplexer_6bit_0_ausgang_0[0]), .clk(Clock), .Q(Data_Minute_OUT[0]));  // open: Qn, preset, reset
  D_Flip_Flop d_ff_2 (
    .D(Multiplexer_6bit_0_ausgang_0[1]), .clk(Clock), .Q(Data_Minute_OUT[1]));  // open: Qn, preset, reset
  D_Flip_Flop d_ff_3 (
    .D(Multiplexer_6bit_0_ausgang_0[2]), .clk(Clock), .Q(Data_Minute_OUT[2]));  // open: Qn, preset, reset
  D_Flip_Flop d_ff_4 (
    .D(Multiplexer_6bit_0_ausgang_0[3]), .clk(Clock), .Q(Data_Minute_OUT[3]));  // open: Qn, preset, reset
  D_Flip_Flop d_ff_5 (
    .D(Multiplexer_6bit_0_ausgang_0[4]), .clk(Clock), .Q(Data_Minute_OUT[4]));  // open: Qn, preset, reset
  D_Flip_Flop d_ff_6 (
    .D(Multiplexer_6bit_0_ausgang_0[5]), .clk(Clock), .Q(Data_Minute_OUT[5]));  // open: Qn, preset, reset
  and and_2 (and_2_out, Data_Minute_OUT[0], Data_Minute_OUT[1], ~Data_Minute_OUT[2], Data_Minute_OUT[3], Data_Minute_OUT[4], Data_Minute_OUT[5]);  // AND_Gate
  and and_3 (and_3_out, and_2_out, ~Carry_Stunde, Enable, ~Load);  // AND_Gate
  D_Flip_Flop d_ff_7 (.D(and_3_out), .clk(Clock), .Q(Carry_Stunde));  // open: Qn, preset, reset
endmodule

module Storage_Counter_Stunde_Data (
  input  Clock,
  input  Load,
  input  Enable,
  input  [4:0] Data_Stunde_Load,
  output [4:0] Data_Stunde_IN,
  output Stunde_Carry
);

  wire and_2_out, and_3_out;
  wire [0:0] and_1_out;
  wire [4:0] add5bit_0_s0, Multiplexer_5bit_0_ausgang_0;

  and and_1 (and_1_out[0], ~Load, Enable, and_2_out);  // AND_Gate
  add5bit add5bit_0 (
    .Minus(1'b0), .C_IN(1'b0), .A0(Data_Stunde_IN[0]), .A1(Data_Stunde_IN[1]), .A2(Data_Stunde_IN[2]),
    .A3(Data_Stunde_IN[3]), .A4(Data_Stunde_IN[4]), .B0(Enable), .B1(1'b0), .B2(1'b0), .B3(1'b0), .B4(1'b0),
    .S0(add5bit_0_s0[0]), .S1(add5bit_0_s0[1]), .S2(add5bit_0_s0[2]), .S3(add5bit_0_s0[3]),
    .S4(add5bit_0_s0[4]));  // open: C_OUT
  Multiplexer_5bit Multiplexer_5bit_0 (
    .Umschalter({Load, and_1_out[0]}), .Eingang_0(add5bit_0_s0), .Eingang_1({5{1'b0}}),
    .Eingang_2(Data_Stunde_Load), .Ausgang_0(Multiplexer_5bit_0_ausgang_0));
  D_Flip_Flop d_ff_1 (
    .D(Multiplexer_5bit_0_ausgang_0[0]), .clk(Clock), .Q(Data_Stunde_IN[0]));  // open: Qn, preset, reset
  D_Flip_Flop d_ff_2 (
    .D(Multiplexer_5bit_0_ausgang_0[1]), .clk(Clock), .Q(Data_Stunde_IN[1]));  // open: Qn, preset, reset
  D_Flip_Flop d_ff_3 (
    .D(Multiplexer_5bit_0_ausgang_0[2]), .clk(Clock), .Q(Data_Stunde_IN[2]));  // open: Qn, preset, reset
  D_Flip_Flop d_ff_4 (
    .D(Multiplexer_5bit_0_ausgang_0[3]), .clk(Clock), .Q(Data_Stunde_IN[3]));  // open: Qn, preset, reset
  D_Flip_Flop d_ff_5 (
    .D(Multiplexer_5bit_0_ausgang_0[4]), .clk(Clock), .Q(Data_Stunde_IN[4]));  // open: Qn, preset, reset
  and and_2 (and_2_out, Data_Stunde_IN[0], Data_Stunde_IN[1], Data_Stunde_IN[2], ~Data_Stunde_IN[3], Data_Stunde_IN[4]);  // AND_Gate
  D_Flip_Flop d_ff_6 (.D(and_3_out), .clk(Clock), .Q(Stunde_Carry));  // open: Qn, preset, reset
  and and_3 (and_3_out, and_2_out, ~Stunde_Carry, Enable, ~Load);  // AND_Gate
endmodule

module Storage_Tag_Data (
  input  Clock,
  input  Load,
  input  [5:0] Data_Tag_IN,
  output [5:0] Data_Tag_OUT
);

  wire [5:0] Multiplexer_6bit_0_ausgang_0;

  Multiplexer_6bit Multiplexer_6bit_0 (
    .Umschalter({1'b0, Load}), .Eingang_0(Data_Tag_OUT), .Eingang_1(Data_Tag_IN), .Eingnag_2({6{1'b0}}),
    .Ausgang_0(Multiplexer_6bit_0_ausgang_0));
  D_Flip_Flop d_ff_1 (
    .D(Multiplexer_6bit_0_ausgang_0[0]), .clk(Clock), .Q(Data_Tag_OUT[0]));  // open: Qn, preset, reset
  D_Flip_Flop d_ff_2 (
    .D(Multiplexer_6bit_0_ausgang_0[1]), .clk(Clock), .Q(Data_Tag_OUT[1]));  // open: Qn, preset, reset
  D_Flip_Flop d_ff_3 (
    .D(Multiplexer_6bit_0_ausgang_0[2]), .clk(Clock), .Q(Data_Tag_OUT[2]));  // open: Qn, preset, reset
  D_Flip_Flop d_ff_4 (
    .D(Multiplexer_6bit_0_ausgang_0[3]), .clk(Clock), .Q(Data_Tag_OUT[3]));  // open: Qn, preset, reset
  D_Flip_Flop d_ff_5 (
    .D(Multiplexer_6bit_0_ausgang_0[4]), .clk(Clock), .Q(Data_Tag_OUT[4]));  // open: Qn, preset, reset
  D_Flip_Flop d_ff_6 (
    .D(Multiplexer_6bit_0_ausgang_0[5]), .clk(Clock), .Q(Data_Tag_OUT[5]));  // open: Qn, preset, reset
endmodule

module Storage_Wochentag_Data (
  input  Clock,
  input  Load,
  input  [2:0] Data_Wochentag_IN,
  output [2:0] Data_Wochentag_OUT
);

  wire [2:0] Multiplexer_0_ausgang_0;

  Multiplexer_3bit Multiplexer_0 (
    .Umschalter({1'b0, Load}), .Eingang_0(Data_Wochentag_OUT), .Eingang_1(Data_Wochentag_IN),
    .Eingang_2(3'b000), .Ausgang_0(Multiplexer_0_ausgang_0));
  D_Flip_Flop d_ff_1 (
    .D(Multiplexer_0_ausgang_0[0]), .clk(Clock), .Q(Data_Wochentag_OUT[0]));  // open: Qn, preset, reset
  D_Flip_Flop d_ff_2 (
    .D(Multiplexer_0_ausgang_0[1]), .clk(Clock), .Q(Data_Wochentag_OUT[1]));  // open: Qn, preset, reset
  D_Flip_Flop d_ff_3 (
    .D(Multiplexer_0_ausgang_0[2]), .clk(Clock), .Q(Data_Wochentag_OUT[2]));  // open: Qn, preset, reset
endmodule

module Storage_Monat_Data (
  input  Clock,
  input  Load,
  input  [4:0] Data_Monat_IN,
  output [4:0] Data_Monat_OUT
);

  wire [4:0] Multiplexer_5bit_0_ausgang_0;

  Multiplexer_5bit Multiplexer_5bit_0 (
    .Umschalter({1'b0, Load}), .Eingang_0(Data_Monat_OUT), .Eingang_1(Data_Monat_IN), .Eingang_2({5{1'b0}}),
    .Ausgang_0(Multiplexer_5bit_0_ausgang_0));
  D_Flip_Flop d_ff_1 (
    .D(Multiplexer_5bit_0_ausgang_0[0]), .clk(Clock), .Q(Data_Monat_OUT[0]));  // open: Qn, preset, reset
  D_Flip_Flop d_ff_2 (
    .D(Multiplexer_5bit_0_ausgang_0[1]), .clk(Clock), .Q(Data_Monat_OUT[1]));  // open: Qn, preset, reset
  D_Flip_Flop d_ff_3 (
    .D(Multiplexer_5bit_0_ausgang_0[2]), .clk(Clock), .Q(Data_Monat_OUT[2]));  // open: Qn, preset, reset
  D_Flip_Flop d_ff_4 (
    .D(Multiplexer_5bit_0_ausgang_0[3]), .clk(Clock), .Q(Data_Monat_OUT[3]));  // open: Qn, preset, reset
  D_Flip_Flop d_ff_5 (
    .D(Multiplexer_5bit_0_ausgang_0[4]), .clk(Clock), .Q(Data_Monat_OUT[4]));  // open: Qn, preset, reset
endmodule

module Storage_Jahr_Data (
  input  Clock,
  input  Load,
  input  [7:0] Data_Jahr_IN,
  output [7:0] Data_Jahr_OUT
);

  wire [7:0] Multiplexer_8bit_0_ausgang_0;

  Multiplexer_8bit Multiplexer_8bit_0 (
    .Umschalter({1'b0, Load}), .Eingang_0(Data_Jahr_OUT), .Eingang_1(Data_Jahr_IN), .Eingang_2({8{1'b0}}),
    .Ausgang_0(Multiplexer_8bit_0_ausgang_0));
  D_Flip_Flop d_ff_1 (
    .D(Multiplexer_8bit_0_ausgang_0[0]), .clk(Clock), .Q(Data_Jahr_OUT[0]));  // open: Qn, preset, reset
  D_Flip_Flop d_ff_2 (
    .D(Multiplexer_8bit_0_ausgang_0[1]), .clk(Clock), .Q(Data_Jahr_OUT[1]));  // open: Qn, preset, reset
  D_Flip_Flop d_ff_3 (
    .D(Multiplexer_8bit_0_ausgang_0[2]), .clk(Clock), .Q(Data_Jahr_OUT[2]));  // open: Qn, preset, reset
  D_Flip_Flop d_ff_4 (
    .D(Multiplexer_8bit_0_ausgang_0[3]), .clk(Clock), .Q(Data_Jahr_OUT[3]));  // open: Qn, preset, reset
  D_Flip_Flop d_ff_5 (
    .D(Multiplexer_8bit_0_ausgang_0[4]), .clk(Clock), .Q(Data_Jahr_OUT[4]));  // open: Qn, preset, reset
  D_Flip_Flop d_ff_6 (
    .D(Multiplexer_8bit_0_ausgang_0[5]), .clk(Clock), .Q(Data_Jahr_OUT[5]));  // open: Qn, preset, reset
  D_Flip_Flop d_ff_7 (
    .D(Multiplexer_8bit_0_ausgang_0[6]), .clk(Clock), .Q(Data_Jahr_OUT[6]));  // open: Qn, preset, reset
  D_Flip_Flop d_ff_8 (
    .D(Multiplexer_8bit_0_ausgang_0[7]), .clk(Clock), .Q(Data_Jahr_OUT[7]));  // open: Qn, preset, reset
endmodule

module SR_1bit (
  input  Clock,
  input  Enable,
  input  Data_Seriell_IN,
  output Data_Seriell_OUT
);

  wire Multiplexer_0_ausgang;

  Multiplexer_1bit Multiplexer_0 (
    .I_0(Data_Seriell_OUT), .I_1(Data_Seriell_IN), .I_2(1'b0), .Umschalter({1'b0, Enable}),
    .Ausgang(Multiplexer_0_ausgang));
  D_Flip_Flop d_ff_1 (.D(Multiplexer_0_ausgang), .clk(Clock), .Q(Data_Seriell_OUT));  // open: Qn, preset, reset
endmodule
module SR_3bit (
  input  Clock,
  input  Enable,
  input  Data_Seriell_IN,
  output [2:0] Data_Parallel_OUT,
  output Data_Seriell_OUT
);

  wire Multiplexer_0_ausgang, Multiplexer_1_ausgang, Multiplexer_2_ausgang;

  Multiplexer_1bit Multiplexer_0 (
    .I_0(Data_Parallel_OUT[0]), .I_1(Data_Seriell_IN), .I_2(1'b0), .Umschalter({1'b0, Enable}),
    .Ausgang(Multiplexer_0_ausgang));
  Multiplexer_1bit Multiplexer_1 (
    .I_0(Data_Parallel_OUT[1]), .I_1(Data_Parallel_OUT[0]), .I_2(1'b0), .Umschalter({1'b0, Enable}),
    .Ausgang(Multiplexer_1_ausgang));
  Multiplexer_1bit Multiplexer_2 (
    .I_0(Data_Parallel_OUT[2]), .I_1(Data_Parallel_OUT[1]), .I_2(1'b0), .Umschalter({1'b0, Enable}),
    .Ausgang(Multiplexer_2_ausgang));
  D_Flip_Flop d_ff_1 (.D(Multiplexer_0_ausgang), .clk(Clock), .Q(Data_Parallel_OUT[0]));  // open: Qn, preset, reset
  D_Flip_Flop d_ff_2 (.D(Multiplexer_1_ausgang), .clk(Clock), .Q(Data_Parallel_OUT[1]));  // open: Qn, preset, reset
  D_Flip_Flop d_ff_3 (.D(Multiplexer_2_ausgang), .clk(Clock), .Q(Data_Parallel_OUT[2]));  // open: Qn, preset, reset

  assign Data_Seriell_OUT = Data_Parallel_OUT[2];
endmodule

module SR_5bit (
  input  Clock,
  input  Enable,
  input  Data_Seriell_IN,
  output [4:0] Data_Parallel_OUT,
  output Data_Seriell_OUT
);

  wire Multiplexer_0_ausgang, Multiplexer_1_ausgang, Multiplexer_2_ausgang, Multiplexer_3_ausgang,
       Multiplexer_4_ausgang;

  Multiplexer_1bit Multiplexer_0 (
    .I_0(Data_Parallel_OUT[0]), .I_1(Data_Seriell_IN), .I_2(1'b0), .Umschalter({1'b0, Enable}),
    .Ausgang(Multiplexer_0_ausgang));
  Multiplexer_1bit Multiplexer_1 (
    .I_0(Data_Parallel_OUT[1]), .I_1(Data_Parallel_OUT[0]), .I_2(1'b0), .Umschalter({1'b0, Enable}),
    .Ausgang(Multiplexer_1_ausgang));
  Multiplexer_1bit Multiplexer_2 (
    .I_0(Data_Parallel_OUT[2]), .I_1(Data_Parallel_OUT[1]), .I_2(1'b0), .Umschalter({1'b0, Enable}),
    .Ausgang(Multiplexer_2_ausgang));
  Multiplexer_1bit Multiplexer_3 (
    .I_0(Data_Parallel_OUT[3]), .I_1(Data_Parallel_OUT[2]), .I_2(1'b0), .Umschalter({1'b0, Enable}),
    .Ausgang(Multiplexer_3_ausgang));
  Multiplexer_1bit Multiplexer_4 (
    .I_0(Data_Parallel_OUT[4]), .I_1(Data_Parallel_OUT[3]), .I_2(1'b0), .Umschalter({1'b0, Enable}),
    .Ausgang(Multiplexer_4_ausgang));
  D_Flip_Flop d_ff_1 (.D(Multiplexer_0_ausgang), .clk(Clock), .Q(Data_Parallel_OUT[0]));  // open: Qn, preset, reset
  D_Flip_Flop d_ff_2 (.D(Multiplexer_1_ausgang), .clk(Clock), .Q(Data_Parallel_OUT[1]));  // open: Qn, preset, reset
  D_Flip_Flop d_ff_3 (.D(Multiplexer_2_ausgang), .clk(Clock), .Q(Data_Parallel_OUT[2]));  // open: Qn, preset, reset
  D_Flip_Flop d_ff_4 (.D(Multiplexer_3_ausgang), .clk(Clock), .Q(Data_Parallel_OUT[3]));  // open: Qn, preset, reset
  D_Flip_Flop d_ff_5 (.D(Multiplexer_4_ausgang), .clk(Clock), .Q(Data_Parallel_OUT[4]));  // open: Qn, preset, reset

  assign Data_Seriell_OUT = Data_Parallel_OUT[4];
endmodule

module SR_6bit (
  input  Clock,
  input  Enable,
  input  Data_Seriell_IN,
  output [5:0] Data_Parallel_OUT,
  output Data_Seriell_OUT
);

  wire Multiplexer_0_ausgang, Multiplexer_1_ausgang, Multiplexer_2_ausgang, Multiplexer_3_ausgang,
       Multiplexer_4_ausgang, Multiplexer_5_ausgang;

  Multiplexer_1bit Multiplexer_0 (
    .I_0(Data_Parallel_OUT[0]), .I_1(Data_Seriell_IN), .I_2(1'b0), .Umschalter({1'b0, Enable}),
    .Ausgang(Multiplexer_0_ausgang));
  Multiplexer_1bit Multiplexer_1 (
    .I_0(Data_Parallel_OUT[1]), .I_1(Data_Parallel_OUT[0]), .I_2(1'b0), .Umschalter({1'b0, Enable}),
    .Ausgang(Multiplexer_1_ausgang));
  Multiplexer_1bit Multiplexer_2 (
    .I_0(Data_Parallel_OUT[2]), .I_1(Data_Parallel_OUT[1]), .I_2(1'b0), .Umschalter({1'b0, Enable}),
    .Ausgang(Multiplexer_2_ausgang));
  Multiplexer_1bit Multiplexer_3 (
    .I_0(Data_Parallel_OUT[3]), .I_1(Data_Parallel_OUT[2]), .I_2(1'b0), .Umschalter({1'b0, Enable}),
    .Ausgang(Multiplexer_3_ausgang));
  Multiplexer_1bit Multiplexer_4 (
    .I_0(Data_Parallel_OUT[4]), .I_1(Data_Parallel_OUT[3]), .I_2(1'b0), .Umschalter({1'b0, Enable}),
    .Ausgang(Multiplexer_4_ausgang));
  Multiplexer_1bit Multiplexer_5 (
    .I_0(Data_Parallel_OUT[5]), .I_1(Data_Parallel_OUT[4]), .I_2(1'b0), .Umschalter({1'b0, Enable}),
    .Ausgang(Multiplexer_5_ausgang));
  D_Flip_Flop d_ff_1 (.D(Multiplexer_0_ausgang), .clk(Clock), .Q(Data_Parallel_OUT[0]));  // open: Qn, preset, reset
  D_Flip_Flop d_ff_2 (.D(Multiplexer_1_ausgang), .clk(Clock), .Q(Data_Parallel_OUT[1]));  // open: Qn, preset, reset
  D_Flip_Flop d_ff_3 (.D(Multiplexer_2_ausgang), .clk(Clock), .Q(Data_Parallel_OUT[2]));  // open: Qn, preset, reset
  D_Flip_Flop d_ff_4 (.D(Multiplexer_3_ausgang), .clk(Clock), .Q(Data_Parallel_OUT[3]));  // open: Qn, preset, reset
  D_Flip_Flop d_ff_5 (.D(Multiplexer_4_ausgang), .clk(Clock), .Q(Data_Parallel_OUT[4]));  // open: Qn, preset, reset
  D_Flip_Flop d_ff_6 (.D(Multiplexer_5_ausgang), .clk(Clock), .Q(Data_Parallel_OUT[5]));  // open: Qn, preset, reset

  assign Data_Seriell_OUT = Data_Parallel_OUT[5];
endmodule

module SR_7bit (
  input  Clock,
  input  Enable,
  input  Data_Seriell_IN,
  output [6:0] Data_Parallel_OUT,
  output Data_Seriell_OUT
);

  wire Multiplexer_0_ausgang, Multiplexer_1_ausgang, Multiplexer_2_ausgang, Multiplexer_3_ausgang,
       Multiplexer_4_ausgang, Multiplexer_5_ausgang, Multiplexer_6_ausgang;

  Multiplexer_1bit Multiplexer_0 (
    .I_0(Data_Parallel_OUT[0]), .I_1(Data_Seriell_IN), .I_2(1'b0), .Umschalter({1'b0, Enable}),
    .Ausgang(Multiplexer_0_ausgang));
  Multiplexer_1bit Multiplexer_1 (
    .I_0(Data_Parallel_OUT[1]), .I_1(Data_Parallel_OUT[0]), .I_2(1'b0), .Umschalter({1'b0, Enable}),
    .Ausgang(Multiplexer_1_ausgang));
  Multiplexer_1bit Multiplexer_2 (
    .I_0(Data_Parallel_OUT[2]), .I_1(Data_Parallel_OUT[1]), .I_2(1'b0), .Umschalter({1'b0, Enable}),
    .Ausgang(Multiplexer_2_ausgang));
  Multiplexer_1bit Multiplexer_3 (
    .I_0(Data_Parallel_OUT[3]), .I_1(Data_Parallel_OUT[2]), .I_2(1'b0), .Umschalter({1'b0, Enable}),
    .Ausgang(Multiplexer_3_ausgang));
  Multiplexer_1bit Multiplexer_4 (
    .I_0(Data_Parallel_OUT[4]), .I_1(Data_Parallel_OUT[3]), .I_2(1'b0), .Umschalter({1'b0, Enable}),
    .Ausgang(Multiplexer_4_ausgang));
  Multiplexer_1bit Multiplexer_5 (
    .I_0(Data_Parallel_OUT[5]), .I_1(Data_Parallel_OUT[4]), .I_2(1'b0), .Umschalter({1'b0, Enable}),
    .Ausgang(Multiplexer_5_ausgang));
  Multiplexer_1bit Multiplexer_6 (
    .I_0(Data_Parallel_OUT[6]), .I_1(Data_Parallel_OUT[5]), .I_2(1'b0), .Umschalter({1'b0, Enable}),
    .Ausgang(Multiplexer_6_ausgang));
  D_Flip_Flop d_ff_1 (.D(Multiplexer_0_ausgang), .clk(Clock), .Q(Data_Parallel_OUT[0]));  // open: Qn, preset, reset
  D_Flip_Flop d_ff_2 (.D(Multiplexer_1_ausgang), .clk(Clock), .Q(Data_Parallel_OUT[1]));  // open: Qn, preset, reset
  D_Flip_Flop d_ff_3 (.D(Multiplexer_2_ausgang), .clk(Clock), .Q(Data_Parallel_OUT[2]));  // open: Qn, preset, reset
  D_Flip_Flop d_ff_4 (.D(Multiplexer_3_ausgang), .clk(Clock), .Q(Data_Parallel_OUT[3]));  // open: Qn, preset, reset
  D_Flip_Flop d_ff_5 (.D(Multiplexer_4_ausgang), .clk(Clock), .Q(Data_Parallel_OUT[4]));  // open: Qn, preset, reset
  D_Flip_Flop d_ff_6 (.D(Multiplexer_5_ausgang), .clk(Clock), .Q(Data_Parallel_OUT[5]));  // open: Qn, preset, reset
  D_Flip_Flop d_ff_7 (.D(Multiplexer_6_ausgang), .clk(Clock), .Q(Data_Parallel_OUT[6]));  // open: Qn, preset, reset

  assign Data_Seriell_OUT = Data_Parallel_OUT[6];
endmodule

module SR_8bit (
  input  Clock,
  input  Enable,
  input  Data_Seriell_IN,
  output [7:0] Data_Parallel_OUT,
  output Data_Seriell_OUT
);

  wire Multiplexer_0_ausgang, Multiplexer_1_ausgang, Multiplexer_2_ausgang, Multiplexer_3_ausgang,
       Multiplexer_4_ausgang, Multiplexer_5_ausgang, Multiplexer_6_ausgang, Multiplexer_7_ausgang;

  Multiplexer_1bit Multiplexer_0 (
    .I_0(Data_Parallel_OUT[0]), .I_1(Data_Seriell_IN), .I_2(1'b0), .Umschalter({1'b0, Enable}),
    .Ausgang(Multiplexer_0_ausgang));
  Multiplexer_1bit Multiplexer_1 (
    .I_0(Data_Parallel_OUT[1]), .I_1(Data_Parallel_OUT[0]), .I_2(1'b0), .Umschalter({1'b0, Enable}),
    .Ausgang(Multiplexer_1_ausgang));
  Multiplexer_1bit Multiplexer_2 (
    .I_0(Data_Parallel_OUT[2]), .I_1(Data_Parallel_OUT[1]), .I_2(1'b0), .Umschalter({1'b0, Enable}),
    .Ausgang(Multiplexer_2_ausgang));
  Multiplexer_1bit Multiplexer_3 (
    .I_0(Data_Parallel_OUT[3]), .I_1(Data_Parallel_OUT[2]), .I_2(1'b0), .Umschalter({1'b0, Enable}),
    .Ausgang(Multiplexer_3_ausgang));
  Multiplexer_1bit Multiplexer_4 (
    .I_0(Data_Parallel_OUT[4]), .I_1(Data_Parallel_OUT[3]), .I_2(1'b0), .Umschalter({1'b0, Enable}),
    .Ausgang(Multiplexer_4_ausgang));
  Multiplexer_1bit Multiplexer_5 (
    .I_0(Data_Parallel_OUT[5]), .I_1(Data_Parallel_OUT[4]), .I_2(1'b0), .Umschalter({1'b0, Enable}),
    .Ausgang(Multiplexer_5_ausgang));
  Multiplexer_1bit Multiplexer_6 (
    .I_0(Data_Parallel_OUT[6]), .I_1(Data_Parallel_OUT[5]), .I_2(1'b0), .Umschalter({1'b0, Enable}),
    .Ausgang(Multiplexer_6_ausgang));
  Multiplexer_1bit Multiplexer_7 (
    .I_0(Data_Parallel_OUT[7]), .I_1(Data_Parallel_OUT[6]), .I_2(1'b0), .Umschalter({1'b0, Enable}),
    .Ausgang(Multiplexer_7_ausgang));
  D_Flip_Flop d_ff_1 (.D(Multiplexer_0_ausgang), .clk(Clock), .Q(Data_Parallel_OUT[0]));  // open: Qn, preset, reset
  D_Flip_Flop d_ff_2 (.D(Multiplexer_1_ausgang), .clk(Clock), .Q(Data_Parallel_OUT[1]));  // open: Qn, preset, reset
  D_Flip_Flop d_ff_3 (.D(Multiplexer_2_ausgang), .clk(Clock), .Q(Data_Parallel_OUT[2]));  // open: Qn, preset, reset
  D_Flip_Flop d_ff_4 (.D(Multiplexer_3_ausgang), .clk(Clock), .Q(Data_Parallel_OUT[3]));  // open: Qn, preset, reset
  D_Flip_Flop d_ff_5 (.D(Multiplexer_4_ausgang), .clk(Clock), .Q(Data_Parallel_OUT[4]));  // open: Qn, preset, reset
  D_Flip_Flop d_ff_6 (.D(Multiplexer_5_ausgang), .clk(Clock), .Q(Data_Parallel_OUT[5]));  // open: Qn, preset, reset
  D_Flip_Flop d_ff_7 (.D(Multiplexer_6_ausgang), .clk(Clock), .Q(Data_Parallel_OUT[6]));  // open: Qn, preset, reset
  D_Flip_Flop d_ff_8 (.D(Multiplexer_7_ausgang), .clk(Clock), .Q(Data_Parallel_OUT[7]));  // open: Qn, preset, reset

  assign Data_Seriell_OUT = Data_Parallel_OUT[7];
endmodule

module SR_14bit (
  input  Clock,
  input  Enable,
  input  Data_Seriell_IN,
  output [13:0] Data_Parallel_OUT,
  output Data_Seriell_OUT
);

  wire Multiplexer_0_ausgang, Multiplexer_1_ausgang, Multiplexer_2_ausgang, Multiplexer_3_ausgang,
       Multiplexer_4_ausgang, Multiplexer_5_ausgang, Multiplexer_6_ausgang, Multiplexer_7_ausgang,
       Multiplexer_8_ausgang, Multiplexer_9_ausgang, Multiplexer_10_ausgang, Multiplexer_11_ausgang,
       Multiplexer_12_ausgang, Multiplexer_13_ausgang;

  Multiplexer_1bit Multiplexer_10 (
    .I_0(Data_Parallel_OUT[10]), .I_1(Data_Parallel_OUT[9]), .I_2(1'b0), .Umschalter({1'b0, Enable}),
    .Ausgang(Multiplexer_10_ausgang));
  Multiplexer_1bit Multiplexer_11 (
    .I_0(Data_Parallel_OUT[11]), .I_1(Data_Parallel_OUT[10]), .I_2(1'b0), .Umschalter({1'b0, Enable}),
    .Ausgang(Multiplexer_11_ausgang));
  Multiplexer_1bit Multiplexer_12 (
    .I_0(Data_Parallel_OUT[12]), .I_1(Data_Parallel_OUT[11]), .I_2(1'b0), .Umschalter({1'b0, Enable}),
    .Ausgang(Multiplexer_12_ausgang));
  Multiplexer_1bit Multiplexer_13 (
    .I_0(Data_Parallel_OUT[13]), .I_1(Data_Parallel_OUT[12]), .I_2(1'b0), .Umschalter({1'b0, Enable}),
    .Ausgang(Multiplexer_13_ausgang));
  Multiplexer_1bit Multiplexer_0 (
    .I_0(Data_Parallel_OUT[0]), .I_1(Data_Seriell_IN), .I_2(1'b0), .Umschalter({1'b0, Enable}),
    .Ausgang(Multiplexer_0_ausgang));
  Multiplexer_1bit Multiplexer_1 (
    .I_0(Data_Parallel_OUT[1]), .I_1(Data_Parallel_OUT[0]), .I_2(1'b0), .Umschalter({1'b0, Enable}),
    .Ausgang(Multiplexer_1_ausgang));
  Multiplexer_1bit Multiplexer_2 (
    .I_0(Data_Parallel_OUT[2]), .I_1(Data_Parallel_OUT[1]), .I_2(1'b0), .Umschalter({1'b0, Enable}),
    .Ausgang(Multiplexer_2_ausgang));
  Multiplexer_1bit Multiplexer_3 (
    .I_0(Data_Parallel_OUT[3]), .I_1(Data_Parallel_OUT[2]), .I_2(1'b0), .Umschalter({1'b0, Enable}),
    .Ausgang(Multiplexer_3_ausgang));
  Multiplexer_1bit Multiplexer_4 (
    .I_0(Data_Parallel_OUT[4]), .I_1(Data_Parallel_OUT[3]), .I_2(1'b0), .Umschalter({1'b0, Enable}),
    .Ausgang(Multiplexer_4_ausgang));
  Multiplexer_1bit Multiplexer_5 (
    .I_0(Data_Parallel_OUT[5]), .I_1(Data_Parallel_OUT[4]), .I_2(1'b0), .Umschalter({1'b0, Enable}),
    .Ausgang(Multiplexer_5_ausgang));
  Multiplexer_1bit Multiplexer_6 (
    .I_0(Data_Parallel_OUT[6]), .I_1(Data_Parallel_OUT[5]), .I_2(1'b0), .Umschalter({1'b0, Enable}),
    .Ausgang(Multiplexer_6_ausgang));
  Multiplexer_1bit Multiplexer_7 (
    .I_0(Data_Parallel_OUT[7]), .I_1(Data_Parallel_OUT[6]), .I_2(1'b0), .Umschalter({1'b0, Enable}),
    .Ausgang(Multiplexer_7_ausgang));
  Multiplexer_1bit Multiplexer_8 (
    .I_0(Data_Parallel_OUT[8]), .I_1(Data_Parallel_OUT[7]), .I_2(1'b0), .Umschalter({1'b0, Enable}),
    .Ausgang(Multiplexer_8_ausgang));
  Multiplexer_1bit Multiplexer_9 (
    .I_0(Data_Parallel_OUT[9]), .I_1(Data_Parallel_OUT[8]), .I_2(1'b0), .Umschalter({1'b0, Enable}),
    .Ausgang(Multiplexer_9_ausgang));
  D_Flip_Flop d_ff_1 (.D(Multiplexer_10_ausgang), .clk(Clock), .Q(Data_Parallel_OUT[10]));  // open: Qn, preset, reset
  D_Flip_Flop d_ff_2 (.D(Multiplexer_11_ausgang), .clk(Clock), .Q(Data_Parallel_OUT[11]));  // open: Qn, preset, reset
  D_Flip_Flop d_ff_3 (.D(Multiplexer_12_ausgang), .clk(Clock), .Q(Data_Parallel_OUT[12]));  // open: Qn, preset, reset
  D_Flip_Flop d_ff_4 (.D(Multiplexer_13_ausgang), .clk(Clock), .Q(Data_Parallel_OUT[13]));  // open: Qn, preset, reset
  D_Flip_Flop d_ff_5 (.D(Multiplexer_0_ausgang), .clk(Clock), .Q(Data_Parallel_OUT[0]));  // open: Qn, preset, reset
  D_Flip_Flop d_ff_6 (.D(Multiplexer_1_ausgang), .clk(Clock), .Q(Data_Parallel_OUT[1]));  // open: Qn, preset, reset
  D_Flip_Flop d_ff_7 (.D(Multiplexer_2_ausgang), .clk(Clock), .Q(Data_Parallel_OUT[2]));  // open: Qn, preset, reset
  D_Flip_Flop d_ff_8 (.D(Multiplexer_3_ausgang), .clk(Clock), .Q(Data_Parallel_OUT[3]));  // open: Qn, preset, reset
  D_Flip_Flop d_ff_9 (.D(Multiplexer_4_ausgang), .clk(Clock), .Q(Data_Parallel_OUT[4]));  // open: Qn, preset, reset
  D_Flip_Flop d_ff_10 (.D(Multiplexer_5_ausgang), .clk(Clock), .Q(Data_Parallel_OUT[5]));  // open: Qn, preset, reset
  D_Flip_Flop d_ff_11 (.D(Multiplexer_6_ausgang), .clk(Clock), .Q(Data_Parallel_OUT[6]));  // open: Qn, preset, reset
  D_Flip_Flop d_ff_12 (.D(Multiplexer_7_ausgang), .clk(Clock), .Q(Data_Parallel_OUT[7]));  // open: Qn, preset, reset
  D_Flip_Flop d_ff_13 (.D(Multiplexer_8_ausgang), .clk(Clock), .Q(Data_Parallel_OUT[8]));  // open: Qn, preset, reset
  D_Flip_Flop d_ff_14 (.D(Multiplexer_9_ausgang), .clk(Clock), .Q(Data_Parallel_OUT[9]));  // open: Qn, preset, reset

  assign Data_Seriell_OUT = Data_Parallel_OUT[13];
endmodule

module Counter_6bit (
  input  Clock,
  input  Reset,
  input  Load,
  input  Enable,
  input  [5:0] Data_Load,
  output [5:0] Counter_Ausgang,
  output [5:0] Counter_Ausgang_negiert
);

  wire [5:0] add6bit_0_s0, Multiplexer_6bit_0_ausgang_0;

  add6bit add6bit_0 (
    .Minus(1'b0), .C_IN(1'b0), .A0(Counter_Ausgang[0]), .A1(Counter_Ausgang[1]), .A2(Counter_Ausgang[2]),
    .A3(Counter_Ausgang[3]), .A4(Counter_Ausgang[4]), .A5(Counter_Ausgang[5]), .B0(Enable), .B1(1'b0),
    .B2(1'b0), .B3(1'b0), .B4(1'b0), .B5(1'b0), .S0(add6bit_0_s0[0]), .S1(add6bit_0_s0[1]),
    .S2(add6bit_0_s0[2]), .S3(add6bit_0_s0[3]), .S4(add6bit_0_s0[4]), .S5(add6bit_0_s0[5]));  // open: C_OUT
  Multiplexer_6bit Multiplexer_6bit_0 (
    .Umschalter({Load, Reset}), .Eingang_0(add6bit_0_s0), .Eingang_1({6{1'b0}}), .Eingnag_2(Data_Load),
    .Ausgang_0(Multiplexer_6bit_0_ausgang_0));
  D_Flip_Flop d_ff_1 (
    .D(Multiplexer_6bit_0_ausgang_0[0]), .clk(Clock), .Q(Counter_Ausgang[0]), .Qn(Counter_Ausgang_negiert[0]));  // open: preset, reset
  D_Flip_Flop d_ff_2 (
    .D(Multiplexer_6bit_0_ausgang_0[1]), .clk(Clock), .Q(Counter_Ausgang[1]), .Qn(Counter_Ausgang_negiert[1]));  // open: preset, reset
  D_Flip_Flop d_ff_3 (
    .D(Multiplexer_6bit_0_ausgang_0[2]), .clk(Clock), .Q(Counter_Ausgang[2]), .Qn(Counter_Ausgang_negiert[2]));  // open: preset, reset
  D_Flip_Flop d_ff_4 (
    .D(Multiplexer_6bit_0_ausgang_0[3]), .clk(Clock), .Q(Counter_Ausgang[3]), .Qn(Counter_Ausgang_negiert[3]));  // open: preset, reset
  D_Flip_Flop d_ff_5 (
    .D(Multiplexer_6bit_0_ausgang_0[4]), .clk(Clock), .Q(Counter_Ausgang[4]), .Qn(Counter_Ausgang_negiert[4]));  // open: preset, reset
  D_Flip_Flop d_ff_6 (
    .D(Multiplexer_6bit_0_ausgang_0[5]), .clk(Clock), .Q(Counter_Ausgang[5]), .Qn(Counter_Ausgang_negiert[5]));  // open: preset, reset
endmodule

module Multiplexer_6bit (
  input  [1:0] Umschalter,
  input  [5:0] Eingang_0,
  input  [5:0] Eingang_1,
  input  [5:0] Eingnag_2,
  output [5:0] Ausgang_0
);

  Multiplexer_1bit Multiplexer_1bit_0 (
    .I_0(Eingang_0[0]), .I_1(Eingang_1[0]), .I_2(Eingnag_2[0]), .Umschalter(Umschalter),
    .Ausgang(Ausgang_0[0]));
  Multiplexer_1bit Multiplexer_1bit_1 (
    .I_0(Eingang_0[1]), .I_1(Eingang_1[1]), .I_2(Eingnag_2[1]), .Umschalter(Umschalter),
    .Ausgang(Ausgang_0[1]));
  Multiplexer_1bit Multiplexer_1bit_2 (
    .I_0(Eingang_0[2]), .I_1(Eingang_1[2]), .I_2(Eingnag_2[2]), .Umschalter(Umschalter),
    .Ausgang(Ausgang_0[2]));
  Multiplexer_1bit Multiplexer_1bit_3 (
    .I_0(Eingang_0[3]), .I_1(Eingang_1[3]), .I_2(Eingnag_2[3]), .Umschalter(Umschalter),
    .Ausgang(Ausgang_0[3]));
  Multiplexer_1bit Multiplexer_1bit_4 (
    .I_0(Eingang_0[4]), .I_1(Eingang_1[4]), .I_2(Eingnag_2[4]), .Umschalter(Umschalter),
    .Ausgang(Ausgang_0[4]));
  Multiplexer_1bit Multiplexer_1bit_5 (
    .I_0(Eingang_0[5]), .I_1(Eingang_1[5]), .I_2(Eingnag_2[5]), .Umschalter(Umschalter),
    .Ausgang(Ausgang_0[5]));
endmodule

module Counter_5bit (
  input  Clock,
  input  Reset,
  input  Load,
  input  Enable,
  input  [4:0] Data_Load,
  output [4:0] Counter_Ausgang,
  output [4:0] Counter_Ausgang_negiert
);

  wire [4:0] add5bit_0_s0, Multiplexer_5bit_0_ausgang_0;

  add5bit add5bit_0 (
    .Minus(1'b0), .C_IN(1'b0), .A0(Counter_Ausgang[0]), .A1(Counter_Ausgang[1]), .A2(Counter_Ausgang[2]),
    .A3(Counter_Ausgang[3]), .A4(Counter_Ausgang[4]), .B0(Enable), .B1(1'b0), .B2(1'b0), .B3(1'b0),
    .B4(1'b0), .S0(add5bit_0_s0[0]), .S1(add5bit_0_s0[1]), .S2(add5bit_0_s0[2]), .S3(add5bit_0_s0[3]),
    .S4(add5bit_0_s0[4]));  // open: C_OUT
  Multiplexer_5bit Multiplexer_5bit_0 (
    .Umschalter({Load, Reset}), .Eingang_0(add5bit_0_s0), .Eingang_1({5{1'b0}}), .Eingang_2(Data_Load),
    .Ausgang_0(Multiplexer_5bit_0_ausgang_0));
  D_Flip_Flop d_ff_1 (
    .D(Multiplexer_5bit_0_ausgang_0[0]), .clk(Clock), .Q(Counter_Ausgang[0]), .Qn(Counter_Ausgang_negiert[0]));  // open: preset, reset
  D_Flip_Flop d_ff_2 (
    .D(Multiplexer_5bit_0_ausgang_0[1]), .clk(Clock), .Q(Counter_Ausgang[1]), .Qn(Counter_Ausgang_negiert[1]));  // open: preset, reset
  D_Flip_Flop d_ff_3 (
    .D(Multiplexer_5bit_0_ausgang_0[2]), .clk(Clock), .Q(Counter_Ausgang[2]), .Qn(Counter_Ausgang_negiert[2]));  // open: preset, reset
  D_Flip_Flop d_ff_4 (
    .D(Multiplexer_5bit_0_ausgang_0[3]), .clk(Clock), .Q(Counter_Ausgang[3]), .Qn(Counter_Ausgang_negiert[3]));  // open: preset, reset
  D_Flip_Flop d_ff_5 (
    .D(Multiplexer_5bit_0_ausgang_0[4]), .clk(Clock), .Q(Counter_Ausgang[4]), .Qn(Counter_Ausgang_negiert[4]));  // open: preset, reset
endmodule

module Multiplexer_5bit (
  input  [1:0] Umschalter,
  input  [4:0] Eingang_0,
  input  [4:0] Eingang_1,
  input  [4:0] Eingang_2,
  output [4:0] Ausgang_0
);

  Multiplexer_1bit Multiplexer_0 (
    .I_0(Eingang_0[0]), .I_1(Eingang_1[0]), .I_2(Eingang_2[0]), .Umschalter(Umschalter),
    .Ausgang(Ausgang_0[0]));
  Multiplexer_1bit Multiplexer_1 (
    .I_0(Eingang_0[1]), .I_1(Eingang_1[1]), .I_2(Eingang_2[1]), .Umschalter(Umschalter),
    .Ausgang(Ausgang_0[1]));
  Multiplexer_1bit Multiplexer_2 (
    .I_0(Eingang_0[2]), .I_1(Eingang_1[2]), .I_2(Eingang_2[2]), .Umschalter(Umschalter),
    .Ausgang(Ausgang_0[2]));
  Multiplexer_1bit Multiplexer_3 (
    .I_0(Eingang_0[3]), .I_1(Eingang_1[3]), .I_2(Eingang_2[3]), .Umschalter(Umschalter),
    .Ausgang(Ausgang_0[3]));
  Multiplexer_1bit Multiplexer_4 (
    .I_0(Eingang_0[4]), .I_1(Eingang_1[4]), .I_2(Eingang_2[4]), .Umschalter(Umschalter),
    .Ausgang(Ausgang_0[4]));
endmodule

module Multiplexer_7bit (
  input  [1:0] Umschalter,
  input  [6:0] Eingang_0,
  input  [6:0] Eingang_1,
  input  [6:0] Eingang_2,
  output [6:0] Ausgang_0
);

  Multiplexer_1bit Multiplexer_0 (
    .I_0(Eingang_0[0]), .I_1(Eingang_1[0]), .I_2(Eingang_2[0]), .Umschalter(Umschalter),
    .Ausgang(Ausgang_0[0]));
  Multiplexer_1bit Multiplexer_1 (
    .I_0(Eingang_0[1]), .I_1(Eingang_1[1]), .I_2(Eingang_2[1]), .Umschalter(Umschalter),
    .Ausgang(Ausgang_0[1]));
  Multiplexer_1bit Multiplexer_2 (
    .I_0(Eingang_0[2]), .I_1(Eingang_1[2]), .I_2(Eingang_2[2]), .Umschalter(Umschalter),
    .Ausgang(Ausgang_0[2]));
  Multiplexer_1bit Multiplexer_3 (
    .I_0(Eingang_0[3]), .I_1(Eingang_1[3]), .I_2(Eingang_2[3]), .Umschalter(Umschalter),
    .Ausgang(Ausgang_0[3]));
  Multiplexer_1bit Multiplexer_4 (
    .I_0(Eingang_0[4]), .I_1(Eingang_1[4]), .I_2(Eingang_2[4]), .Umschalter(Umschalter),
    .Ausgang(Ausgang_0[4]));
  Multiplexer_1bit Multiplexer_5 (
    .I_0(Eingang_0[5]), .I_1(Eingang_1[5]), .I_2(Eingang_2[5]), .Umschalter(Umschalter),
    .Ausgang(Ausgang_0[5]));
  Multiplexer_1bit Multiplexer_6 (
    .I_0(Eingang_0[6]), .I_1(Eingang_1[6]), .I_2(Eingang_2[6]), .Umschalter(Umschalter),
    .Ausgang(Ausgang_0[6]));
endmodule

module Multiplexer_8bit (
  input  [1:0] Umschalter,
  input  [7:0] Eingang_0,
  input  [7:0] Eingang_1,
  input  [7:0] Eingang_2,
  output [7:0] Ausgang_0
);

  Multiplexer_1bit Multiplexer_0 (
    .I_0(Eingang_0[0]), .I_1(Eingang_1[0]), .I_2(Eingang_2[0]), .Umschalter(Umschalter),
    .Ausgang(Ausgang_0[0]));
  Multiplexer_1bit Multiplexer_1 (
    .I_0(Eingang_0[1]), .I_1(Eingang_1[1]), .I_2(Eingang_2[1]), .Umschalter(Umschalter),
    .Ausgang(Ausgang_0[1]));
  Multiplexer_1bit Multiplexer_2 (
    .I_0(Eingang_0[2]), .I_1(Eingang_1[2]), .I_2(Eingang_2[2]), .Umschalter(Umschalter),
    .Ausgang(Ausgang_0[2]));
  Multiplexer_1bit Multiplexer_3 (
    .I_0(Eingang_0[3]), .I_1(Eingang_1[3]), .I_2(Eingang_2[3]), .Umschalter(Umschalter),
    .Ausgang(Ausgang_0[3]));
  Multiplexer_1bit Multiplexer_4 (
    .I_0(Eingang_0[4]), .I_1(Eingang_1[4]), .I_2(Eingang_2[4]), .Umschalter(Umschalter),
    .Ausgang(Ausgang_0[4]));
  Multiplexer_1bit Multiplexer_5 (
    .I_0(Eingang_0[5]), .I_1(Eingang_1[5]), .I_2(Eingang_2[5]), .Umschalter(Umschalter),
    .Ausgang(Ausgang_0[5]));
  Multiplexer_1bit Multiplexer_6 (
    .I_0(Eingang_0[6]), .I_1(Eingang_1[6]), .I_2(Eingang_2[6]), .Umschalter(Umschalter),
    .Ausgang(Ausgang_0[6]));
  Multiplexer_1bit Multiplexer_7 (
    .I_0(Eingang_0[7]), .I_1(Eingang_1[7]), .I_2(Eingang_2[7]), .Umschalter(Umschalter),
    .Ausgang(Ausgang_0[7]));
endmodule

module Multiplexer_3bit (
  input  [1:0] Umschalter,
  input  [2:0] Eingang_0,
  input  [2:0] Eingang_1,
  input  [2:0] Eingang_2,
  output [2:0] Ausgang_0
);

  Multiplexer_1bit Multiplexer_0 (
    .I_0(Eingang_0[0]), .I_1(Eingang_1[0]), .I_2(Eingang_2[0]), .Umschalter(Umschalter),
    .Ausgang(Ausgang_0[0]));
  Multiplexer_1bit Multiplexer_1 (
    .I_0(Eingang_0[1]), .I_1(Eingang_1[1]), .I_2(Eingang_2[1]), .Umschalter(Umschalter),
    .Ausgang(Ausgang_0[1]));
  Multiplexer_1bit Multiplexer_2 (
    .I_0(Eingang_0[2]), .I_1(Eingang_1[2]), .I_2(Eingang_2[2]), .Umschalter(Umschalter),
    .Ausgang(Ausgang_0[2]));
endmodule

module Synchroerkenner (
  input  Clock,
  input  sekunde_extern,
  input  sekunde_intern,
  output sync,
  output offline
);

  wire and_1_out, and_2_out, and_3_out, and_4_out, and_5_out, d_ff_3_q, or_1_out;
  wire [1:0] Counter_2bit_0_ausgang_counter;

  and and_1 (and_1_out, ~Counter_2bit_0_ausgang_counter[0], Counter_2bit_0_ausgang_counter[1]);  // AND_Gate
  and and_2 (and_2_out, and_1_out, sekunde_extern);
  and and_3 (and_3_out, and_1_out, ~sekunde_extern, sekunde_intern);  // AND_Gate
  and and_4 (and_4_out, ~sekunde_extern, offline);  // AND_Gate
  or or_1 (or_1_out, and_3_out, and_4_out);
  and and_5 (and_5_out, ~sekunde_extern, ~offline, ~d_ff_3_q, sekunde_intern);  // AND_Gate
  D_Flip_Flop d_ff_1 (.D(and_2_out), .clk(Clock), .Q(sync));  // open: Qn, preset, reset
  D_Flip_Flop d_ff_2 (.D(or_1_out), .clk(Clock), .Q(offline));  // open: Qn, preset, reset
  D_Flip_Flop d_ff_3 (.D(and_5_out), .clk(Clock), .Q(d_ff_3_q));  // open: Qn, preset, reset
  Counter_2bit Counter_2bit_0 (
    .Clock(Clock), .Enable(d_ff_3_q), .Reset(sekunde_extern), .Ausgang_Counter(Counter_2bit_0_ausgang_counter));  // open: Ausgang_Counter_negiert
endmodule

module Test (
  input  Antenna_IN
);

  wire block_1_c_out, block_2_c_out, Block_3_c_out, clock_1_out, not_1_out;
  wire [7:0] block_0_signalbreite;

  Clock clock_1 (.out(clock_1_out));
  Signalbreite_Zusammenzaehlen block_0 (
    .Clock_2kHz(clock_1_out), .Data_Seriell(Antenna_IN), .Signalbreite(block_0_signalbreite));
  LED LED_Antenna (.in(Antenna_IN));
  not not_1 (not_1_out, 1'b0);
  add8bit block_1 (
    .Minus(not_1_out), .C_IN(1'b0), .A0(1'b1), .A1(1'b1), .A2(1'b0), .A3(1'b1), .A4(1'b0), .A5(1'b0),
    .A6(1'b1), .A7(1'b0), .B0(block_0_signalbreite[0]), .B1(block_0_signalbreite[1]),
    .B2(block_0_signalbreite[2]), .B3(block_0_signalbreite[3]), .B4(block_0_signalbreite[4]),
    .B5(block_0_signalbreite[5]), .B6(block_0_signalbreite[6]), .B7(block_0_signalbreite[7]),
    .C_OUT(block_1_c_out));  // open: S0, S1, S2, S3, S4, S5, S6, S7
  add8bit block_2 (
    .Minus(not_1_out), .C_IN(1'b0), .A0(1'b0), .A1(1'b0), .A2(1'b0), .A3(1'b0), .A4(1'b0), .A5(1'b1),
    .A6(1'b0), .A7(1'b1), .B0(block_0_signalbreite[0]), .B1(block_0_signalbreite[1]),
    .B2(block_0_signalbreite[2]), .B3(block_0_signalbreite[3]), .B4(block_0_signalbreite[4]),
    .B5(block_0_signalbreite[5]), .B6(block_0_signalbreite[6]), .B7(block_0_signalbreite[7]),
    .C_OUT(block_2_c_out));  // open: S0, S1, S2, S3, S4, S5, S6, S7
  add8bit Block_3 (
    .Minus(not_1_out), .C_IN(1'b0), .A0(block_0_signalbreite[0]), .A1(block_0_signalbreite[1]),
    .A2(block_0_signalbreite[2]), .A3(block_0_signalbreite[3]), .A4(block_0_signalbreite[4]),
    .A5(block_0_signalbreite[5]), .A6(block_0_signalbreite[6]), .A7(block_0_signalbreite[7]), .B0(1'b0),
    .B1(1'b1), .B2(1'b0), .B3(1'b0), .B4(1'b1), .B5(1'b1), .B6(1'b0), .B7(1'b0), .C_OUT(Block_3_c_out));  // open: S0, S1, S2, S3, S4, S5, S6, S7
  LED LED_0 (.in(block_1_c_out));
  LED LED_1 (.in(block_2_c_out));
  LED LED_2 (.in(Block_3_c_out));
endmodule

module Testing_2 (
  input  Antenna_IN
);

  wire and_1_out, bcd2seg7_0_seg_a, bcd2seg7_0_seg_b, bcd2seg7_0_seg_c, bcd2seg7_0_seg_d, bcd2seg7_0_seg_e,
       bcd2seg7_0_seg_f, bcd2seg7_0_seg_g, bin2bcd_0_p11, bin2bcd_0_p12, bin2bcd_0_p13, bin2bcd_0_p14,
       block_1_c_out, block_3_counter_300ms_out, block_4_counting_out, block_5_c_out, block_6_bitdata_out,
       block_7_c_out, clock_1_out, not_1_out, not_2_out;
  wire [7:0] block_0_signalbreite;
  wire [12:0] block_2_ausgang_counter;

  Clock clock_1 (.out(clock_1_out));
  Signalbreite_Zusammenzaehlen block_0 (
    .Clock_2kHz(clock_1_out), .Data_Seriell(Antenna_IN), .Signalbreite(block_0_signalbreite));
  not not_1 (not_1_out, 1'b0);
  add8bit block_1 (
    .Minus(not_1_out), .C_IN(1'b0), .A0(1'b0), .A1(1'b1), .A2(1'b0), .A3(1'b0), .A4(1'b1), .A5(1'b1),
    .A6(1'b0), .A7(1'b0), .B0(block_0_signalbreite[0]), .B1(block_0_signalbreite[1]),
    .B2(block_0_signalbreite[2]), .B3(block_0_signalbreite[3]), .B4(block_0_signalbreite[4]),
    .B5(block_0_signalbreite[5]), .B6(block_0_signalbreite[6]), .B7(block_0_signalbreite[7]),
    .C_OUT(block_1_c_out));  // open: S0, S1, S2, S3, S4, S5, S6, S7
  add8bit block_5 (
    .Minus(not_1_out), .C_IN(1'b0), .A0(1'b0), .A1(1'b1), .A2(1'b1), .A3(1'b0), .A4(1'b1), .A5(1'b0),
    .A6(1'b0), .A7(1'b1), .B0(block_0_signalbreite[0]), .B1(block_0_signalbreite[1]),
    .B2(block_0_signalbreite[2]), .B3(block_0_signalbreite[3]), .B4(block_0_signalbreite[4]),
    .B5(block_0_signalbreite[5]), .B6(block_0_signalbreite[6]), .B7(block_0_signalbreite[7]),
    .C_OUT(block_5_c_out));  // open: S0, S1, S2, S3, S4, S5, S6, S7
  LED LED_0 (.in(block_1_c_out));
  LED LED_1 (.in(block_5_c_out));
  add8bit block_7 (
    .Minus(not_1_out), .C_IN(1'b0), .A0(block_0_signalbreite[0]), .A1(block_0_signalbreite[1]),
    .A2(block_0_signalbreite[2]), .A3(block_0_signalbreite[3]), .A4(block_0_signalbreite[4]),
    .A5(block_0_signalbreite[5]), .A6(block_0_signalbreite[6]), .A7(block_0_signalbreite[7]), .B0(1'b0),
    .B1(1'b1), .B2(1'b0), .B3(1'b0), .B4(1'b1), .B5(1'b1), .B6(1'b0), .B7(1'b0), .C_OUT(block_7_c_out));  // open: S0, S1, S2, S3, S4, S5, S6, S7
  LED LED_Antenna (.in(Antenna_IN));
  LED LED_2 (.in(block_7_c_out));
  Decode_DCF77_Signal_counting block_4 (
    .Clock(clock_1_out), .Bit_threshhold1(block_1_c_out), .Counter_300ms(block_3_counter_300ms_out),
    .counting_OUT(block_4_counting_out));
  Decode_DCF77_Signal_Bitdata block_6 (
    .Clock(clock_1_out), .Counting(block_4_counting_out), .Bit_threshhold1(block_1_c_out),
    .Bitdata(block_5_c_out), .BitData_OUT(block_6_bitdata_out));
  not not_2 (not_2_out, block_4_counting_out);
  Counter_300ms block_3 (
    .Clock_1kHz(clock_1_out), .Enable(block_4_counting_out), .Reset(not_2_out),
    .Counter_300ms_OUT(block_3_counter_300ms_out));
  and and_1 (and_1_out, block_3_counter_300ms_out, block_7_c_out);
  Counter_13bit block_2 (
    .Clock(clock_1_out), .Reset(1'b0), .Load(1'b0), .Enable(and_1_out),
    .Ausgang_Counter(block_2_ausgang_counter));  // open: Data_Load_13bit, Ausgang_Counter_Negiert
  // bcd bin2bcd_0: pin names not known; wires that end beside it: block_2_ausgang_counter[0], block_2_ausgang_counter[1], block_2_ausgang_counter[2], block_2_ausgang_counter[3], block_2_ausgang_counter[4], block_2_ausgang_counter[5], block_2_ausgang_counter[6], block_2_ausgang_counter[7], block_2_ausgang_counter[8], block_2_ausgang_counter[9], bin2bcd_0_p11, bin2bcd_0_p12, bin2bcd_0_p13, bin2bcd_0_p14
  seg7 bcd2seg7_0 (
    .A3(bin2bcd_0_p14), .A2(bin2bcd_0_p13), .A1(bin2bcd_0_p12), .A0(bin2bcd_0_p11), .SEG_A(bcd2seg7_0_seg_a),
    .SEG_B(bcd2seg7_0_seg_b), .SEG_C(bcd2seg7_0_seg_c), .SEG_D(bcd2seg7_0_seg_d), .SEG_E(bcd2seg7_0_seg_e),
    .SEG_F(bcd2seg7_0_seg_f), .SEG_G(bcd2seg7_0_seg_g));
  _7_Segment_Display LED_Seconds (
    .g(bcd2seg7_0_seg_g), .f(bcd2seg7_0_seg_f), .a(bcd2seg7_0_seg_a), .b(bcd2seg7_0_seg_b),
    .e(bcd2seg7_0_seg_e), .d(bcd2seg7_0_seg_d), .c(bcd2seg7_0_seg_c), .dp(block_6_bitdata_out));
  LED LED_Data (.in(block_6_bitdata_out));
endmodule

module Testing_Pruefen (
  output out_1
);

  wire add5bit_1_c_out, add6bit_1_c_out, add6bit_2_c_out, add7bit_1_s7, add8bit_1_c_out;

  add7bit add7bit_1 (
    .Minus(1'b1), .C_IN(1'b0), .A0(1'b1), .A1(1'b1), .A2(1'b0), .A3(1'b1), .A4(1'b1), .A5(1'b1), .A6(1'b0),
    .B0(1'b1), .B1(1'b1), .B2(1'b0), .B3(1'b1), .B4(1'b1), .B5(1'b1), .B7(1'b0), .S7(add7bit_1_s7));  // open: S0, S1, S2, S3, S4, S5, S6
  add6bit add6bit_1 (
    .Minus(1'b1), .C_IN(1'b0), .A0(1'b1), .A1(1'b1), .A2(1'b1), .A3(1'b0), .A4(1'b1), .A5(1'b0), .B0(1'b0),
    .B1(1'b0), .B2(1'b0), .B3(1'b1), .B4(1'b1), .B5(1'b0), .C_OUT(add6bit_1_c_out));  // open: S0, S1, S2, S3, S4, S5
  add6bit add6bit_2 (
    .Minus(1'b1), .C_IN(1'b0), .A0(1'b0), .A1(1'b0), .A2(1'b0), .A3(1'b0), .A4(1'b0), .A5(1'b1), .B0(1'b1),
    .B1(1'b0), .B2(1'b0), .B3(1'b0), .B4(1'b0), .B5(1'b1), .C_OUT(add6bit_2_c_out));  // open: S0, S1, S2, S3, S4, S5
  add5bit add5bit_1 (
    .Minus(1'b1), .C_IN(1'b0), .A0(1'b0), .A1(1'b0), .A2(1'b1), .A3(1'b1), .A4(1'b0), .B0(1'b1), .B1(1'b0),
    .B2(1'b1), .B3(1'b1), .B4(1'b0), .C_OUT(add5bit_1_c_out));  // open: S0, S1, S2, S3, S4
  add8bit add8bit_1 (
    .Minus(1'b1), .C_IN(1'b0), .A0(1'b1), .A1(1'b1), .A2(1'b0), .A3(1'b0), .A4(1'b0), .A5(1'b1), .A6(1'b1),
    .A7(1'b0), .B0(1'b0), .B1(1'b0), .B2(1'b0), .B3(1'b0), .B4(1'b0), .B5(1'b0), .B6(1'b0), .B7(1'b0),
    .C_OUT(add8bit_1_c_out));  // open: S0, S1, S2, S3, S4, S5, S6, S7
  or or_1 (out_1, add7bit_1_s7, add6bit_1_c_out, add6bit_2_c_out, add5bit_1_c_out, add8bit_1_c_out);
endmodule

module Test_Funkuhr (
  input  Antenna_IN
);

  wire and_1_out, block_0_data_fehler, block_2_p11, block_2_p12, block_2_p13, block_2_p14,
       block_3_data_fehler, block_4_seg_a, block_4_seg_b, block_4_seg_c, block_4_seg_d, block_4_seg_e,
       block_4_seg_f, block_4_seg_g, block_5_bit_minuteanfang, block_5_parity3, block_7_bit_data,
       block_7_bit_sekunde_erkannt, block_9_sync, block_10_ausgang_sekunde, block_11_p11, block_11_p12,
       block_11_p13, block_11_p14, block_12_seg_a, block_12_seg_b, block_12_seg_c, block_12_seg_d,
       block_12_seg_e, block_12_seg_f, block_12_seg_g, blocK_14_p11, blocK_14_p12, blocK_14_p13,
       blocK_14_p14, blocK_15_seg_a, blocK_15_seg_b, blocK_15_seg_c, blocK_15_seg_d, blocK_15_seg_e,
       blocK_15_seg_f, blocK_15_seg_g, clock_1_out, d_ff_1_q, or_1_out;
  wire [2:0] block_5_data_wochentag, D_FF_Array_0_data_wocentag_out;
  wire [4:0] block_5_data_monat, block_6_data_monat_out, block_6_data_stunde_out, block_8_data_monat_out,
       D_FF_Array_0_data_monat_out, D_FF_Array_0_data_stunde_out;
  wire [5:0] block_5_data_tag, block_6_data_tag_out, block_8_data_stunde_out, block_8_data_tag_out,
       D_FF_Array_0_data_minute_out, D_FF_Array_0_data_tag_out;
  wire [6:0] block_5_data_minute_2, block_5_data_stunden, block_8_data_minute_out;
  wire [7:0] block_5_data_jahr, block_8_data_jahr_out, D_FF_Array_0_data_jahr_out;
  wire [7:7] block_5_data_minute;
  wire [12:0] block_1_ausgang_counter, block_13_ausgang_counter, blocK_16_ausgang_counter;

  Clock clock_1 (.out(clock_1_out));
  Decode_DCF77_Signal block_7 (
    .Clock_2kHz(clock_1_out), .Data_Seriell(Antenna_IN), .Bit_Sekunde_erkannt(block_7_bit_sekunde_erkannt),
    .Bit_Data(block_7_bit_data));
  Schieberegister_DCF77Data_59bit block_5 (
    .Clock(clock_1_out), .Data_In(block_7_bit_data), .Enable(block_7_bit_sekunde_erkannt),
    .Bit_MinuteAnfang(block_5_bit_minuteanfang),
    .Data_Minute({block_5_data_minute[7], block_5_data_minute_2}), .Data_Stunden(block_5_data_stunden),
    .Data_Tag(block_5_data_tag), .Data_Wochentag(block_5_data_wochentag), .Data_Monat(block_5_data_monat),
    .Data_Jahr(block_5_data_jahr), .Parity3(block_5_parity3));  // open: Data_Wetter, Data_Zeitsystem
  Counter_Second block_10 (
    .Clock_2kHz(clock_1_out), .Set(block_7_bit_sekunde_erkannt), .Enable(1'b1),
    .Data_SetClock_13bit(13'h12c), .Ausgang_Sekunde(block_10_ausgang_sekunde));
  Synchroerkenner block_9 (
    .Clock(clock_1_out), .sekunde_extern(block_7_bit_sekunde_erkannt),
    .sekunde_intern(block_10_ausgang_sekunde), .sync(block_9_sync));  // open: offline
  Parity_Check block_0 (
    .Data_Minute({block_5_data_minute[7], block_5_data_minute_2}), .Data_Stunde(block_5_data_stunden),
    .Data_Tag(block_5_data_tag), .Data_Wochentag(block_5_data_wochentag), .Data_Monat(block_5_data_monat),
    .Data_Jahr(block_5_data_jahr), .Parity3(block_5_parity3), .Data_Fehler(block_0_data_fehler));
  Decode_DCF77Data block_8 (
    .Data_Minute_IN(block_5_data_minute_2), .Data_Stunde_IN(block_5_data_stunden[5:0]),
    .Data_Tag_IN(block_5_data_tag), .Data_Monat_IN(block_5_data_monat), .Data_Jahr_IN(block_5_data_jahr),
    .Data_Minute_OUT(block_8_data_minute_out), .Data_Stunde_OUT(block_8_data_stunde_out),
    .Data_Tag_OUT(block_8_data_tag_out), .Data_Monat_OUT(block_8_data_monat_out),
    .Data_Jahr_OUT(block_8_data_jahr_out));
  DCF77Data_Pruefen block_3 (
    .Data_Minute_bin(block_8_data_minute_out), .Data_Stunde_bin(block_8_data_stunde_out),
    .Data_Tag_bin(block_8_data_tag_out), .Data_Monat_bin(block_8_data_monat_out),
    .Data_Jahr_bin(block_8_data_jahr_out), .Data_Fehler(block_3_data_fehler));
  D_Flip_Flop d_ff_1 (.D(or_1_out), .clk(clock_1_out), .Q(d_ff_1_q));  // open: Qn, preset, reset
  or or_1 (or_1_out, block_0_data_fehler, block_3_data_fehler, block_5_bit_minuteanfang);
  and and_1 (and_1_out, ~d_ff_1_q, block_9_sync);  // AND_Gate
  LED LED_Parity (.in(block_0_data_fehler));
  LED LED_Possibility (.in(block_3_data_fehler));
  LED LED_Minute_start (.in(block_5_bit_minuteanfang));
  DFlipFlop_Array D_FF_Array_0 (
    .Clock(clock_1_out), .Enable(block_7_bit_sekunde_erkannt), .Data_Minute_IN(block_8_data_minute_out[5:0]),
    .Data_Stunde_IN(block_8_data_stunde_out[4:0]), .Data_Tag_IN(block_8_data_tag_out),
    .Data_Wochentag_IN(block_5_data_wochentag), .Data_Monat_IN(block_8_data_monat_out),
    .Data_Jahr_IN(block_8_data_jahr_out), .Data_Minute_OUT(D_FF_Array_0_data_minute_out),
    .Data_Stunde_OUT(D_FF_Array_0_data_stunde_out), .Data_Tag_OUT(D_FF_Array_0_data_tag_out),
    .Data_Wocentag_OUT(D_FF_Array_0_data_wocentag_out), .Data_Monat_OUT(D_FF_Array_0_data_monat_out),
    .Data_Jahr_OUT(D_FF_Array_0_data_jahr_out));
  LED LED_Data_Tag_vor_0 (.in(D_FF_Array_0_data_tag_out[0]));
  LED LED_Data_Tag_vor_1 (.in(D_FF_Array_0_data_tag_out[1]));
  LED LED_Data_Tag_vor_2 (.in(D_FF_Array_0_data_tag_out[2]));
  LED LED_Data_Tag_vor_3 (.in(D_FF_Array_0_data_tag_out[3]));
  LED LED_Data_Tag_vor_4 (.in(D_FF_Array_0_data_tag_out[4]));
  LED LED_Data_Tag_vor_5 (.in(D_FF_Array_0_data_tag_out[5]));
  LED LED_Data_Monat_vor_0 (.in(D_FF_Array_0_data_monat_out[0]));
  LED LED_Data_Monat_vor_1 (.in(D_FF_Array_0_data_monat_out[1]));
  LED LED_Data_Monat_vor_2 (.in(D_FF_Array_0_data_monat_out[2]));
  LED LED_Data_Monat_vor_3 (.in(D_FF_Array_0_data_monat_out[3]));
  LED LED_Data_Monat_vor_4 (.in(D_FF_Array_0_data_monat_out[4]));
  LED LED_Data_Stunde_vor_0 (.in(D_FF_Array_0_data_stunde_out[0]));
  LED LED_Data_Stunde_vor_1 (.in(D_FF_Array_0_data_stunde_out[1]));
  LED LED_Data_Stunde_vor_2 (.in(D_FF_Array_0_data_stunde_out[2]));
  LED LED_Data_Stunde_vor_3 (.in(D_FF_Array_0_data_stunde_out[3]));
  LED LED_Data_Stunde_vor_4 (.in(D_FF_Array_0_data_stunde_out[4]));
  Storage_Time_Data block_6 (
    .Clock(clock_1_out), .Load(and_1_out), .Sekunde_IN(block_10_ausgang_sekunde),
    .Data_Minute_IN(D_FF_Array_0_data_minute_out), .Data_Stunde_IN(D_FF_Array_0_data_stunde_out),
    .Data_Tag_IN(D_FF_Array_0_data_tag_out), .Data_Wochentag_IN(D_FF_Array_0_data_wocentag_out),
    .Data_Monat_IN(D_FF_Array_0_data_monat_out), .Data_Jahr_IN(D_FF_Array_0_data_jahr_out),
    .Data_Stunde_OUT(block_6_data_stunde_out), .Data_Tag_OUT(block_6_data_tag_out),
    .Data_Monat_OUT(block_6_data_monat_out));  // open: Data_Sekunde_OUT, Data_Minute_OUT, Data_Wochentag_OUT, Data_Jahr_OUT
  Counter_13bit block_1 (
    .Clock(clock_1_out), .Reset(1'b0), .Load(1'b0), .Enable(and_1_out), .Data_Load_13bit({13{1'b0}}),
    .Ausgang_Counter(block_1_ausgang_counter));  // open: Ausgang_Counter_Negiert
  LED LED_Tag_OUT_0 (.in(block_6_data_tag_out[0]));
  LED LED_Tag_OUT_1 (.in(block_6_data_tag_out[1]));
  LED LED_Tag_OUT_2 (.in(block_6_data_tag_out[2]));
  LED LED_Tag_OUT_3 (.in(block_6_data_tag_out[3]));
  LED LED_Tag_OUT_4 (.in(block_6_data_tag_out[4]));
  LED LED_Tag_OUT_5 (.in(block_6_data_tag_out[5]));
  LED LED_Data_Monat_0 (.in(block_6_data_monat_out[0]));
  LED LED_Data_Monat_1 (.in(block_6_data_monat_out[1]));
  LED LED_Data_Monat_2 (.in(block_6_data_monat_out[2]));
  LED LED_Data_Monat_3 (.in(block_6_data_monat_out[3]));
  LED LED_Data_Monat_4 (.in(block_6_data_monat_out[4]));
  LED LED_Data_Stunde_0 (.in(block_6_data_stunde_out[0]));
  LED LED_Data_Stunde_1 (.in(block_6_data_stunde_out[1]));
  LED LED_Data_Stunde_2 (.in(block_6_data_stunde_out[2]));
  LED LED_Data_Stunde_3 (.in(block_6_data_stunde_out[3]));
  LED LED_Data_Stunde_4 (.in(block_6_data_stunde_out[4]));
  Counter_13bit blocK_16 (
    .Clock(clock_1_out), .Reset(1'b0), .Load(1'b0), .Enable(block_7_bit_sekunde_erkannt),
    .Data_Load_13bit({13{1'b0}}), .Ausgang_Counter(blocK_16_ausgang_counter));  // open: Ausgang_Counter_Negiert
  // bcd block_2: pin names not known; wires that end beside it: block_1_ausgang_counter[0], block_1_ausgang_counter[1], block_1_ausgang_counter[2], block_1_ausgang_counter[3], block_1_ausgang_counter[4], block_1_ausgang_counter[5], block_1_ausgang_counter[6], block_1_ausgang_counter[7], block_1_ausgang_counter[8], block_1_ausgang_counter[9], block_2_p11, block_2_p12, block_2_p13, block_2_p14
  // bcd blocK_14: pin names not known; wires that end beside it: blocK_16_ausgang_counter[0], blocK_16_ausgang_counter[1], blocK_16_ausgang_counter[2], blocK_16_ausgang_counter[3], blocK_16_ausgang_counter[4], blocK_16_ausgang_counter[5], blocK_16_ausgang_counter[6], blocK_16_ausgang_counter[7], blocK_16_ausgang_counter[8], blocK_16_ausgang_counter[9], blocK_14_p11, blocK_14_p12, blocK_14_p13, blocK_14_p14
  seg7 block_4 (
    .A3(block_2_p14), .A2(block_2_p13), .A1(block_2_p12), .A0(block_2_p11), .SEG_A(block_4_seg_a),
    .SEG_B(block_4_seg_b), .SEG_C(block_4_seg_c), .SEG_D(block_4_seg_d), .SEG_E(block_4_seg_e),
    .SEG_F(block_4_seg_f), .SEG_G(block_4_seg_g));
  Counter_13bit block_13 (
    .Clock(clock_1_out), .Reset(1'b0), .Load(1'b0), .Enable(block_9_sync), .Data_Load_13bit({13{1'b0}}),
    .Ausgang_Counter(block_13_ausgang_counter));  // open: Ausgang_Counter_Negiert
  seg7 blocK_15 (
    .A3(blocK_14_p14), .A2(blocK_14_p13), .A1(blocK_14_p12), .A0(blocK_14_p11), .SEG_A(blocK_15_seg_a),
    .SEG_B(blocK_15_seg_b), .SEG_C(blocK_15_seg_c), .SEG_D(blocK_15_seg_d), .SEG_E(blocK_15_seg_e),
    .SEG_F(blocK_15_seg_f), .SEG_G(blocK_15_seg_g));
  _7_Segment_Display LED_synchronized (
    .g(block_4_seg_g), .f(block_4_seg_f), .a(block_4_seg_a), .b(block_4_seg_b), .e(block_4_seg_e),
    .d(block_4_seg_d), .c(block_4_seg_c), .dp(Antenna_IN));
  // bcd block_11: pin names not known; wires that end beside it: block_13_ausgang_counter[0], block_13_ausgang_counter[1], block_13_ausgang_counter[2], block_13_ausgang_counter[3], block_13_ausgang_counter[4], block_13_ausgang_counter[5], block_13_ausgang_counter[6], block_13_ausgang_counter[7], block_13_ausgang_counter[8], block_13_ausgang_counter[9], block_11_p11, block_11_p12, block_11_p13, block_11_p14
  _7_Segment_Display LED_Secunde (
    .g(blocK_15_seg_g), .f(blocK_15_seg_f), .a(blocK_15_seg_a), .b(blocK_15_seg_b), .e(blocK_15_seg_e),
    .d(blocK_15_seg_d), .c(blocK_15_seg_c), .dp(Antenna_IN));
  seg7 block_12 (
    .A3(block_11_p14), .A2(block_11_p13), .A1(block_11_p12), .A0(block_11_p11), .SEG_A(block_12_seg_a),
    .SEG_B(block_12_seg_b), .SEG_C(block_12_seg_c), .SEG_D(block_12_seg_d), .SEG_E(block_12_seg_e),
    .SEG_F(block_12_seg_f), .SEG_G(block_12_seg_g));
  _7_Segment_Display LED_raw_sync (
    .g(block_12_seg_g), .f(block_12_seg_f), .a(block_12_seg_a), .b(block_12_seg_b), .e(block_12_seg_e),
    .d(block_12_seg_d), .c(block_12_seg_c), .dp(Antenna_IN));
endmodule

module Test_Decocedr (
  input  in_1,
  input  in_2,
  input  in_3,
  input  in_4,
  input  in_5,
  input  in_6,
  input  in_7,
  input  in_8,
  input  in_9,
  input  in_10,
  input  in_11,
  input  in_12,
  input  in_13,
  input  in_14,
  input  in_15,
  input  in_16,
  input  in_17,
  input  in_18,
  input  in_19,
  input  in_20,
  input  in_21,
  output [6:0] out_22,
  output [5:0] out_23,
  output [5:0] out_24,
  output [4:0] out_25,
  output [7:0] out_26
);

  wire [5:0] undriven;
  wire [7:0] undriven_2;

  Decode_Minute decode_minute_1 (
    .Data_Minute_7bit_Eingang({in_7, in_6, in_5, in_4, in_3, in_2, in_1}), .Data_Minute_7bit_Ausgang(out_22));
  Decode_Stunde decode_stunde_1 (.Data_Stunde_6bit_Eingang(undriven), .Data_Stunde_6bit_Ausgang(out_23));
  Decode_Tag decode_tag_1 (
    .Data_Tag_6bit_Eingang({in_14, in_13, in_12, in_11, in_10, in_9}), .Data_Tag_6bit_Ausgang(out_24));
  Deode_Monat deode_monat_1 (
    .Data_Monat_5bit_Eingang({in_21, in_20, in_19, in_18, in_17}), .Data_Jahr_5bit_Ausgang(out_25));
  Decode_Jahr decode_jahr_1 (.Data_Jahr_8bit_Eingang(undriven_2), .Data_Jahr_8bit_Ausgang(out_26));
endmodule

module Test_Tag (
  input  in_1,
  input  in_2,
  output [5:0] out_3
);

  wire [5:0] multiplexer_6bit_1_ausgang_0;

  Multiplexer_6bit multiplexer_6bit_1 (
    .Umschalter({1'b0, in_2}), .Eingang_0(out_3), .Eingang_1(6'b011000), .Eingnag_2({6{1'b0}}),
    .Ausgang_0(multiplexer_6bit_1_ausgang_0));
  D_Flip_Flop d_ff_1 (.D(multiplexer_6bit_1_ausgang_0[0]), .clk(in_1), .Q(out_3[0]));  // open: Qn, preset, reset
  D_Flip_Flop d_ff_2 (.D(multiplexer_6bit_1_ausgang_0[1]), .clk(in_1), .Q(out_3[1]));  // open: Qn, preset, reset
  D_Flip_Flop d_ff_3 (.D(multiplexer_6bit_1_ausgang_0[2]), .clk(in_1), .Q(out_3[2]));  // open: Qn, preset, reset
  D_Flip_Flop d_ff_4 (.D(multiplexer_6bit_1_ausgang_0[3]), .clk(in_1), .Q(out_3[3]));  // open: Qn, preset, reset
  D_Flip_Flop d_ff_5 (.D(multiplexer_6bit_1_ausgang_0[4]), .clk(in_1), .Q(out_3[4]));  // open: Qn, preset, reset
  D_Flip_Flop d_ff_6 (.D(multiplexer_6bit_1_ausgang_0[5]), .clk(in_1), .Q(out_3[5]));  // open: Qn, preset, reset
endmodule

module DFlipFlop_Array (
  input  Clock,
  input  Enable,
  input  [5:0] Data_Minute_IN,
  input  [4:0] Data_Stunde_IN,
  input  [5:0] Data_Tag_IN,
  input  [2:0] Data_Wochentag_IN,
  input  [4:0] Data_Monat_IN,
  input  [7:0] Data_Jahr_IN,
  output [5:0] Data_Minute_OUT,
  output [4:0] Data_Stunde_OUT,
  output [5:0] Data_Tag_OUT,
  output [2:0] Data_Wocentag_OUT,
  output [4:0] Data_Monat_OUT,
  output [7:0] Data_Jahr_OUT
);

  Register #(.width(6)) register_1 (.D(Data_Minute_IN), .en(Enable), .clk(Clock), .Q(Data_Minute_OUT));  // open: clr
  Register #(.width(5)) register_2 (.D(Data_Stunde_IN), .en(Enable), .clk(Clock), .Q(Data_Stunde_OUT));  // open: clr
  Register #(.width(6)) register_3 (.D(Data_Tag_IN), .en(Enable), .clk(Clock), .Q(Data_Tag_OUT));  // open: clr
  Register #(.width(3)) register_4 (
    .D(Data_Wochentag_IN), .en(Enable), .clk(Clock), .Q(Data_Wocentag_OUT));  // open: clr
  Register #(.width(5)) register_5 (.D(Data_Monat_IN), .en(Enable), .clk(Clock), .Q(Data_Monat_OUT));  // open: clr
  Register register_6 (.D(Data_Jahr_IN), .en(Enable), .clk(Clock), .Q(Data_Jahr_OUT));  // open: clr
endmodule
