// Logisim project LED_Anzeige.circ as structural Verilog: 6 circuits, main circuit Hauptschaltung_LED_Anzeige
module Hauptschaltung_LED_Anzeige (
  input  Input_1,
  input  Weckfunktion,
  input  Eingangstaste_Min_Sek,
  input  Eingangstaste_Tag_Monat,
  input  Eingangstaste_Jahr,
  output LED_Rahmen_Rest_Wecker,
  output LED_3_2,
  output LED_3_3,
  output LED_3_7,
  output LED_3_11,
  output LED_4_2,
  output LED_4_4,
  output LED_4_7,
  output LED_4_8,
  output LED_4_9,
  output LED_4_10,
  output LED_4_11,
  output LED_5_2,
  output LED_5_3,
  output LED_5_4,
  output LED_5_5,
  output LED_5_6,
  output LED_5_7,
  output LED_5_8,
  output LED_5_9,
  output LED_5_10,
  output LED_5_11,
  output LED_6_2,
  output LED_6_3,
  output LED_6_4,
  output LED_6_5,
  output LED_6_6,
  output LED_6_7,
  output LED_6_8,
  output LED_6_9,
  output LED_6_10,
  output LED_6_11,
  output LED_7_2,
  output LED_7_4,
  output LED_7_5,
  output LED_7_6,
  output LED_7_7,
  output LED_7_9,
  output LED_7_10,
  output LED_7_11,
  output LED_8_2,
  output LED_8_3,
  output LED_8_5,
  output LED_8_6,
  output LED_8_7,
  output LED_8_8,
  output LED_8_9,
  output LED_8_10,
  output LED_8_11
);

  wire D_und_M_1_led_3_2, D_und_M_1_led_3_3, D_und_M_1_led_3_7, D_und_M_1_led_3_11, D_und_M_1_led_4_2,
       D_und_M_1_led_4_4, D_und_M_1_led_4_7, D_und_M_1_led_4_8, D_und_M_1_led_4_10, D_und_M_1_led_4_11,
       D_und_M_1_led_5_2, D_und_M_1_led_5_5, D_und_M_1_led_5_7, D_und_M_1_led_5_9, D_und_M_1_led_5_11,
       D_und_M_1_led_6_2, D_und_M_1_led_6_5, D_und_M_1_led_6_7, D_und_M_1_led_6_11, D_und_M_1_led_7_2,
       D_und_M_1_led_7_4, D_und_M_1_led_7_7, D_und_M_1_led_7_11, D_und_M_1_led_8_2, D_und_M_1_led_8_3,
       D_und_M_1_led_8_7, D_und_M_1_led_8_11, h_und_m_1_led_3_2, h_und_m_1_led_4_2, h_und_m_1_led_5_2,
       h_und_m_1_led_5_7, h_und_m_1_led_5_8, h_und_m_1_led_5_9, h_und_m_1_led_5_10, h_und_m_1_led_5_11,
       h_und_m_1_led_6_2, h_und_m_1_led_6_3, h_und_m_1_led_6_4, h_und_m_1_led_6_5, h_und_m_1_led_6_7,
       h_und_m_1_led_6_9, h_und_m_1_led_6_11, h_und_m_1_led_7_2, h_und_m_1_led_7_5, h_und_m_1_led_7_7,
       h_und_m_1_led_7_9, h_und_m_1_led_7_11, h_und_m_1_led_8_2, h_und_m_1_led_8_5, h_und_m_1_led_8_7,
       h_und_m_1_led_8_11, m_und_s_1_led_4_8, m_und_s_1_led_4_9, m_und_s_1_led_4_10, m_und_s_1_led_5_2,
       m_und_s_1_led_5_3, m_und_s_1_led_5_4, m_und_s_1_led_5_5, m_und_s_1_led_5_6, m_und_s_1_led_5_8,
       m_und_s_1_led_6_2, m_und_s_1_led_6_4, m_und_s_1_led_6_6, m_und_s_1_led_6_8, m_und_s_1_led_6_9,
       m_und_s_1_led_6_10, m_und_s_1_led_7_2, m_und_s_1_led_7_4, m_und_s_1_led_7_6, m_und_s_1_led_7_10,
       m_und_s_1_led_8_2, m_und_s_1_led_8_6, m_und_s_1_led_8_8, m_und_s_1_led_8_9, m_und_s_1_led_8_10,
       or_1_out, or_2_out, or_3_out, or_4_out, or_5_out, or_6_out, or_7_out, or_8_out, or_9_out, or_10_out,
       or_11_out, or_12_out, or_13_out, or_14_out, or_15_out, or_16_out, or_17_out, or_18_out, or_19_out,
       or_20_out, or_21_out, or_22_out, or_23_out, or_24_out, or_25_out, or_26_out, or_27_out, or_28_out,
       or_29_out, or_30_out, Y_1_led_3_7, Y_1_led_3_11, Y_1_led_4_7, Y_1_led_4_11, Y_1_led_5_8, Y_1_led_5_10,
       Y_1_led_6_9, Y_1_led_7_9, Y_1_led_8_9;

  and and_1 (LED_Rahmen_Rest_Wecker, Input_1, Weckfunktion);
  h_und_m h_und_m_1 (
    .Taste_min_sek(Eingangstaste_Min_Sek), .Taste_tag_mon(Eingangstaste_Tag_Monat),
    .Taste_jahr(Eingangstaste_Jahr), .LED_3_2(h_und_m_1_led_3_2), .LED_4_2(h_und_m_1_led_4_2),
    .LED_5_2(h_und_m_1_led_5_2), .LED_5_7(h_und_m_1_led_5_7), .LED_5_8(h_und_m_1_led_5_8),
    .LED_5_9(h_und_m_1_led_5_9), .LED_5_10(h_und_m_1_led_5_10), .LED_5_11(h_und_m_1_led_5_11),
    .LED_6_2(h_und_m_1_led_6_2), .LED_6_3(h_und_m_1_led_6_3), .LED_6_4(h_und_m_1_led_6_4),
    .LED_6_5(h_und_m_1_led_6_5), .LED_6_7(h_und_m_1_led_6_7), .LED_6_9(h_und_m_1_led_6_9),
    .LED_6_11(h_und_m_1_led_6_11), .LED_7_2(h_und_m_1_led_7_2), .LED_7_5(h_und_m_1_led_7_5),
    .LED_7_7(h_und_m_1_led_7_7), .LED_7_9(h_und_m_1_led_7_9), .LED_7_11(h_und_m_1_led_7_11),
    .LED_8_2(h_und_m_1_led_8_2), .LED_8_5(h_und_m_1_led_8_5), .LED_8_7(h_und_m_1_led_8_7),
    .LED_8_11(h_und_m_1_led_8_11));
  m_und_s m_und_s_1 (
    .Taste_min_sek(Eingangstaste_Min_Sek), .LED_4_8(m_und_s_1_led_4_8), .LED_4_9(m_und_s_1_led_4_9),
    .LED_4_10(m_und_s_1_led_4_10), .LED_5_2(m_und_s_1_led_5_2), .LED_5_3(m_und_s_1_led_5_3),
    .LED_5_4(m_und_s_1_led_5_4), .LED_5_5(m_und_s_1_led_5_5), .LED_5_6(m_und_s_1_led_5_6),
    .LED_5_8(m_und_s_1_led_5_8), .LED_6_2(m_und_s_1_led_6_2), .LED_6_4(m_und_s_1_led_6_4),
    .LED_6_6(m_und_s_1_led_6_6), .LED_6_8(m_und_s_1_led_6_8), .LED_6_9(m_und_s_1_led_6_9),
    .LED_6_10(m_und_s_1_led_6_10), .LED_7_2(m_und_s_1_led_7_2), .LED_7_4(m_und_s_1_led_7_4),
    .LED_7_6(m_und_s_1_led_7_6), .LED_7_10(m_und_s_1_led_7_10), .LED_8_2(m_und_s_1_led_8_2),
    .LED_8_6(m_und_s_1_led_8_6), .LED_8_8(m_und_s_1_led_8_8), .LED_8_9(m_und_s_1_led_8_9),
    .LED_8_10(m_und_s_1_led_8_10));
  D_und_M D_und_M_1 (
    .Taste_Tag_Monat(Eingangstaste_Tag_Monat), .LED_3_2(D_und_M_1_led_3_2), .LED_3_3(D_und_M_1_led_3_3),
    .LED_3_7(D_und_M_1_led_3_7), .LED_3_11(D_und_M_1_led_3_11), .LED_4_2(D_und_M_1_led_4_2),
    .LED_4_4(D_und_M_1_led_4_4), .LED_4_7(D_und_M_1_led_4_7), .LED_4_8(D_und_M_1_led_4_8),
    .LED_4_10(D_und_M_1_led_4_10), .LED_4_11(D_und_M_1_led_4_11), .LED_5_2(D_und_M_1_led_5_2),
    .LED_5_5(D_und_M_1_led_5_5), .LED_5_7(D_und_M_1_led_5_7), .LED_5_9(D_und_M_1_led_5_9),
    .LED_5_11(D_und_M_1_led_5_11), .LED_6_2(D_und_M_1_led_6_2), .LED_6_5(D_und_M_1_led_6_5),
    .LED_6_7(D_und_M_1_led_6_7), .LED_6_11(D_und_M_1_led_6_11), .LED_7_2(D_und_M_1_led_7_2),
    .LED_7_4(D_und_M_1_led_7_4), .LED_7_7(D_und_M_1_led_7_7), .LED_7_11(D_und_M_1_led_7_11),
    .LED_8_2(D_und_M_1_led_8_2), .LED_8_3(D_und_M_1_led_8_3), .LED_8_7(D_und_M_1_led_8_7),
    .LED_8_11(D_und_M_1_led_8_11));
  Y Y_1 (
    .Taste_Jahr(Eingangstaste_Jahr), .LED_3_7(Y_1_led_3_7), .LED_3_11(Y_1_led_3_11), .LED_4_7(Y_1_led_4_7),
    .LED_4_11(Y_1_led_4_11), .LED_5_8(Y_1_led_5_8), .LED_5_10(Y_1_led_5_10), .LED_6_9(Y_1_led_6_9),
    .LED_7_9(Y_1_led_7_9), .LED_8_9(Y_1_led_8_9));
  or or_1 (or_1_out, h_und_m_1_led_3_2, D_und_M_1_led_3_2);
  or or_2 (or_2_out, D_und_M_1_led_3_7, Y_1_led_3_7);
  or or_3 (or_3_out, D_und_M_1_led_3_11, Y_1_led_3_11);
  or or_4 (or_4_out, h_und_m_1_led_4_2, D_und_M_1_led_4_2);
  or or_5 (or_5_out, D_und_M_1_led_4_7, Y_1_led_4_7);
  or or_6 (or_6_out, m_und_s_1_led_4_8, D_und_M_1_led_4_8);
  or or_7 (or_7_out, m_und_s_1_led_4_10, D_und_M_1_led_4_10);
  or or_8 (or_8_out, D_und_M_1_led_4_11, Y_1_led_4_11);
  or or_9 (or_9_out, h_und_m_1_led_5_2, D_und_M_1_led_5_2, m_und_s_1_led_5_2);
  or or_10 (or_10_out, m_und_s_1_led_5_5, D_und_M_1_led_5_5);
  or or_11 (or_11_out, h_und_m_1_led_5_7, D_und_M_1_led_5_7);
  or or_12 (or_12_out, h_und_m_1_led_5_8, m_und_s_1_led_5_8, Y_1_led_5_8);
  or or_13 (or_13_out, h_und_m_1_led_5_9, D_und_M_1_led_5_9);
  or or_14 (or_14_out, h_und_m_1_led_5_10, Y_1_led_5_10);
  or or_15 (or_15_out, h_und_m_1_led_5_11, D_und_M_1_led_5_11);
  or or_16 (or_16_out, h_und_m_1_led_6_2, m_und_s_1_led_6_2, D_und_M_1_led_6_2);
  or or_17 (or_17_out, h_und_m_1_led_6_4, m_und_s_1_led_6_4);
  or or_18 (or_18_out, h_und_m_1_led_6_5, D_und_M_1_led_6_5);
  or or_19 (or_19_out, h_und_m_1_led_6_7, D_und_M_1_led_6_7);
  or or_20 (or_20_out, h_und_m_1_led_6_9, Y_1_led_6_9, m_und_s_1_led_6_9);
  or or_21 (or_21_out, h_und_m_1_led_6_11, D_und_M_1_led_6_11);
  or or_22 (or_22_out, h_und_m_1_led_7_2, m_und_s_1_led_7_2, D_und_M_1_led_7_2);
  or or_23 (or_23_out, m_und_s_1_led_7_4, D_und_M_1_led_7_4);
  or or_24 (or_24_out, D_und_M_1_led_7_7, h_und_m_1_led_7_7);
  or or_25 (or_25_out, h_und_m_1_led_7_9, Y_1_led_7_9);
  or or_26 (or_26_out, h_und_m_1_led_7_11, D_und_M_1_led_7_11);
  or or_27 (or_27_out, h_und_m_1_led_8_2, m_und_s_1_led_8_2, D_und_M_1_led_8_2);
  or or_28 (or_28_out, h_und_m_1_led_8_7, D_und_M_1_led_8_7);
  or or_29 (or_29_out, m_und_s_1_led_8_9, Y_1_led_8_9);
  or or_30 (or_30_out, h_und_m_1_led_8_11, D_und_M_1_led_8_11);
  xor xor_1 (LED_3_2, LED_Rahmen_Rest_Wecker, or_1_out);
  xor xor_2 (LED_3_3, LED_Rahmen_Rest_Wecker, D_und_M_1_led_3_3);
  xor xor_3 (LED_3_7, LED_Rahmen_Rest_Wecker, or_2_out);
  xor xor_4 (LED_3_11, LED_Rahmen_Rest_Wecker, or_3_out);
  xor xor_5 (LED_4_2, LED_Rahmen_Rest_Wecker, or_4_out);
  xor xor_6 (LED_4_4, LED_Rahmen_Rest_Wecker, D_und_M_1_led_4_4);
  xor xor_7 (LED_4_7, LED_Rahmen_Rest_Wecker, or_5_out);
  xor xor_8 (LED_4_8, LED_Rahmen_Rest_Wecker, or_6_out);
  xor xor_9 (LED_4_9, LED_Rahmen_Rest_Wecker, m_und_s_1_led_4_9);
  xor xor_10 (LED_4_10, LED_Rahmen_Rest_Wecker, or_7_out);
  xor xor_11 (LED_4_11, LED_Rahmen_Rest_Wecker, or_8_out);
  xor xor_12 (LED_5_2, LED_Rahmen_Rest_Wecker, or_9_out);
  xor xor_13 (LED_5_3, LED_Rahmen_Rest_Wecker, m_und_s_1_led_5_3);
  xor xor_14 (LED_5_4, LED_Rahmen_Rest_Wecker, m_und_s_1_led_5_4);
  xor xor_15 (LED_5_5, LED_Rahmen_Rest_Wecker, or_10_out);
  xor xor_16 (LED_5_6, LED_Rahmen_Rest_Wecker, m_und_s_1_led_5_6);
  xor xor_17 (LED_5_7, LED_Rahmen_Rest_Wecker, or_11_out);
  xor xor_18 (LED_5_8, LED_Rahmen_Rest_Wecker, or_12_out);
  xor xor_19 (LED_5_9, LED_Rahmen_Rest_Wecker, or_13_out);
  xor xor_20 (LED_5_10, LED_Rahmen_Rest_Wecker, or_14_out);
  xor xor_21 (LED_5_11, LED_Rahmen_Rest_Wecker, or_15_out);
  xor xor_22 (LED_6_2, LED_Rahmen_Rest_Wecker, or_16_out);
  xor xor_23 (LED_6_3, LED_Rahmen_Rest_Wecker, h_und_m_1_led_6_3);
  xor xor_24 (LED_6_4, LED_Rahmen_Rest_Wecker, or_17_out);
  xor xor_25 (LED_6_5, LED_Rahmen_Rest_Wecker, or_18_out);
  xor xor_26 (LED_6_6, LED_Rahmen_Rest_Wecker, m_und_s_1_led_6_6);
  xor xor_27 (LED_6_7, LED_Rahmen_Rest_Wecker, or_19_out);
  xor xor_28 (LED_6_8, LED_Rahmen_Rest_Wecker, m_und_s_1_led_6_8);
  xor xor_29 (LED_6_9, LED_Rahmen_Rest_Wecker, or_20_out);
  xor xor_30 (LED_6_10, LED_Rahmen_Rest_Wecker, m_und_s_1_led_6_10);
  xor xor_31 (LED_6_11, LED_Rahmen_Rest_Wecker, or_21_out);
  xor xor_32 (LED_7_2, LED_Rahmen_Rest_Wecker, or_22_out);
  xor xor_33 (LED_7_4, LED_Rahmen_Rest_Wecker, or_23_out);
  xor xor_34 (LED_7_5, LED_Rahmen_Rest_Wecker, h_und_m_1_led_7_5);
  xor xor_35 (LED_7_6, LED_Rahmen_Rest_Wecker, m_und_s_1_led_7_6);
  xor xor_36 (LED_7_7, LED_Rahmen_Rest_Wecker, or_24_out);
  xor xor_37 (LED_7_9, LED_Rahmen_Rest_Wecker, or_25_out);
  xor xor_38 (LED_7_10, LED_Rahmen_Rest_Wecker, m_und_s_1_led_7_10);
  xor xor_39 (LED_7_11, LED_Rahmen_Rest_Wecker, or_26_out);
  xor xor_40 (LED_8_2, LED_Rahmen_Rest_Wecker, or_27_out);
  xor xor_41 (LED_8_3, LED_Rahmen_Rest_Wecker, D_und_M_1_led_8_3);
  xor xor_42 (LED_8_5, LED_Rahmen_Rest_Wecker, h_und_m_1_led_8_5);
  xor xor_43 (LED_8_6, LED_Rahmen_Rest_Wecker, m_und_s_1_led_8_6);
  xor xor_44 (LED_8_7, LED_Rahmen_Rest_Wecker, or_28_out);
  xor xor_45 (LED_8_8, LED_Rahmen_Rest_Wecker, m_und_s_1_led_8_8);
  xor xor_46 (LED_8_9, LED_Rahmen_Rest_Wecker, or_29_out);
  xor xor_47 (LED_8_10, LED_Rahmen_Rest_Wecker, m_und_s_1_led_8_10);
  xor xor_48 (LED_8_11, LED_Rahmen_Rest_Wecker, or_30_out);
endmodule

module Testing_LED (
);

  wire Button_1_out, Button_2_out, Button_3_out, Button_4_out, Button_5_out,
       Hauptschaltung_LED_Anzeige_1_led_3_2, Hauptschaltung_LED_Anzeige_1_led_3_3,
       Hauptschaltung_LED_Anzeige_1_led_3_7, Hauptschaltung_LED_Anzeige_1_led_3_11,
       Hauptschaltung_LED_Anzeige_1_led_4_2, Hauptschaltung_LED_Anzeige_1_led_4_4,
       Hauptschaltung_LED_Anzeige_1_led_4_7, Hauptschaltung_LED_Anzeige_1_led_4_8,
       Hauptschaltung_LED_Anzeige_1_led_4_9, Hauptschaltung_LED_Anzeige_1_led_4_10,
       Hauptschaltung_LED_Anzeige_1_led_4_11, Hauptschaltung_LED_Anzeige_1_led_5_2,
       Hauptschaltung_LED_Anzeige_1_led_5_3, Hauptschaltung_LED_Anzeige_1_led_5_4,
       Hauptschaltung_LED_Anzeige_1_led_5_5, Hauptschaltung_LED_Anzeige_1_led_5_6,
       Hauptschaltung_LED_Anzeige_1_led_5_7, Hauptschaltung_LED_Anzeige_1_led_5_8,
       Hauptschaltung_LED_Anzeige_1_led_5_9, Hauptschaltung_LED_Anzeige_1_led_5_10,
       Hauptschaltung_LED_Anzeige_1_led_5_11, Hauptschaltung_LED_Anzeige_1_led_6_2,
       Hauptschaltung_LED_Anzeige_1_led_6_3, Hauptschaltung_LED_Anzeige_1_led_6_4,
       Hauptschaltung_LED_Anzeige_1_led_6_5, Hauptschaltung_LED_Anzeige_1_led_6_6,
       Hauptschaltung_LED_Anzeige_1_led_6_7, Hauptschaltung_LED_Anzeige_1_led_6_8,
       Hauptschaltung_LED_Anzeige_1_led_6_9, Hauptschaltung_LED_Anzeige_1_led_6_10,
       Hauptschaltung_LED_Anzeige_1_led_6_11, Hauptschaltung_LED_Anzeige_1_led_7_2,
       Hauptschaltung_LED_Anzeige_1_led_7_4, Hauptschaltung_LED_Anzeige_1_led_7_5,
       Hauptschaltung_LED_Anzeige_1_led_7_6, Hauptschaltung_LED_Anzeige_1_led_7_7,
       Hauptschaltung_LED_Anzeige_1_led_7_9, Hauptschaltung_LED_Anzeige_1_led_7_10,
       Hauptschaltung_LED_Anzeige_1_led_7_11, Hauptschaltung_LED_Anzeige_1_led_8_2,
       Hauptschaltung_LED_Anzeige_1_led_8_3, Hauptschaltung_LED_Anzeige_1_led_8_5,
       Hauptschaltung_LED_Anzeige_1_led_8_6, Hauptschaltung_LED_Anzeige_1_led_8_7,
       Hauptschaltung_LED_Anzeige_1_led_8_8, Hauptschaltung_LED_Anzeige_1_led_8_9,
       Hauptschaltung_LED_Anzeige_1_led_8_10, Hauptschaltung_LED_Anzeige_1_led_8_11,
       Hauptschaltung_LED_Anzeige_1_led_rahmen_rest_wecker;

  Button Button_1 (.out(Button_1_out));
  Button Button_2 (.out(Button_2_out));
  Button Button_3 (.out(Button_3_out));
  Button Button_4 (.out(Button_4_out));
  Button Button_5 (.out(Button_5_out));
  Hauptschaltung_LED_Anzeige Hauptschaltung_LED_Anzeige_1 (
    .Input_1(Button_1_out), .Weckfunktion(Button_2_out), .Eingangstaste_Min_Sek(Button_3_out),
    .Eingangstaste_Tag_Monat(Button_4_out), .Eingangstaste_Jahr(Button_5_out),
    .LED_Rahmen_Rest_Wecker(Hauptschaltung_LED_Anzeige_1_led_rahmen_rest_wecker),
    .LED_3_2(Hauptschaltung_LED_Anzeige_1_led_3_2), .LED_3_3(Hauptschaltung_LED_Anzeige_1_led_3_3),
    .LED_3_7(Hauptschaltung_LED_Anzeige_1_led_3_7), .LED_3_11(Hauptschaltung_LED_Anzeige_1_led_3_11),
    .LED_4_2(Hauptschaltung_LED_Anzeige_1_led_4_2), .LED_4_4(Hauptschaltung_LED_Anzeige_1_led_4_4),
    .LED_4_7(Hauptschaltung_LED_Anzeige_1_led_4_7), .LED_4_8(Hauptschaltung_LED_Anzeige_1_led_4_8),
    .LED_4_9(Hauptschaltung_LED_Anzeige_1_led_4_9), .LED_4_10(Hauptschaltung_LED_Anzeige_1_led_4_10),
    .LED_4_11(Hauptschaltung_LED_Anzeige_1_led_4_11), .LED_5_2(Hauptschaltung_LED_Anzeige_1_led_5_2),
    .LED_5_3(Hauptschaltung_LED_Anzeige_1_led_5_3), .LED_5_4(Hauptschaltung_LED_Anzeige_1_led_5_4),
    .LED_5_5(Hauptschaltung_LED_Anzeige_1_led_5_5), .LED_5_6(Hauptschaltung_LED_Anzeige_1_led_5_6),
    .LED_5_7(Hauptschaltung_LED_Anzeige_1_led_5_7), .LED_5_8(Hauptschaltung_LED_Anzeige_1_led_5_8),
    .LED_5_9(Hauptschaltung_LED_Anzeige_1_led_5_9), .LED_5_10(Hauptschaltung_LED_Anzeige_1_led_5_10),
    .LED_5_11(Hauptschaltung_LED_Anzeige_1_led_5_11), .LED_6_2(Hauptschaltung_LED_Anzeige_1_led_6_2),
    .LED_6_3(Hauptschaltung_LED_Anzeige_1_led_6_3), .LED_6_4(Hauptschaltung_LED_Anzeige_1_led_6_4),
    .LED_6_5(Hauptschaltung_LED_Anzeige_1_led_6_5), .LED_6_6(Hauptschaltung_LED_Anzeige_1_led_6_6),
    .LED_6_7(Hauptschaltung_LED_Anzeige_1_led_6_7), .LED_6_8(Hauptschaltung_LED_Anzeige_1_led_6_8),
    .LED_6_9(Hauptschaltung_LED_Anzeige_1_led_6_9), .LED_6_10(Hauptschaltung_LED_Anzeige_1_led_6_10),
    .LED_6_11(Hauptschaltung_LED_Anzeige_1_led_6_11), .LED_7_2(Hauptschaltung_LED_Anzeige_1_led_7_2),
    .LED_7_4(Hauptschaltung_LED_Anzeige_1_led_7_4), .LED_7_5(Hauptschaltung_LED_Anzeige_1_led_7_5),
    .LED_7_6(Hauptschaltung_LED_Anzeige_1_led_7_6), .LED_7_7(Hauptschaltung_LED_Anzeige_1_led_7_7),
    .LED_7_9(Hauptschaltung_LED_Anzeige_1_led_7_9), .LED_7_10(Hauptschaltung_LED_Anzeige_1_led_7_10),
    .LED_7_11(Hauptschaltung_LED_Anzeige_1_led_7_11), .LED_8_2(Hauptschaltung_LED_Anzeige_1_led_8_2),
    .LED_8_3(Hauptschaltung_LED_Anzeige_1_led_8_3), .LED_8_5(Hauptschaltung_LED_Anzeige_1_led_8_5),
    .LED_8_6(Hauptschaltung_LED_Anzeige_1_led_8_6), .LED_8_7(Hauptschaltung_LED_Anzeige_1_led_8_7),
    .LED_8_8(Hauptschaltung_LED_Anzeige_1_led_8_8), .LED_8_9(Hauptschaltung_LED_Anzeige_1_led_8_9),
    .LED_8_10(Hauptschaltung_LED_Anzeige_1_led_8_10), .LED_8_11(Hauptschaltung_LED_Anzeige_1_led_8_11));
  LED LED_1 (.in(Hauptschaltung_LED_Anzeige_1_led_rahmen_rest_wecker));
  LED LED_13 (.in(Hauptschaltung_LED_Anzeige_1_led_rahmen_rest_wecker));
  LED LED_25 (.in(Hauptschaltung_LED_Anzeige_1_led_rahmen_rest_wecker));
  LED LED_37 (.in(Hauptschaltung_LED_Anzeige_1_led_rahmen_rest_wecker));
  LED LED_49 (.in(Hauptschaltung_LED_Anzeige_1_led_rahmen_rest_wecker));
  LED LED_61 (.in(Hauptschaltung_LED_Anzeige_1_led_rahmen_rest_wecker));
  LED LED_73 (.in(Hauptschaltung_LED_Anzeige_1_led_rahmen_rest_wecker));
  LED LED_85 (.in(Hauptschaltung_LED_Anzeige_1_led_rahmen_rest_wecker));
  LED LED_97 (.in(Hauptschaltung_LED_Anzeige_1_led_rahmen_rest_wecker));
  LED LED_109 (.in(Hauptschaltung_LED_Anzeige_1_led_rahmen_rest_wecker));
  LED LED_2 (.in(Hauptschaltung_LED_Anzeige_1_led_rahmen_rest_wecker));
  LED LED_14 (.in(Hauptschaltung_LED_Anzeige_1_led_rahmen_rest_wecker));
  LED LED_26 (.in(Hauptschaltung_LED_Anzeige_1_led_3_2));
  LED LED_38 (.in(Hauptschaltung_LED_Anzeige_1_led_4_2));
  LED LED_50 (.in(Hauptschaltung_LED_Anzeige_1_led_5_2));
  LED LED_62 (.in(Hauptschaltung_LED_Anzeige_1_led_6_2));
  LED LED_74 (.in(Hauptschaltung_LED_Anzeige_1_led_7_2));
  LED LED_86 (.in(Hauptschaltung_LED_Anzeige_1_led_8_2));
  LED LED_98 (.in(Hauptschaltung_LED_Anzeige_1_led_rahmen_rest_wecker));
  LED LED_110 (.in(Hauptschaltung_LED_Anzeige_1_led_rahmen_rest_wecker));
  LED LED_3 (.in(Hauptschaltung_LED_Anzeige_1_led_rahmen_rest_wecker));
  LED LED_15 (.in(Hauptschaltung_LED_Anzeige_1_led_rahmen_rest_wecker));
  LED LED_27 (.in(Hauptschaltung_LED_Anzeige_1_led_3_3));
  LED LED_39 (.in(Hauptschaltung_LED_Anzeige_1_led_rahmen_rest_wecker));
  LED LED_51 (.in(Hauptschaltung_LED_Anzeige_1_led_5_3));
  LED LED_63 (.in(Hauptschaltung_LED_Anzeige_1_led_6_3));
  LED LED_75 (.in(Hauptschaltung_LED_Anzeige_1_led_rahmen_rest_wecker));
  LED LED_87 (.in(Hauptschaltung_LED_Anzeige_1_led_8_3));
  LED LED_99 (.in(Hauptschaltung_LED_Anzeige_1_led_rahmen_rest_wecker));
  LED LED_111 (.in(Hauptschaltung_LED_Anzeige_1_led_rahmen_rest_wecker));
  LED LED_4 (.in(Hauptschaltung_LED_Anzeige_1_led_rahmen_rest_wecker));
  LED LED_16 (.in(Hauptschaltung_LED_Anzeige_1_led_rahmen_rest_wecker));
  LED LED_28 (.in(Hauptschaltung_LED_Anzeige_1_led_rahmen_rest_wecker));
  LED LED_40 (.in(Hauptschaltung_LED_Anzeige_1_led_4_4));
  LED LED_52 (.in(Hauptschaltung_LED_Anzeige_1_led_5_4));
  LED LED_64 (.in(Hauptschaltung_LED_Anzeige_1_led_6_4));
  LED LED_76 (.in(Hauptschaltung_LED_Anzeige_1_led_7_4));
  LED LED_88 (.in(Hauptschaltung_LED_Anzeige_1_led_rahmen_rest_wecker));
  LED LED_100 (.in(Hauptschaltung_LED_Anzeige_1_led_rahmen_rest_wecker));
  LED LED_112 (.in(Hauptschaltung_LED_Anzeige_1_led_rahmen_rest_wecker));
  LED LED_5 (.in(Hauptschaltung_LED_Anzeige_1_led_rahmen_rest_wecker));
  LED LED_17 (.in(Hauptschaltung_LED_Anzeige_1_led_rahmen_rest_wecker));
  LED LED_29 (.in(Hauptschaltung_LED_Anzeige_1_led_rahmen_rest_wecker));
  LED LED_41 (.in(Hauptschaltung_LED_Anzeige_1_led_rahmen_rest_wecker));
  LED LED_53 (.in(Hauptschaltung_LED_Anzeige_1_led_5_5));
  LED LED_65 (.in(Hauptschaltung_LED_Anzeige_1_led_6_5));
  LED LED_77 (.in(Hauptschaltung_LED_Anzeige_1_led_7_5));
  LED LED_89 (.in(Hauptschaltung_LED_Anzeige_1_led_8_5));
  LED LED_101 (.in(Hauptschaltung_LED_Anzeige_1_led_rahmen_rest_wecker));
  LED LED_113 (.in(Hauptschaltung_LED_Anzeige_1_led_rahmen_rest_wecker));
  LED LED_6 (.in(Hauptschaltung_LED_Anzeige_1_led_rahmen_rest_wecker));
  LED LED_18 (.in(Hauptschaltung_LED_Anzeige_1_led_rahmen_rest_wecker));
  LED LED_30 (.in(Hauptschaltung_LED_Anzeige_1_led_rahmen_rest_wecker));
  LED LED_42 (.in(Hauptschaltung_LED_Anzeige_1_led_rahmen_rest_wecker));
  LED LED_54 (.in(Hauptschaltung_LED_Anzeige_1_led_5_6));
  LED LED_66 (.in(Hauptschaltung_LED_Anzeige_1_led_6_6));
  LED LED_78 (.in(Hauptschaltung_LED_Anzeige_1_led_7_6));
  LED LED_90 (.in(Hauptschaltung_LED_Anzeige_1_led_8_6));
  LED LED_102 (.in(Hauptschaltung_LED_Anzeige_1_led_rahmen_rest_wecker));
  LED LED_114 (.in(Hauptschaltung_LED_Anzeige_1_led_rahmen_rest_wecker));
  LED LED_7 (.in(Hauptschaltung_LED_Anzeige_1_led_rahmen_rest_wecker));
  LED LED_19 (.in(Hauptschaltung_LED_Anzeige_1_led_rahmen_rest_wecker));
  LED LED_31 (.in(Hauptschaltung_LED_Anzeige_1_led_3_7));
  LED LED_43 (.in(Hauptschaltung_LED_Anzeige_1_led_4_7));
  LED LED_55 (.in(Hauptschaltung_LED_Anzeige_1_led_5_7));
  LED LED_67 (.in(Hauptschaltung_LED_Anzeige_1_led_6_7));
  LED LED_79 (.in(Hauptschaltung_LED_Anzeige_1_led_7_7));
  LED LED_91 (.in(Hauptschaltung_LED_Anzeige_1_led_8_7));
  LED LED_103 (.in(Hauptschaltung_LED_Anzeige_1_led_rahmen_rest_wecker));
  LED LED_115 (.in(Hauptschaltung_LED_Anzeige_1_led_rahmen_rest_wecker));
  LED LED_8 (.in(Hauptschaltung_LED_Anzeige_1_led_rahmen_rest_wecker));
  LED LED_20 (.in(Hauptschaltung_LED_Anzeige_1_led_rahmen_rest_wecker));
  LED LED_32 (.in(Hauptschaltung_LED_Anzeige_1_led_rahmen_rest_wecker));
  LED LED_44 (.in(Hauptschaltung_LED_Anzeige_1_led_4_8));
  LED LED_56 (.in(Hauptschaltung_LED_Anzeige_1_led_5_8));
  LED LED_68 (.in(Hauptschaltung_LED_Anzeige_1_led_6_8));
  LED LED_80 (.in(Hauptschaltung_LED_Anzeige_1_led_rahmen_rest_wecker));
  LED LED_92 (.in(Hauptschaltung_LED_Anzeige_1_led_8_8));
  LED LED_104 (.in(Hauptschaltung_LED_Anzeige_1_led_rahmen_rest_wecker));
  LED LED_116 (.in(Hauptschaltung_LED_Anzeige_1_led_rahmen_rest_wecker));
  LED LED_9 (.in(Hauptschaltung_LED_Anzeige_1_led_rahmen_rest_wecker));
  LED LED_21 (.in(Hauptschaltung_LED_Anzeige_1_led_rahmen_rest_wecker));
  LED LED_33 (.in(Hauptschaltung_LED_Anzeige_1_led_rahmen_rest_wecker));
  LED LED_45 (.in(Hauptschaltung_LED_Anzeige_1_led_4_9));
  LED LED_57 (.in(Hauptschaltung_LED_Anzeige_1_led_5_9));
  LED LED_69 (.in(Hauptschaltung_LED_Anzeige_1_led_6_9));
  LED LED_81 (.in(Hauptschaltung_LED_Anzeige_1_led_7_9));
  LED LED_93 (.in(Hauptschaltung_LED_Anzeige_1_led_8_9));
  LED LED_105 (.in(Hauptschaltung_LED_Anzeige_1_led_rahmen_rest_wecker));
  LED LED_117 (.in(Hauptschaltung_LED_Anzeige_1_led_rahmen_rest_wecker));
  LED LED_10 (.in(Hauptschaltung_LED_Anzeige_1_led_rahmen_rest_wecker));
  LED LED_22 (.in(Hauptschaltung_LED_Anzeige_1_led_rahmen_rest_wecker));
  LED LED_34 (.in(Hauptschaltung_LED_Anzeige_1_led_rahmen_rest_wecker));
  LED LED_46 (.in(Hauptschaltung_LED_Anzeige_1_led_4_10));
  LED LED_58 (.in(Hauptschaltung_LED_Anzeige_1_led_5_10));
  LED LED_70 (.in(Hauptschaltung_LED_Anzeige_1_led_6_10));
  LED LED_82 (.in(Hauptschaltung_LED_Anzeige_1_led_7_10));
  LED LED_94 (.in(Hauptschaltung_LED_Anzeige_1_led_8_10));
  LED LED_106 (.in(Hauptschaltung_LED_Anzeige_1_led_rahmen_rest_wecker));
  LED LED_118 (.in(Hauptschaltung_LED_Anzeige_1_led_rahmen_rest_wecker));
  LED LED_11 (.in(Hauptschaltung_LED_Anzeige_1_led_rahmen_rest_wecker));
  LED LED_23 (.in(Hauptschaltung_LED_Anzeige_1_led_rahmen_rest_wecker));
  LED LED_35 (.in(Hauptschaltung_LED_Anzeige_1_led_3_11));
  LED LED_47 (.in(Hauptschaltung_LED_Anzeige_1_led_4_11));
  LED LED_59 (.in(Hauptschaltung_LED_Anzeige_1_led_5_11));
  LED LED_71 (.in(Hauptschaltung_LED_Anzeige_1_led_6_11));
  LED LED_83 (.in(Hauptschaltung_LED_Anzeige_1_led_7_11));
  LED LED_95 (.in(Hauptschaltung_LED_Anzeige_1_led_8_11));
  LED LED_107 (.in(Hauptschaltung_LED_Anzeige_1_led_rahmen_rest_wecker));
  LED LED_119 (.in(Hauptschaltung_LED_Anzeige_1_led_rahmen_rest_wecker));
  LED LED_12 (.in(Hauptschaltung_LED_Anzeige_1_led_rahmen_rest_wecker));
  LED LED_24 (.in(Hauptschaltung_LED_Anzeige_1_led_rahmen_rest_wecker));
  LED LED_36 (.in(Hauptschaltung_LED_Anzeige_1_led_rahmen_rest_wecker));
  LED LED_48 (.in(Hauptschaltung_LED_Anzeige_1_led_rahmen_rest_wecker));
  LED LED_60 (.in(Hauptschaltung_LED_Anzeige_1_led_rahmen_rest_wecker));
  LED LED_72 (.in(Hauptschaltung_LED_Anzeige_1_led_rahmen_rest_wecker));
  LED LED_84 (.in(Hauptschaltung_LED_Anzeige_1_led_rahmen_rest_wecker));
  LED LED_96 (.in(Hauptschaltung_LED_Anzeige_1_led_rahmen_rest_wecker));
  LED LED_108 (.in(Hauptschaltung_LED_Anzeige_1_led_rahmen_rest_wecker));
  LED LED_120 (.in(Hauptschaltung_LED_Anzeige_1_led_rahmen_rest_wecker));
endmodule

module h_und_m (
  input  Taste_min_sek,
  input  Taste_tag_mon,
  input  Taste_jahr,
  output LED_3_2,
  output LED_4_2,
  output LED_5_2,
  output LED_5_7,
  output LED_5_8,
  output LED_5_9,
  output LED_5_10,
  output LED_5_11,
  output LED_6_2,
  output LED_6_3,
  output LED_6_4,
  output LED_6_5,
  output LED_6_7,
  output LED_6_9,
  output LED_6_11,
  output LED_7_2,
  output LED_7_5,
  output LED_7_7,
  output LED_7_9,
  output LED_7_11,
  output LED_8_2,
  output LED_8_5,
  output LED_8_7,
  output LED_8_11
);

  and and_1 (LED_3_2, ~Taste_min_sek, ~Taste_tag_mon, ~Taste_jahr);  // AND_Gate

  assign LED_4_2 = LED_3_2;
  assign LED_5_2 = LED_3_2;
  assign LED_5_7 = LED_3_2;
  assign LED_5_8 = LED_3_2;
  assign LED_5_9 = LED_3_2;
  assign LED_5_10 = LED_3_2;
  assign LED_5_11 = LED_3_2;
  assign LED_6_2 = LED_3_2;
  assign LED_6_3 = LED_3_2;
  assign LED_6_4 = LED_3_2;
  assign LED_6_5 = LED_3_2;
  assign LED_6_7 = LED_3_2;
  assign LED_6_9 = LED_3_2;
  assign LED_6_11 = LED_3_2;
  assign LED_7_2 = LED_3_2;
  assign LED_7_5 = LED_3_2;
  assign LED_7_7 = LED_3_2;
  assign LED_7_9 = LED_3_2;
  assign LED_7_11 = LED_3_2;
  assign LED_8_2 = LED_3_2;
  assign LED_8_5 = LED_3_2;
  assign LED_8_7 = LED_3_2;
  assign LED_8_11 = LED_3_2;
endmodule

module m_und_s (
  input  Taste_min_sek,
  output LED_4_8,
  output LED_4_9,
  output LED_4_10,
  output LED_5_2,
  output LED_5_3,
  output LED_5_4,
  output LED_5_5,
  output LED_5_6,
  output LED_5_8,
  output LED_6_2,
  output LED_6_4,
  output LED_6_6,
  output LED_6_8,
  output LED_6_9,
  output LED_6_10,
  output LED_7_2,
  output LED_7_4,
  output LED_7_6,
  output LED_7_10,
  output LED_8_2,
  output LED_8_6,
  output LED_8_8,
  output LED_8_9,
  output LED_8_10
);


  assign LED_4_8 = Taste_min_sek;
  assign LED_4_9 = Taste_min_sek;
  assign LED_4_10 = Taste_min_sek;
  assign LED_5_2 = Taste_min_sek;
  assign LED_5_3 = Taste_min_sek;
  assign LED_5_4 = Taste_min_sek;
  assign LED_5_5 = Taste_min_sek;
  assign LED_5_6 = Taste_min_sek;
  assign LED_5_8 = Taste_min_sek;
  assign LED_6_2 = Taste_min_sek;
  assign LED_6_4 = Taste_min_sek;
  assign LED_6_6 = Taste_min_sek;
  assign LED_6_8 = Taste_min_sek;
  assign LED_6_9 = Taste_min_sek;
  assign LED_6_10 = Taste_min_sek;
  assign LED_7_2 = Taste_min_sek;
  assign LED_7_4 = Taste_min_sek;
  assign LED_7_6 = Taste_min_sek;
  assign LED_7_10 = Taste_min_sek;
  assign LED_8_2 = Taste_min_sek;
  assign LED_8_6 = Taste_min_sek;
  assign LED_8_8 = Taste_min_sek;
  assign LED_8_9 = Taste_min_sek;
  assign LED_8_10 = Taste_min_sek;
endmodule

module D_und_M (
  input  Taste_Tag_Monat,
  output LED_3_2,
  output LED_3_3,
  output LED_3_7,
  output LED_3_11,
  output LED_4_2,
  output LED_4_4,
  output LED_4_7,
  output LED_4_8,
  output LED_4_10,
  output LED_4_11,
  output LED_5_2,
  output LED_5_5,
  output LED_5_7,
  output LED_5_9,
  output LED_5_11,
  output LED_6_2,
  output LED_6_5,
  output LED_6_7,
  output LED_6_11,
  output LED_7_2,
  output LED_7_4,
  output LED_7_7,
  output LED_7_11,
  output LED_8_2,
  output LED_8_3,
  output LED_8_7,
  output LED_8_11
);


  assign LED_3_2 = Taste_Tag_Monat;
  assign LED_3_3 = Taste_Tag_Monat;
  assign LED_3_7 = Taste_Tag_Monat;
  assign LED_3_11 = Taste_Tag_Monat;
  assign LED_4_2 = Taste_Tag_Monat;
  assign LED_4_4 = Taste_Tag_Monat;
  assign LED_4_7 = Taste_Tag_Monat;
  assign LED_4_8 = Taste_Tag_Monat;
  assign LED_4_10 = Taste_Tag_Monat;
  assign LED_4_11 = Taste_Tag_Monat;
  assign LED_5_2 = Taste_Tag_Monat;
  assign LED_5_5 = Taste_Tag_Monat;
  assign LED_5_7 = Taste_Tag_Monat;
  assign LED_5_9 = Taste_Tag_Monat;
  assign LED_5_11 = Taste_Tag_Monat;
  assign LED_6_2 = Taste_Tag_Monat;
  assign LED_6_5 = Taste_Tag_Monat;
  assign LED_6_7 = Taste_Tag_Monat;
  assign LED_6_11 = Taste_Tag_Monat;
  assign LED_7_2 = Taste_Tag_Monat;
  assign LED_7_4 = Taste_Tag_Monat;
  assign LED_7_7 = Taste_Tag_Monat;
  assign LED_7_11 = Taste_Tag_Monat;
  assign LED_8_2 = Taste_Tag_Monat;
  assign LED_8_3 = Taste_Tag_Monat;
  assign LED_8_7 = Taste_Tag_Monat;
  assign LED_8_11 = Taste_Tag_Monat;
endmodule

module Y (
  input  Taste_Jahr,
  output LED_3_7,
  output LED_3_11,
  output LED_4_7,
  output LED_4_11,
  output LED_5_8,
  output LED_5_10,
  output LED_6_9,
  output LED_7_9,
  output LED_8_9
);


  assign LED_3_7 = Taste_Jahr;
  assign LED_3_11 = Taste_Jahr;
  assign LED_4_7 = Taste_Jahr;
  assign LED_4_11 = Taste_Jahr;
  assign LED_5_8 = Taste_Jahr;
  assign LED_5_10 = Taste_Jahr;
  assign LED_6_9 = Taste_Jahr;
  assign LED_7_9 = Taste_Jahr;
  assign LED_8_9 = Taste_Jahr;
endmodule
